// Logisim project Pipeline.circ as structural Verilog: 16 circuits, main circuit ◇单周期MIPS
module \单周期MIPS  (
);

  wire and_1_out, and_2_out, and_3_out, Beq, BLTZ, Bne, CLK, comparator_1_eq, Cond, Display, Go, JAL, Jmp,
       JR, LBU, MemWrite, mips_alu_1_equal, RST, Run, Shift, SignedExt, Syscall, \硬布线控制器_1_alu_src ,
       \硬布线控制器_1_memtoreg , \硬布线控制器_1_regdst , \硬布线控制器_1_regwrite , \硬布线控制器_1_sllv , \硬布线控制器_1_srlv ;
  wire [3:0] \硬布线控制器_1_alu_op ;
  wire [4:0] multiplexer_3_out, multiplexer_4_out, multiplexer_5_out, multiplexer_8_out, multiplexer_10_out;
  wire [7:0] multiplexer_12_out;
  wire [15:0] \总周期数 , \无条件分支数 , \条件分支成功数 ;
  wire [27:0] PC_q;
  wire [31:0] adder_2_out, bit_extender_1_out, bit_extender_2_out, Din, LedData, mips_alu_1_result,
       multiplexer_1_out, multiplexer_2_out, multiplexer_6_out, multiplexer_7_out, multiplexer_9_out,
       multiplexer_11_out, PC_4, R1, R2, ram_1_data, shifter_1_out;
  wire [31:2] Jaddr;
  wire [31:26] rom_1_data;

  Button \u_总复位  (.out(RST));
  Button \u_继续运行  (.out(Go));
  Clock clock_1 (.out(CLK));
  Multiplexer #(.width(32), .enable("false")) multiplexer_1 (
    .in0({Jaddr, 2'b00}), .in1(R1), .out(multiplexer_1_out), .sel(JR));
  Hex_Digit_Display hex_digit_display_1 (.value(LedData[31:28]));  // open: dp
  Hex_Digit_Display hex_digit_display_2 (.value(LedData[27:24]));  // open: dp
  and and_1 (and_1_out, mips_alu_1_result[0], BLTZ);
  and and_2 (and_2_out, ~mips_alu_1_equal, Bne);  // AND_Gate
  and and_3 (and_3_out, mips_alu_1_equal, Beq);
  or or_1 (Cond, and_1_out, and_2_out, and_3_out);
  Multiplexer #(.select(2), .width(32), .enable("false")) multiplexer_2 (
    .in0(PC_4), .in1(adder_2_out), .in2(multiplexer_1_out), .out(multiplexer_2_out), .sel({Jmp, Cond}));  // open: in3
  Hex_Digit_Display hex_digit_display_3 (.value(LedData[23:20]));  // open: dp
  Hex_Digit_Display hex_digit_display_4 (.value(LedData[19:16]));  // open: dp
  // Probe on multiplexer_2_out
  Register #(.width(32)) PC (.D(multiplexer_2_out), .en(Run), .Q({Jaddr[31:28], PC_q}), .clk(CLK), .clr(RST));
  Hex_Digit_Display hex_digit_display_5 (.value(LedData[11:8]));  // open: dp
  Hex_Digit_Display hex_digit_display_6 (.value(LedData[15:12]));  // open: dp
  // Probe on {Jaddr[31:28], PC_q}
  Adder #(.width(32)) adder_1 (.a({Jaddr[31:28], PC_q}), .b(32'h4), .out(PC_4));  // open: cin, cout
  or or_2 (Run, ~Syscall, Go, Display);  // OR_Gate
  Hex_Digit_Display hex_digit_display_7 (.value(LedData[3:0]));  // open: dp
  Hex_Digit_Display hex_digit_display_8 (.value(LedData[7:4]));  // open: dp
  ROM #(.addrWidth(10), .dataWidth(32)) rom_1 (.addr(PC_q[11:2]), .data({rom_1_data, Jaddr[27:2]}));  // open: sel
  Counter #(.width(16), .max('hffff)) counter_1 (
    .count(Run), .Q(\总周期数 ), .clk(CLK), .clr(RST));  // open: load, D, carry
  or or_3 (Shift, \硬布线控制器_1_sllv , \硬布线控制器_1_srlv );
  // Probe on \总周期数 
  // Probe on \无条件分支数 
  // Probe on \条件分支成功数 
  \硬布线控制器  \u_硬布线控制器_1  (
    .Func(Jaddr[7:2]), .OP(rom_1_data), .ALU_OP(\硬布线控制器_1_alu_op ), .MemToReg(\硬布线控制器_1_memtoreg ),
    .MemWrite(MemWrite), .ALU_SRC(\硬布线控制器_1_alu_src ), .RegWrite(\硬布线控制器_1_regwrite ), .SysCALL(Syscall),
    .SignedExt(SignedExt), .RegDst(\硬布线控制器_1_regdst ), .JR(JR), .JMP(Jmp), .Beq(Beq), .JAL(JAL), .Bne(Bne),
    .SLLV(\硬布线控制器_1_sllv ), .SRLV(\硬布线控制器_1_srlv ), .LBU(LBU), .BLTZ(BLTZ), .REGIMM(Jaddr[22:18]));
  Multiplexer #(.width(5), .enable("false")) multiplexer_3 (
    .in0(Jaddr[27:23]), .in1(5'b00010), .out(multiplexer_3_out), .sel(Syscall));
  assign bit_extender_1_out = {{16{1'b0}}, Jaddr[17:2]};  // Bit_Extender bit_extender_1
  assign bit_extender_2_out = {{16{Jaddr[17]}}, Jaddr[17:2]};  // Bit_Extender bit_extender_2
  // Probe on {Jaddr, 2'b00}
  Multiplexer #(.width(5), .enable("false")) multiplexer_4 (
    .in0(Jaddr[22:18]), .in1(5'b00100), .out(multiplexer_4_out), .sel(Syscall));
  Multiplexer #(.width(5), .enable("false")) multiplexer_5 (
    .in0(Jaddr[22:18]), .in1(Jaddr[17:13]), .out(multiplexer_5_out), .sel(\硬布线控制器_1_regdst ));
  Multiplexer #(.width(32), .enable("false")) multiplexer_6 (.in0(Din), .in1(PC_4), .out(multiplexer_6_out), .sel(JAL));
  Multiplexer #(.width(32), .enable("false")) multiplexer_7 (
    .in0(bit_extender_1_out), .in1(bit_extender_2_out), .out(multiplexer_7_out), .sel(SignedExt));
  Counter #(.width(16), .max('hffff)) counter_2 (
    .count(Cond), .Q(\条件分支成功数 ), .clk(CLK), .clr(RST));  // open: load, D, carry
  Multiplexer #(.width(5), .enable("false")) multiplexer_8 (
    .in0(multiplexer_5_out), .in1({5{1'b1}}), .out(multiplexer_8_out), .sel(JAL));
  // Probe on multiplexer_6_out
  // Probe on multiplexer_8_out
  MIPS_Regifile mips_regifile_1 (
    .Din(multiplexer_6_out), .Clk(CLK), .R1(R1), .R2(R2), .WE(\硬布线控制器_1_regwrite ),
    .W_num(multiplexer_8_out), .R1_num(multiplexer_3_out), .R2_num(multiplexer_4_out));
  Counter #(.width(16), .max('hffff)) counter_3 (
    .count(Jmp), .Q(\无条件分支数 ), .clk(CLK), .clr(RST));  // open: load, D, carry
  Multiplexer #(.width(32), .enable("false")) multiplexer_9 (
    .in0(R2), .in1(multiplexer_7_out), .out(multiplexer_9_out), .sel(\硬布线控制器_1_alu_src ));
  Shifter #(.width(32)) shifter_1 (.in(multiplexer_7_out), .\dist (5'b00010), .out(shifter_1_out));
  // Probe on \硬布线控制器_1_alu_op 
  // Probe on R1
  // Probe on multiplexer_9_out
  Multiplexer #(.width(5), .enable("false")) multiplexer_10 (
    .in0(Jaddr[12:8]), .in1(R1[4:0]), .out(multiplexer_10_out), .sel(Shift));
  Adder #(.width(32)) adder_2 (.a(shifter_1_out), .b(PC_4), .out(adder_2_out));  // open: cin, cout
  MIPS_ALU mips_alu_1 (
    .X(R1), .Y(multiplexer_9_out), .AluOP(\硬布线控制器_1_alu_op ), .Equal(mips_alu_1_equal),
    .Result(mips_alu_1_result), .shamt(multiplexer_10_out));  // open: Result_2
  // Probe on mips_alu_1_result
  Comparator #(.width(32), .mode("unsigned")) comparator_1 (.a(R1), .b(32'h22), .eq(comparator_1_eq));  // open: gt, lt
  RAM #(.addrWidth(10), .dataWidth(32), .bus("separate")) ram_1 (
    .addr(mips_alu_1_result[11:2]), .din(R2), .data(ram_1_data), .str(MemWrite), .sel(1'b1), .clk(CLK),
    .ld(1'b1), .clr(RST));
  and and_4 (Display, comparator_1_eq, Syscall);
  Multiplexer #(.width(32), .enable("false")) multiplexer_11 (
    .in0(mips_alu_1_result), .in1(ram_1_data), .out(multiplexer_11_out), .sel(\硬布线控制器_1_memtoreg ));
  Multiplexer #(.select(2), .width(8), .enable("false")) multiplexer_12 (
    .in0(multiplexer_11_out[7:0]), .in1(multiplexer_11_out[15:8]), .in2(multiplexer_11_out[23:16]),
    .in3(multiplexer_11_out[31:24]), .out(multiplexer_12_out), .sel(mips_alu_1_result[1:0]));
  Register #(.width(32)) register_1 (.D(R2), .en(Display), .Q(LedData), .clk(CLK), .clr(RST));
  Multiplexer #(.width(32), .enable("false")) multiplexer_13 (
    .in0(multiplexer_11_out), .in1({{24{1'b0}}, multiplexer_12_out}), .out(Din), .sel(LBU));
  // Probe on Din

  // Other names for the same wires on the sheet: Uncond = Jmp

  // Notes on the sheet:
  //   数码管输出应该用寄存器锁存，否则显示数据只能一闪而过
  //   可以通过项目增加Logisim库的方式将前几次实验完成的电路作为子电路引入到本电路中使用
  //   数码管输出
  //   指令存储器
  //   指令字
  //   contents of rom_1 (hex, n*v repeats v):
  //   20080001 20090003 20110876 112020 20020022 c 200b0008 1118804 1318804 112020 20020022 c 216bffff
  //   1560fff9 2002000a c
  //   SignedExt
  //   OP
  //   Func
  //   rs
  //   rt
  //   rd
  //   shmat
  //   immed
  //   总复位信号应将除ROM以外所有存储组件全部清零
  //   JMP
  //   JR
  //   SLLV
  //   SRLV
  //   LBU
  //   Syscall
  //   Beq
  //   Bne
  //   MemToReg
  //   MemWrite
  //   AluOP
  //   AluSrcB
  //   RegWrite
  //   JAL
  //   RegDst
endmodule

// 单周期硬布线控制器
module \硬布线控制器  (
  input  [5:0] OP,
  input  [5:0] Func,
  input  [4:0] REGIMM,
  output [3:0] ALU_OP,
  output MemToReg,
  output MemWrite,
  output ALU_SRC,
  output RegWrite,
  output SysCALL,
  output SignedExt,
  output RegDst,
  output Beq,
  output Bne,
  output JR,
  output JMP,
  output JAL,
  output SLLV,
  output SRLV,
  output LBU,
  output BLTZ
);

  wire comparator_1_eq, comparator_3_eq, comparator_4_eq, comparator_5_eq, comparator_6_eq;

  Comparator #(.width(6), .mode("unsigned")) comparator_1 (
    .a(OP), .b({6{1'b0}}), .eq(comparator_1_eq));  // open: gt, lt
  Comparator #(.width(6), .mode("unsigned")) comparator_2 (.a(OP), .b(6'b100100), .eq(LBU));  // open: gt, lt
  Comparator #(.width(6), .mode("unsigned")) comparator_3 (
    .a(OP), .b(6'b000001), .eq(comparator_3_eq));  // open: gt, lt
  \运算控制器  \u_运算控制器_1  (
    .OP0(OP[0]), .OP1(OP[1]), .OP2(OP[2]), .OP3(OP[3]), .OP4(OP[4]), .OP5(OP[5]), .F0(Func[0]), .F1(Func[1]),
    .F2(Func[2]), .F3(Func[3]), .F4(Func[4]), .F5(Func[5]), .S0(ALU_OP[0]), .S1(ALU_OP[1]), .S2(ALU_OP[2]),
    .S3(ALU_OP[3]));
  \控制信号生成  \u_控制信号生成_1  (
    .OP0(OP[0]), .OP1(OP[1]), .OP2(OP[2]), .OP3(OP[3]), .OP4(OP[4]), .OP5(OP[5]), .F0(Func[0]), .F1(Func[1]),
    .F2(Func[2]), .F3(Func[3]), .F4(Func[4]), .F5(Func[5]), .MemToReg(MemToReg), .MemWrite(MemWrite),
    .ALU_SRC(ALU_SRC), .RegWrite(RegWrite), .SysCALL(SysCALL), .SignedExt(SignedExt), .RegDst(RegDst),
    .BEQ(Beq), .BNE(Bne), .JR(JR), .JMP(JMP), .JAL(JAL));
  Comparator #(.width(5), .mode("unsigned")) comparator_4 (
    .a(REGIMM), .b({5{1'b0}}), .eq(comparator_4_eq));  // open: gt, lt
  Comparator #(.width(6), .mode("unsigned")) comparator_5 (
    .a(Func), .b(6'b000100), .eq(comparator_5_eq));  // open: gt, lt
  Comparator #(.width(6), .mode("unsigned")) comparator_6 (
    .a(Func), .b(6'b000110), .eq(comparator_6_eq));  // open: gt, lt
  and and_1 (BLTZ, comparator_3_eq, comparator_4_eq);
  and and_2 (SLLV, comparator_5_eq, comparator_1_eq);
  and and_3 (SRLV, comparator_6_eq, comparator_1_eq);

  // Other names for the same wires on the sheet: OP_CODE[5:0] = OP

  // Notes on the sheet:
  //   运算器控制器，根据指令生成运算器功能选择信号
  //   控制信号生成，产生数据通路需要的其他控制信号
endmodule

// 运算器控制器
module \运算控制器  (
  input  OP0,
  input  OP1,
  input  OP2,
  input  OP3,
  input  OP4,
  input  OP5,
  input  F0,
  input  F1,
  input  F2,
  input  F3,
  input  F4,
  input  F5,
  output S0,
  output S1,
  output S2,
  output S3
);

  wire and_1_out, and_2_out, and_3_out, and_4_out, and_5_out, and_6_out, and_7_out, and_8_out, and_9_out,
       and_10_out, and_11_out, and_12_out, and_13_out, and_14_out, and_15_out, and_16_out, and_17_out,
       and_18_out, and_19_out, and_20_out, and_21_out, and_22_out, and_23_out, and_24_out, and_25_out,
       and_26_out, and_27_out, and_28_out, and_29_out, and_30_out, and_31_out, and_32_out, and_33_out,
       and_34_out, and_35_out, and_36_out, and_37_out, and_38_out, and_39_out, and_40_out, not_1_out,
       not_2_out, not_3_out, not_4_out, not_5_out, not_6_out, not_7_out, not_8_out, not_9_out, not_10_out,
       not_11_out, not_12_out, not_13_out, not_14_out, not_15_out, not_16_out, not_17_out, not_18_out,
       not_19_out, not_20_out, not_21_out, not_22_out, not_23_out, not_24_out, not_25_out, not_26_out,
       not_27_out, not_28_out, not_29_out, not_30_out, not_31_out, not_32_out, not_33_out, not_34_out,
       not_35_out, not_36_out, not_37_out, not_38_out, not_39_out, not_40_out, not_41_out, not_42_out,
       not_43_out, not_44_out, not_45_out, not_46_out, not_47_out, not_48_out, not_49_out, not_50_out,
       not_51_out, not_52_out, not_53_out, not_54_out, not_55_out, not_56_out, not_57_out, not_58_out,
       not_59_out, not_60_out, not_61_out, not_62_out, not_63_out, not_64_out, not_65_out, not_66_out,
       not_67_out, not_68_out, not_69_out, not_70_out, not_71_out, not_72_out, not_73_out, not_74_out,
       not_75_out, not_76_out, not_77_out, not_78_out, not_79_out, not_80_out, not_81_out, not_82_out,
       not_83_out, not_84_out, not_85_out, not_86_out, not_87_out, not_88_out, not_89_out, not_90_out,
       not_91_out, not_92_out, not_93_out, not_94_out, not_95_out, not_96_out, not_97_out, not_98_out,
       not_99_out, not_100_out, not_101_out, not_102_out, not_103_out, not_104_out, not_105_out, not_106_out,
       not_107_out, not_108_out, not_109_out, not_110_out, not_111_out, not_112_out, not_113_out,
       not_114_out, not_115_out, not_116_out, not_117_out, not_118_out, not_119_out, not_120_out,
       not_121_out, not_122_out, not_123_out, not_124_out, not_125_out, not_126_out, not_127_out,
       not_128_out, not_129_out, not_130_out, not_131_out, not_132_out, not_133_out, not_134_out,
       not_135_out, not_136_out, not_137_out, not_138_out, not_139_out, not_140_out, not_141_out,
       not_142_out, not_143_out, not_144_out, not_145_out, not_146_out, not_147_out, not_148_out,
       not_149_out, not_150_out, not_151_out, not_152_out, not_153_out, not_154_out, not_155_out,
       not_156_out, not_157_out, not_158_out, not_159_out, not_160_out, not_161_out, not_162_out,
       not_163_out, not_164_out, not_165_out, not_166_out, not_167_out, not_168_out, not_169_out,
       not_170_out, not_171_out, not_172_out, not_173_out, not_174_out, not_175_out, not_176_out,
       not_177_out, not_178_out, not_179_out, not_180_out, not_181_out, not_182_out, not_183_out,
       not_184_out, not_185_out, not_186_out, not_187_out, not_188_out, not_189_out, not_190_out,
       not_191_out, not_192_out, not_193_out, not_194_out, not_195_out, not_196_out, not_197_out,
       not_198_out, not_199_out, not_200_out, not_201_out, not_202_out, not_203_out, not_204_out,
       not_205_out, not_206_out, not_207_out, not_208_out, not_209_out, not_210_out, not_211_out,
       not_212_out, not_213_out, not_214_out, not_215_out, not_216_out, not_217_out, not_218_out,
       not_219_out, not_220_out, not_221_out, not_222_out, not_223_out, not_224_out, not_225_out,
       not_226_out, not_227_out, not_228_out, not_229_out, not_230_out, not_231_out, not_232_out,
       not_233_out, not_234_out, not_235_out, not_236_out, not_237_out, not_238_out, not_239_out,
       not_240_out, not_241_out, not_242_out, not_243_out, not_244_out, not_245_out, not_246_out,
       not_247_out, not_248_out, not_249_out, not_250_out, not_251_out, not_252_out, not_253_out,
       not_254_out, not_255_out, not_256_out, not_257_out, not_258_out, not_259_out, not_260_out,
       not_261_out, not_262_out, not_263_out, not_264_out, not_265_out, not_266_out, not_267_out,
       not_268_out, not_269_out;

  not not_1 (not_1_out, OP5);
  not not_2 (not_2_out, OP4);
  not not_3 (not_3_out, OP3);
  not not_4 (not_4_out, OP2);
  not not_5 (not_5_out, OP1);
  not not_6 (not_6_out, OP0);
  not not_7 (not_7_out, F5);
  not not_8 (not_8_out, F4);
  not not_9 (not_9_out, F3);
  not not_10 (not_10_out, F2);
  not not_11 (not_11_out, OP5);
  not not_12 (not_12_out, OP4);
  not not_13 (not_13_out, OP3);
  not not_14 (not_14_out, OP2);
  not not_15 (not_15_out, OP1);
  not not_16 (not_16_out, OP0);
  not not_17 (not_17_out, F4);
  not not_18 (not_18_out, F3);
  not not_19 (not_19_out, F2);
  not not_20 (not_20_out, F1);
  not not_21 (not_21_out, F0);
  not not_22 (not_22_out, OP5);
  not not_23 (not_23_out, OP4);
  not not_24 (not_24_out, OP3);
  not not_25 (not_25_out, OP2);
  not not_26 (not_26_out, OP1);
  not not_27 (not_27_out, OP0);
  not not_28 (not_28_out, F4);
  not not_29 (not_29_out, F3);
  not not_30 (not_30_out, F2);
  not not_31 (not_31_out, F1);
  not not_32 (not_32_out, OP5);
  not not_33 (not_33_out, OP4);
  not not_34 (not_34_out, OP3);
  not not_35 (not_35_out, OP2);
  not not_36 (not_36_out, OP1);
  not not_37 (not_37_out, OP0);
  not not_38 (not_38_out, F4);
  not not_39 (not_39_out, F3);
  not not_40 (not_40_out, F1);
  not not_41 (not_41_out, F0);
  not not_42 (not_42_out, OP5);
  not not_43 (not_43_out, OP4);
  not not_44 (not_44_out, OP3);
  not not_45 (not_45_out, OP2);
  not not_46 (not_46_out, OP1);
  not not_47 (not_47_out, OP0);
  not not_48 (not_48_out, F4);
  not not_49 (not_49_out, F2);
  not not_50 (not_50_out, F0);
  not not_51 (not_51_out, OP5);
  not not_52 (not_52_out, OP4);
  not not_53 (not_53_out, OP2);
  not not_54 (not_54_out, OP1);
  not not_55 (not_55_out, OP0);
  not not_56 (not_56_out, OP5);
  not not_57 (not_57_out, OP4);
  not not_58 (not_58_out, OP1);
  not not_59 (not_59_out, OP0);
  not not_60 (not_60_out, OP5);
  not not_61 (not_61_out, OP4);
  not not_62 (not_62_out, OP2);
  not not_63 (not_63_out, OP1);
  not not_64 (not_64_out, OP5);
  not not_65 (not_65_out, OP4);
  not not_66 (not_66_out, OP2);
  not not_67 (not_67_out, OP0);
  not not_68 (not_68_out, OP4);
  not not_69 (not_69_out, OP3);
  not not_70 (not_70_out, OP2);
  not not_71 (not_71_out, OP4);
  not not_72 (not_72_out, OP2);
  not not_73 (not_73_out, OP4);
  not not_74 (not_74_out, OP3);
  not not_75 (not_75_out, OP1);
  not not_76 (not_76_out, OP0);
  not not_77 (not_77_out, OP5);
  not not_78 (not_78_out, OP4);
  not not_79 (not_79_out, OP3);
  not not_80 (not_80_out, OP2);
  not not_81 (not_81_out, OP1);
  not not_82 (not_82_out, OP5);
  not not_83 (not_83_out, OP4);
  not not_84 (not_84_out, OP3);
  not not_85 (not_85_out, OP2);
  not not_86 (not_86_out, OP1);
  not not_87 (not_87_out, OP0);
  not not_88 (not_88_out, F5);
  not not_89 (not_89_out, F4);
  not not_90 (not_90_out, F3);
  not not_91 (not_91_out, F2);
  not not_92 (not_92_out, F0);
  not not_93 (not_93_out, OP5);
  not not_94 (not_94_out, OP4);
  not not_95 (not_95_out, OP3);
  not not_96 (not_96_out, OP2);
  not not_97 (not_97_out, OP1);
  not not_98 (not_98_out, OP0);
  not not_99 (not_99_out, F4);
  not not_100 (not_100_out, F3);
  not not_101 (not_101_out, F2);
  not not_102 (not_102_out, F0);
  not not_103 (not_103_out, OP5);
  not not_104 (not_104_out, OP4);
  not not_105 (not_105_out, OP3);
  not not_106 (not_106_out, OP2);
  not not_107 (not_107_out, OP1);
  not not_108 (not_108_out, OP0);
  not not_109 (not_109_out, F4);
  not not_110 (not_110_out, F3);
  not not_111 (not_111_out, F1);
  not not_112 (not_112_out, F0);
  not not_113 (not_113_out, OP5);
  not not_114 (not_114_out, OP4);
  not not_115 (not_115_out, OP3);
  not not_116 (not_116_out, OP2);
  not not_117 (not_117_out, OP1);
  not not_118 (not_118_out, OP0);
  not not_119 (not_119_out, F4);
  not not_120 (not_120_out, F3);
  not not_121 (not_121_out, OP5);
  not not_122 (not_122_out, OP4);
  not not_123 (not_123_out, OP3);
  not not_124 (not_124_out, OP2);
  not not_125 (not_125_out, OP1);
  not not_126 (not_126_out, OP0);
  not not_127 (not_127_out, F4);
  not not_128 (not_128_out, F2);
  not not_129 (not_129_out, F0);
  not not_130 (not_130_out, OP5);
  not not_131 (not_131_out, OP4);
  not not_132 (not_132_out, OP1);
  not not_133 (not_133_out, OP0);
  not not_134 (not_134_out, OP5);
  not not_135 (not_135_out, OP4);
  not not_136 (not_136_out, OP2);
  not not_137 (not_137_out, OP0);
  not not_138 (not_138_out, OP5);
  not not_139 (not_139_out, OP4);
  not not_140 (not_140_out, OP3);
  not not_141 (not_141_out, OP2);
  not not_142 (not_142_out, OP1);
  not not_143 (not_143_out, OP0);
  not not_144 (not_144_out, F5);
  not not_145 (not_145_out, F4);
  not not_146 (not_146_out, F3);
  not not_147 (not_147_out, F0);
  not not_148 (not_148_out, OP5);
  not not_149 (not_149_out, OP4);
  not not_150 (not_150_out, OP3);
  not not_151 (not_151_out, OP2);
  not not_152 (not_152_out, OP1);
  not not_153 (not_153_out, OP5);
  not not_154 (not_154_out, OP4);
  not not_155 (not_155_out, OP3);
  not not_156 (not_156_out, OP2);
  not not_157 (not_157_out, OP1);
  not not_158 (not_158_out, OP0);
  not not_159 (not_159_out, F4);
  not not_160 (not_160_out, F3);
  not not_161 (not_161_out, F2);
  not not_162 (not_162_out, F1);
  not not_163 (not_163_out, F0);
  not not_164 (not_164_out, OP5);
  not not_165 (not_165_out, OP4);
  not not_166 (not_166_out, OP3);
  not not_167 (not_167_out, OP2);
  not not_168 (not_168_out, OP1);
  not not_169 (not_169_out, OP0);
  not not_170 (not_170_out, F4);
  not not_171 (not_171_out, F3);
  not not_172 (not_172_out, F2);
  not not_173 (not_173_out, F1);
  not not_174 (not_174_out, OP5);
  not not_175 (not_175_out, OP4);
  not not_176 (not_176_out, OP3);
  not not_177 (not_177_out, OP2);
  not not_178 (not_178_out, OP1);
  not not_179 (not_179_out, OP0);
  not not_180 (not_180_out, F4);
  not not_181 (not_181_out, F3);
  not not_182 (not_182_out, F2);
  not not_183 (not_183_out, F0);
  not not_184 (not_184_out, OP5);
  not not_185 (not_185_out, OP4);
  not not_186 (not_186_out, OP3);
  not not_187 (not_187_out, OP2);
  not not_188 (not_188_out, OP1);
  not not_189 (not_189_out, OP0);
  not not_190 (not_190_out, F4);
  not not_191 (not_191_out, F3);
  not not_192 (not_192_out, F1);
  not not_193 (not_193_out, F0);
  not not_194 (not_194_out, OP5);
  not not_195 (not_195_out, OP4);
  not not_196 (not_196_out, OP3);
  not not_197 (not_197_out, OP2);
  not not_198 (not_198_out, OP1);
  not not_199 (not_199_out, OP0);
  not not_200 (not_200_out, F4);
  not not_201 (not_201_out, F2);
  not not_202 (not_202_out, OP5);
  not not_203 (not_203_out, OP4);
  not not_204 (not_204_out, OP2);
  not not_205 (not_205_out, OP1);
  not not_206 (not_206_out, OP0);
  not not_207 (not_207_out, OP5);
  not not_208 (not_208_out, OP4);
  not not_209 (not_209_out, OP1);
  not not_210 (not_210_out, OP0);
  not not_211 (not_211_out, OP5);
  not not_212 (not_212_out, OP4);
  not not_213 (not_213_out, OP2);
  not not_214 (not_214_out, OP1);
  not not_215 (not_215_out, OP4);
  not not_216 (not_216_out, OP3);
  not not_217 (not_217_out, OP2);
  not not_218 (not_218_out, OP4);
  not not_219 (not_219_out, OP2);
  not not_220 (not_220_out, OP4);
  not not_221 (not_221_out, OP3);
  not not_222 (not_222_out, OP1);
  not not_223 (not_223_out, OP0);
  not not_224 (not_224_out, OP5);
  not not_225 (not_225_out, OP4);
  not not_226 (not_226_out, OP3);
  not not_227 (not_227_out, OP2);
  not not_228 (not_228_out, OP1);
  not not_229 (not_229_out, OP0);
  not not_230 (not_230_out, F4);
  not not_231 (not_231_out, F3);
  not not_232 (not_232_out, F1);
  not not_233 (not_233_out, OP5);
  not not_234 (not_234_out, OP4);
  not not_235 (not_235_out, OP3);
  not not_236 (not_236_out, OP2);
  not not_237 (not_237_out, OP1);
  not not_238 (not_238_out, OP0);
  not not_239 (not_239_out, F4);
  not not_240 (not_240_out, F3);
  not not_241 (not_241_out, OP5);
  not not_242 (not_242_out, OP4);
  not not_243 (not_243_out, OP3);
  not not_244 (not_244_out, OP2);
  not not_245 (not_245_out, OP1);
  not not_246 (not_246_out, OP0);
  not not_247 (not_247_out, F4);
  not not_248 (not_248_out, F2);
  not not_249 (not_249_out, F0);
  not not_250 (not_250_out, OP5);
  not not_251 (not_251_out, OP4);
  not not_252 (not_252_out, OP3);
  not not_253 (not_253_out, OP2);
  not not_254 (not_254_out, OP1);
  not not_255 (not_255_out, OP0);
  not not_256 (not_256_out, F4);
  not not_257 (not_257_out, F2);
  not not_258 (not_258_out, OP5);
  not not_259 (not_259_out, OP4);
  not not_260 (not_260_out, OP2);
  not not_261 (not_261_out, OP0);
  not not_262 (not_262_out, OP5);
  not not_263 (not_263_out, OP4);
  not not_264 (not_264_out, OP1);
  not not_265 (not_265_out, OP5);
  not not_266 (not_266_out, OP4);
  not not_267 (not_267_out, OP3);
  not not_268 (not_268_out, OP2);
  not not_269 (not_269_out, OP1);
  and and_1 (and_1_out, not_1_out, not_2_out, not_3_out, not_4_out, not_5_out, not_6_out, not_7_out, not_8_out, not_9_out, not_10_out, F1, F0);
  and and_2 (and_2_out, not_11_out, not_12_out, not_13_out, not_14_out, not_15_out, not_16_out, F5, not_17_out, not_18_out, not_19_out, not_20_out, not_21_out);
  and and_3 (and_3_out, not_22_out, not_23_out, not_24_out, not_25_out, not_26_out, not_27_out, F5, not_28_out, not_29_out, not_30_out, not_31_out, F0);
  and and_4 (and_4_out, not_32_out, not_33_out, not_34_out, not_35_out, not_36_out, not_37_out, F5, not_38_out, not_39_out, F2, not_40_out, not_41_out);
  and and_5 (and_5_out, not_42_out, not_43_out, not_44_out, not_45_out, not_46_out, not_47_out, F5, not_48_out, F3, not_49_out, F1, not_50_out);
  and and_6 (and_6_out, not_51_out, not_52_out, OP3, not_53_out, not_54_out, not_55_out);
  and and_7 (and_7_out, not_56_out, not_57_out, OP3, OP2, not_58_out, not_59_out);
  and and_8 (and_8_out, not_60_out, not_61_out, OP3, not_62_out, not_63_out, OP0);
  and and_9 (and_9_out, not_64_out, not_65_out, OP3, not_66_out, OP1, not_67_out);
  and and_10 (and_10_out, OP5, not_68_out, not_69_out, not_70_out, OP1, OP0);
  and and_11 (and_11_out, OP5, not_71_out, OP3, not_72_out, OP1, OP0);
  and and_12 (and_12_out, OP5, not_73_out, not_74_out, OP2, not_75_out, not_76_out);
  and and_13 (and_13_out, not_77_out, not_78_out, not_79_out, not_80_out, not_81_out, OP0);
  and and_14 (and_14_out, not_82_out, not_83_out, not_84_out, not_85_out, not_86_out, not_87_out, not_88_out, not_89_out, not_90_out, not_91_out, F1, not_92_out);
  and and_15 (and_15_out, not_93_out, not_94_out, not_95_out, not_96_out, not_97_out, not_98_out, F5, not_99_out, not_100_out, not_101_out, F1, not_102_out);
  and and_16 (and_16_out, not_103_out, not_104_out, not_105_out, not_106_out, not_107_out, not_108_out, F5, not_109_out, not_110_out, F2, not_111_out, not_112_out);
  and and_17 (and_17_out, not_113_out, not_114_out, not_115_out, not_116_out, not_117_out, not_118_out, F5, not_119_out, not_120_out, F2, F1, F0);
  and and_18 (and_18_out, not_121_out, not_122_out, not_123_out, not_124_out, not_125_out, not_126_out, F5, not_127_out, F3, not_128_out, F1, not_129_out);
  and and_19 (and_19_out, not_130_out, not_131_out, OP3, OP2, not_132_out, not_133_out);
  and and_20 (and_20_out, not_134_out, not_135_out, OP3, not_136_out, OP1, not_137_out);
  and and_21 (and_21_out, not_138_out, not_139_out, not_140_out, not_141_out, not_142_out, not_143_out, not_144_out, not_145_out, not_146_out, F2, F1, not_147_out);
  and and_22 (and_22_out, not_148_out, not_149_out, not_150_out, not_151_out, not_152_out, OP0);
  and and_23 (and_23_out, not_153_out, not_154_out, not_155_out, not_156_out, not_157_out, not_158_out, F5, not_159_out, not_160_out, not_161_out, not_162_out, not_163_out);
  and and_24 (and_24_out, not_164_out, not_165_out, not_166_out, not_167_out, not_168_out, not_169_out, F5, not_170_out, not_171_out, not_172_out, not_173_out, F0);
  and and_25 (and_25_out, not_174_out, not_175_out, not_176_out, not_177_out, not_178_out, not_179_out, F5, not_180_out, not_181_out, not_182_out, F1, not_183_out);
  and and_26 (and_26_out, not_184_out, not_185_out, not_186_out, not_187_out, not_188_out, not_189_out, F5, not_190_out, not_191_out, F2, not_192_out, not_193_out);
  and and_27 (and_27_out, not_194_out, not_195_out, not_196_out, not_197_out, not_198_out, not_199_out, F5, not_200_out, F3, not_201_out, F1, F0);
  and and_28 (and_28_out, not_202_out, not_203_out, OP3, not_204_out, not_205_out, not_206_out);
  and and_29 (and_29_out, not_207_out, not_208_out, OP3, OP2, not_209_out, not_210_out);
  and and_30 (and_30_out, not_211_out, not_212_out, OP3, not_213_out, not_214_out, OP0);
  and and_31 (and_31_out, OP5, not_215_out, not_216_out, not_217_out, OP1, OP0);
  and and_32 (and_32_out, OP5, not_218_out, OP3, not_219_out, OP1, OP0);
  and and_33 (and_33_out, OP5, not_220_out, not_221_out, OP2, not_222_out, not_223_out);
  and and_34 (and_34_out, not_224_out, not_225_out, not_226_out, not_227_out, not_228_out, not_229_out, F5, not_230_out, not_231_out, F2, not_232_out, F0);
  and and_35 (and_35_out, not_233_out, not_234_out, not_235_out, not_236_out, not_237_out, not_238_out, F5, not_239_out, not_240_out, F2, F1, F0);
  and and_36 (and_36_out, not_241_out, not_242_out, not_243_out, not_244_out, not_245_out, not_246_out, F5, not_247_out, F3, not_248_out, F1, not_249_out);
  and and_37 (and_37_out, not_250_out, not_251_out, not_252_out, not_253_out, not_254_out, not_255_out, F5, not_256_out, F3, not_257_out, F1, F0);
  and and_38 (and_38_out, not_258_out, not_259_out, OP3, not_260_out, OP1, not_261_out);
  and and_39 (and_39_out, not_262_out, not_263_out, OP3, OP2, not_264_out, OP0);
  and and_40 (and_40_out, not_265_out, not_266_out, not_267_out, not_268_out, not_269_out, OP0);
  or or_1 (S1, and_14_out, and_15_out, and_16_out, and_17_out, and_18_out, and_19_out, and_20_out, and_21_out, and_22_out);
  or or_2 (S2, and_23_out, and_24_out, and_25_out, and_26_out, and_27_out, and_28_out, and_29_out, and_30_out, and_31_out, and_32_out, and_33_out);
  or or_3 (S3, and_34_out, and_35_out, and_36_out, and_37_out, and_38_out, and_39_out, and_40_out);
  or or_4 (S0, and_1_out, and_2_out, and_3_out, and_4_out, and_5_out, and_6_out, and_7_out, and_8_out, and_9_out, and_10_out, and_11_out, and_12_out, and_13_out);
endmodule

// 控制信号生成
module \控制信号生成  (
  input  OP0,
  input  OP1,
  input  OP2,
  input  OP3,
  input  OP4,
  input  OP5,
  input  F0,
  input  F1,
  input  F2,
  input  F3,
  input  F4,
  input  F5,
  output MemToReg,
  output MemWrite,
  output ALU_SRC,
  output RegWrite,
  output SysCALL,
  output SignedExt,
  output RegDst,
  output BEQ,
  output BNE,
  output JR,
  output JMP,
  output JAL
);

  wire and_1_out, and_2_out, and_4_out, and_5_out, and_6_out, and_7_out, and_8_out, and_9_out, and_10_out,
       and_11_out, and_12_out, and_13_out, and_14_out, and_15_out, and_16_out, and_17_out, and_18_out,
       and_19_out, and_20_out, and_21_out, and_22_out, and_23_out, and_24_out, and_25_out, and_26_out,
       and_27_out, and_28_out, and_29_out, and_30_out, and_31_out, and_32_out, and_34_out, and_35_out,
       and_36_out, and_37_out, and_38_out, and_39_out, and_40_out, and_41_out, and_42_out, and_43_out,
       and_44_out, and_45_out, and_46_out, and_47_out, and_48_out, and_49_out, and_50_out, and_51_out,
       and_52_out, and_53_out, and_54_out, and_55_out, and_59_out, and_60_out, and_61_out, not_1_out,
       not_2_out, not_3_out, not_4_out, not_5_out, not_6_out, not_7_out, not_8_out, not_9_out, not_10_out,
       not_11_out, not_12_out, not_13_out, not_14_out, not_15_out, not_16_out, not_17_out, not_18_out,
       not_19_out, not_20_out, not_21_out, not_22_out, not_23_out, not_24_out, not_25_out, not_26_out,
       not_27_out, not_28_out, not_29_out, not_30_out, not_31_out, not_32_out, not_33_out, not_34_out,
       not_35_out, not_36_out, not_37_out, not_38_out, not_39_out, not_40_out, not_41_out, not_42_out,
       not_43_out, not_44_out, not_45_out, not_46_out, not_47_out, not_48_out, not_49_out, not_50_out,
       not_51_out, not_52_out, not_53_out, not_54_out, not_55_out, not_56_out, not_57_out, not_58_out,
       not_59_out, not_60_out, not_61_out, not_62_out, not_63_out, not_64_out, not_65_out, not_66_out,
       not_67_out, not_68_out, not_69_out, not_70_out, not_71_out, not_72_out, not_73_out, not_74_out,
       not_75_out, not_76_out, not_77_out, not_78_out, not_79_out, not_80_out, not_81_out, not_82_out,
       not_83_out, not_84_out, not_85_out, not_86_out, not_87_out, not_88_out, not_89_out, not_90_out,
       not_91_out, not_92_out, not_93_out, not_94_out, not_95_out, not_96_out, not_97_out, not_98_out,
       not_99_out, not_100_out, not_101_out, not_102_out, not_103_out, not_104_out, not_105_out, not_106_out,
       not_107_out, not_108_out, not_109_out, not_110_out, not_111_out, not_112_out, not_113_out,
       not_114_out, not_115_out, not_116_out, not_117_out, not_118_out, not_119_out, not_120_out,
       not_121_out, not_122_out, not_123_out, not_124_out, not_125_out, not_126_out, not_127_out,
       not_128_out, not_129_out, not_130_out, not_131_out, not_132_out, not_133_out, not_134_out,
       not_135_out, not_136_out, not_137_out, not_138_out, not_139_out, not_140_out, not_141_out,
       not_142_out, not_143_out, not_144_out, not_145_out, not_146_out, not_147_out, not_148_out,
       not_149_out, not_150_out, not_151_out, not_152_out, not_153_out, not_154_out, not_155_out,
       not_156_out, not_157_out, not_158_out, not_159_out, not_160_out, not_161_out, not_162_out,
       not_163_out, not_164_out, not_165_out, not_166_out, not_167_out, not_168_out, not_169_out,
       not_170_out, not_171_out, not_172_out, not_173_out, not_174_out, not_175_out, not_176_out,
       not_177_out, not_178_out, not_179_out, not_180_out, not_181_out, not_182_out, not_183_out,
       not_184_out, not_185_out, not_186_out, not_187_out, not_188_out, not_189_out, not_190_out,
       not_191_out, not_192_out, not_193_out, not_194_out, not_195_out, not_196_out, not_197_out,
       not_198_out, not_199_out, not_200_out, not_201_out, not_202_out, not_203_out, not_204_out,
       not_205_out, not_206_out, not_207_out, not_208_out, not_209_out, not_210_out, not_211_out,
       not_212_out, not_213_out, not_214_out, not_215_out, not_216_out, not_217_out, not_218_out,
       not_219_out, not_220_out, not_221_out, not_222_out, not_223_out, not_224_out, not_225_out,
       not_226_out, not_227_out, not_228_out, not_229_out, not_230_out, not_231_out, not_232_out,
       not_233_out, not_234_out, not_235_out, not_236_out, not_237_out, not_238_out, not_239_out,
       not_240_out, not_241_out, not_242_out, not_243_out, not_244_out, not_245_out, not_246_out,
       not_247_out, not_248_out, not_249_out, not_250_out, not_251_out, not_252_out, not_253_out,
       not_254_out, not_255_out, not_256_out, not_257_out, not_258_out, not_259_out, not_260_out,
       not_261_out, not_262_out, not_263_out, not_264_out, not_265_out, not_266_out, not_267_out,
       not_268_out, not_269_out, not_270_out, not_271_out, not_272_out, not_273_out, not_274_out,
       not_275_out, not_276_out, not_277_out, not_278_out, not_279_out, not_280_out, not_281_out,
       not_282_out, not_283_out, not_284_out, not_285_out, not_286_out, not_287_out, not_288_out,
       not_289_out, not_290_out, not_291_out, not_292_out, not_293_out, not_294_out, not_295_out,
       not_296_out, not_297_out, not_298_out, not_299_out, not_300_out, not_301_out, not_302_out,
       not_303_out, not_304_out, not_305_out, not_306_out, not_307_out, not_308_out, not_309_out,
       not_310_out, not_311_out, not_312_out, not_313_out, not_314_out, not_315_out, not_316_out,
       not_317_out, not_318_out, not_319_out, not_320_out, not_321_out, not_322_out, not_323_out,
       not_324_out, not_325_out, not_326_out, not_327_out, not_328_out, not_329_out, not_330_out,
       not_331_out, not_332_out, not_333_out, not_334_out, not_335_out, not_336_out, not_337_out,
       not_338_out, not_339_out, not_340_out, not_341_out, not_342_out, not_343_out, not_344_out,
       not_345_out, not_346_out, not_347_out, not_348_out, not_349_out, not_350_out, not_351_out,
       not_352_out, not_353_out, not_354_out, not_355_out, not_356_out, not_357_out, not_358_out,
       not_359_out, not_360_out, not_361_out, not_362_out, not_363_out, not_364_out, not_365_out,
       not_366_out, not_367_out, not_368_out, not_369_out, not_370_out, not_371_out, not_372_out,
       not_373_out, not_374_out, not_375_out, not_376_out, not_377_out, not_378_out, not_379_out,
       not_380_out, not_381_out, not_382_out, not_383_out, not_384_out, not_385_out, not_386_out,
       not_387_out, not_388_out, not_389_out, not_390_out, not_391_out, not_392_out, not_393_out,
       not_394_out, not_395_out, not_396_out, not_397_out, not_398_out, not_399_out, not_400_out,
       not_401_out, not_402_out, not_403_out, not_404_out, not_405_out, not_406_out, not_407_out,
       not_408_out, not_409_out, not_410_out, not_411_out, not_412_out, not_413_out, not_414_out,
       not_415_out, not_416_out, not_417_out;

  not not_1 (not_1_out, OP4);
  not not_2 (not_2_out, OP3);
  not not_3 (not_3_out, OP2);
  not not_4 (not_4_out, OP4);
  not not_5 (not_5_out, OP3);
  not not_6 (not_6_out, OP1);
  not not_7 (not_7_out, OP0);
  not not_8 (not_8_out, OP4);
  not not_9 (not_9_out, OP2);
  not not_10 (not_10_out, OP5);
  not not_11 (not_11_out, OP4);
  not not_12 (not_12_out, OP2);
  not not_13 (not_13_out, OP1);
  not not_14 (not_14_out, OP0);
  not not_15 (not_15_out, OP5);
  not not_16 (not_16_out, OP4);
  not not_17 (not_17_out, OP1);
  not not_18 (not_18_out, OP0);
  not not_19 (not_19_out, OP5);
  not not_20 (not_20_out, OP4);
  not not_21 (not_21_out, OP2);
  not not_22 (not_22_out, OP1);
  not not_23 (not_23_out, OP5);
  not not_24 (not_24_out, OP4);
  not not_25 (not_25_out, OP2);
  not not_26 (not_26_out, OP0);
  not not_27 (not_27_out, OP5);
  not not_28 (not_28_out, OP4);
  not not_29 (not_29_out, OP1);
  not not_30 (not_30_out, OP4);
  not not_31 (not_31_out, OP3);
  not not_32 (not_32_out, OP2);
  not not_33 (not_33_out, OP4);
  not not_34 (not_34_out, OP2);
  not not_35 (not_35_out, OP4);
  not not_36 (not_36_out, OP3);
  not not_37 (not_37_out, OP1);
  not not_38 (not_38_out, OP0);
  not not_39 (not_39_out, OP5);
  not not_40 (not_40_out, OP4);
  not not_41 (not_41_out, OP3);
  not not_42 (not_42_out, OP2);
  not not_43 (not_43_out, OP1);
  not not_44 (not_44_out, OP0);
  not not_45 (not_45_out, F5);
  not not_46 (not_46_out, F4);
  not not_47 (not_47_out, F3);
  not not_48 (not_48_out, F2);
  not not_49 (not_49_out, F1);
  not not_50 (not_50_out, F0);
  not not_51 (not_51_out, OP5);
  not not_52 (not_52_out, OP4);
  not not_53 (not_53_out, OP3);
  not not_54 (not_54_out, OP2);
  not not_55 (not_55_out, OP1);
  not not_56 (not_56_out, OP0);
  not not_57 (not_57_out, F5);
  not not_58 (not_58_out, F4);
  not not_59 (not_59_out, F3);
  not not_60 (not_60_out, F2);
  not not_61 (not_61_out, OP5);
  not not_62 (not_62_out, OP4);
  not not_63 (not_63_out, OP3);
  not not_64 (not_64_out, OP2);
  not not_65 (not_65_out, OP1);
  not not_66 (not_66_out, OP0);
  not not_67 (not_67_out, F5);
  not not_68 (not_68_out, F4);
  not not_69 (not_69_out, F3);
  not not_70 (not_70_out, F2);
  not not_71 (not_71_out, F0);
  not not_72 (not_72_out, OP5);
  not not_73 (not_73_out, OP4);
  not not_74 (not_74_out, OP3);
  not not_75 (not_75_out, OP2);
  not not_76 (not_76_out, OP1);
  not not_77 (not_77_out, OP0);
  not not_78 (not_78_out, F4);
  not not_79 (not_79_out, F3);
  not not_80 (not_80_out, F2);
  not not_81 (not_81_out, F1);
  not not_82 (not_82_out, F0);
  not not_83 (not_83_out, OP5);
  not not_84 (not_84_out, OP4);
  not not_85 (not_85_out, OP3);
  not not_86 (not_86_out, OP2);
  not not_87 (not_87_out, OP1);
  not not_88 (not_88_out, OP0);
  not not_89 (not_89_out, F4);
  not not_90 (not_90_out, F3);
  not not_91 (not_91_out, F2);
  not not_92 (not_92_out, F1);
  not not_93 (not_93_out, OP5);
  not not_94 (not_94_out, OP4);
  not not_95 (not_95_out, OP3);
  not not_96 (not_96_out, OP2);
  not not_97 (not_97_out, OP1);
  not not_98 (not_98_out, OP0);
  not not_99 (not_99_out, F4);
  not not_100 (not_100_out, F3);
  not not_101 (not_101_out, F2);
  not not_102 (not_102_out, F0);
  not not_103 (not_103_out, OP5);
  not not_104 (not_104_out, OP4);
  not not_105 (not_105_out, OP3);
  not not_106 (not_106_out, OP2);
  not not_107 (not_107_out, OP1);
  not not_108 (not_108_out, OP0);
  not not_109 (not_109_out, F4);
  not not_110 (not_110_out, F3);
  not not_111 (not_111_out, F1);
  not not_112 (not_112_out, F0);
  not not_113 (not_113_out, OP5);
  not not_114 (not_114_out, OP4);
  not not_115 (not_115_out, OP3);
  not not_116 (not_116_out, OP2);
  not not_117 (not_117_out, OP1);
  not not_118 (not_118_out, OP0);
  not not_119 (not_119_out, F4);
  not not_120 (not_120_out, F3);
  not not_121 (not_121_out, F1);
  not not_122 (not_122_out, OP5);
  not not_123 (not_123_out, OP4);
  not not_124 (not_124_out, OP3);
  not not_125 (not_125_out, OP2);
  not not_126 (not_126_out, OP1);
  not not_127 (not_127_out, OP0);
  not not_128 (not_128_out, F4);
  not not_129 (not_129_out, F3);
  not not_130 (not_130_out, OP5);
  not not_131 (not_131_out, OP4);
  not not_132 (not_132_out, OP3);
  not not_133 (not_133_out, OP2);
  not not_134 (not_134_out, OP1);
  not not_135 (not_135_out, OP0);
  not not_136 (not_136_out, F4);
  not not_137 (not_137_out, F2);
  not not_138 (not_138_out, F0);
  not not_139 (not_139_out, OP5);
  not not_140 (not_140_out, OP4);
  not not_141 (not_141_out, OP3);
  not not_142 (not_142_out, OP2);
  not not_143 (not_143_out, OP1);
  not not_144 (not_144_out, OP0);
  not not_145 (not_145_out, F4);
  not not_146 (not_146_out, F2);
  not not_147 (not_147_out, OP5);
  not not_148 (not_148_out, OP4);
  not not_149 (not_149_out, OP3);
  not not_150 (not_150_out, OP2);
  not not_151 (not_151_out, OP5);
  not not_152 (not_152_out, OP4);
  not not_153 (not_153_out, OP2);
  not not_154 (not_154_out, OP1);
  not not_155 (not_155_out, OP0);
  not not_156 (not_156_out, OP5);
  not not_157 (not_157_out, OP4);
  not not_158 (not_158_out, OP1);
  not not_159 (not_159_out, OP0);
  not not_160 (not_160_out, OP5);
  not not_161 (not_161_out, OP4);
  not not_162 (not_162_out, OP2);
  not not_163 (not_163_out, OP1);
  not not_164 (not_164_out, OP5);
  not not_165 (not_165_out, OP4);
  not not_166 (not_166_out, OP2);
  not not_167 (not_167_out, OP0);
  not not_168 (not_168_out, OP5);
  not not_169 (not_169_out, OP4);
  not not_170 (not_170_out, OP1);
  not not_171 (not_171_out, OP4);
  not not_172 (not_172_out, OP3);
  not not_173 (not_173_out, OP2);
  not not_174 (not_174_out, OP5);
  not not_175 (not_175_out, OP4);
  not not_176 (not_176_out, OP3);
  not not_177 (not_177_out, OP2);
  not not_178 (not_178_out, OP1);
  not not_179 (not_179_out, OP0);
  not not_180 (not_180_out, F5);
  not not_181 (not_181_out, F4);
  not not_182 (not_182_out, F3);
  not not_183 (not_183_out, F1);
  not not_184 (not_184_out, F0);
  not not_185 (not_185_out, OP5);
  not not_186 (not_186_out, OP4);
  not not_187 (not_187_out, OP3);
  not not_188 (not_188_out, OP2);
  not not_189 (not_189_out, OP1);
  not not_190 (not_190_out, OP0);
  not not_191 (not_191_out, F5);
  not not_192 (not_192_out, F4);
  not not_193 (not_193_out, F3);
  not not_194 (not_194_out, F0);
  not not_195 (not_195_out, OP4);
  not not_196 (not_196_out, OP3);
  not not_197 (not_197_out, OP1);
  not not_198 (not_198_out, OP0);
  not not_199 (not_199_out, OP5);
  not not_200 (not_200_out, OP4);
  not not_201 (not_201_out, OP3);
  not not_202 (not_202_out, OP2);
  not not_203 (not_203_out, OP1);
  not not_204 (not_204_out, OP0);
  not not_205 (not_205_out, F5);
  not not_206 (not_206_out, F4);
  not not_207 (not_207_out, F1);
  not not_208 (not_208_out, F0);
  not not_209 (not_209_out, OP5);
  not not_210 (not_210_out, OP4);
  not not_211 (not_211_out, OP3);
  not not_212 (not_212_out, OP1);
  not not_213 (not_213_out, OP0);
  not not_214 (not_214_out, OP5);
  not not_215 (not_215_out, OP4);
  not not_216 (not_216_out, OP3);
  not not_217 (not_217_out, OP1);
  not not_218 (not_218_out, OP5);
  not not_219 (not_219_out, OP4);
  not not_220 (not_220_out, OP2);
  not not_221 (not_221_out, OP1);
  not not_222 (not_222_out, OP0);
  not not_223 (not_223_out, OP5);
  not not_224 (not_224_out, OP4);
  not not_225 (not_225_out, OP2);
  not not_226 (not_226_out, OP1);
  not not_227 (not_227_out, OP5);
  not not_228 (not_228_out, OP4);
  not not_229 (not_229_out, OP2);
  not not_230 (not_230_out, OP0);
  not not_231 (not_231_out, OP4);
  not not_232 (not_232_out, OP3);
  not not_233 (not_233_out, OP2);
  not not_234 (not_234_out, OP4);
  not not_235 (not_235_out, OP2);
  not not_236 (not_236_out, OP4);
  not not_237 (not_237_out, OP3);
  not not_238 (not_238_out, OP1);
  not not_239 (not_239_out, OP0);
  not not_240 (not_240_out, OP5);
  not not_241 (not_241_out, OP4);
  not not_242 (not_242_out, OP3);
  not not_243 (not_243_out, OP2);
  not not_244 (not_244_out, OP1);
  not not_245 (not_245_out, OP5);
  not not_246 (not_246_out, OP4);
  not not_247 (not_247_out, OP3);
  not not_248 (not_248_out, OP2);
  not not_249 (not_249_out, OP1);
  not not_250 (not_250_out, OP0);
  not not_251 (not_251_out, F5);
  not not_252 (not_252_out, F4);
  not not_253 (not_253_out, F3);
  not not_254 (not_254_out, F2);
  not not_255 (not_255_out, F1);
  not not_256 (not_256_out, F0);
  not not_257 (not_257_out, OP5);
  not not_258 (not_258_out, OP4);
  not not_259 (not_259_out, OP3);
  not not_260 (not_260_out, OP2);
  not not_261 (not_261_out, OP1);
  not not_262 (not_262_out, OP0);
  not not_263 (not_263_out, F5);
  not not_264 (not_264_out, F4);
  not not_265 (not_265_out, F3);
  not not_266 (not_266_out, F2);
  not not_267 (not_267_out, OP5);
  not not_268 (not_268_out, OP4);
  not not_269 (not_269_out, OP3);
  not not_270 (not_270_out, OP2);
  not not_271 (not_271_out, OP1);
  not not_272 (not_272_out, OP0);
  not not_273 (not_273_out, F5);
  not not_274 (not_274_out, F4);
  not not_275 (not_275_out, F3);
  not not_276 (not_276_out, F2);
  not not_277 (not_277_out, F0);
  not not_278 (not_278_out, OP5);
  not not_279 (not_279_out, OP4);
  not not_280 (not_280_out, OP3);
  not not_281 (not_281_out, OP2);
  not not_282 (not_282_out, OP1);
  not not_283 (not_283_out, OP0);
  not not_284 (not_284_out, F4);
  not not_285 (not_285_out, F3);
  not not_286 (not_286_out, F2);
  not not_287 (not_287_out, F1);
  not not_288 (not_288_out, F0);
  not not_289 (not_289_out, OP5);
  not not_290 (not_290_out, OP4);
  not not_291 (not_291_out, OP3);
  not not_292 (not_292_out, OP2);
  not not_293 (not_293_out, OP1);
  not not_294 (not_294_out, OP0);
  not not_295 (not_295_out, F4);
  not not_296 (not_296_out, F3);
  not not_297 (not_297_out, F2);
  not not_298 (not_298_out, F1);
  not not_299 (not_299_out, OP5);
  not not_300 (not_300_out, OP4);
  not not_301 (not_301_out, OP3);
  not not_302 (not_302_out, OP2);
  not not_303 (not_303_out, OP1);
  not not_304 (not_304_out, OP0);
  not not_305 (not_305_out, F4);
  not not_306 (not_306_out, F3);
  not not_307 (not_307_out, F2);
  not not_308 (not_308_out, F0);
  not not_309 (not_309_out, OP5);
  not not_310 (not_310_out, OP4);
  not not_311 (not_311_out, OP3);
  not not_312 (not_312_out, OP2);
  not not_313 (not_313_out, OP1);
  not not_314 (not_314_out, OP0);
  not not_315 (not_315_out, F4);
  not not_316 (not_316_out, F3);
  not not_317 (not_317_out, F1);
  not not_318 (not_318_out, F0);
  not not_319 (not_319_out, OP5);
  not not_320 (not_320_out, OP4);
  not not_321 (not_321_out, OP3);
  not not_322 (not_322_out, OP2);
  not not_323 (not_323_out, OP1);
  not not_324 (not_324_out, OP0);
  not not_325 (not_325_out, F4);
  not not_326 (not_326_out, F3);
  not not_327 (not_327_out, F1);
  not not_328 (not_328_out, OP5);
  not not_329 (not_329_out, OP4);
  not not_330 (not_330_out, OP3);
  not not_331 (not_331_out, OP2);
  not not_332 (not_332_out, OP1);
  not not_333 (not_333_out, OP0);
  not not_334 (not_334_out, F4);
  not not_335 (not_335_out, F3);
  not not_336 (not_336_out, OP5);
  not not_337 (not_337_out, OP4);
  not not_338 (not_338_out, OP3);
  not not_339 (not_339_out, OP2);
  not not_340 (not_340_out, OP1);
  not not_341 (not_341_out, OP0);
  not not_342 (not_342_out, F4);
  not not_343 (not_343_out, F2);
  not not_344 (not_344_out, F0);
  not not_345 (not_345_out, OP5);
  not not_346 (not_346_out, OP4);
  not not_347 (not_347_out, OP3);
  not not_348 (not_348_out, OP2);
  not not_349 (not_349_out, OP1);
  not not_350 (not_350_out, OP0);
  not not_351 (not_351_out, F4);
  not not_352 (not_352_out, F2);
  not not_353 (not_353_out, OP5);
  not not_354 (not_354_out, OP4);
  not not_355 (not_355_out, OP3);
  not not_356 (not_356_out, OP2);
  not not_357 (not_357_out, OP1);
  not not_358 (not_358_out, OP0);
  not not_359 (not_359_out, F5);
  not not_360 (not_360_out, F4);
  not not_361 (not_361_out, F3);
  not not_362 (not_362_out, F1);
  not not_363 (not_363_out, F0);
  not not_364 (not_364_out, OP5);
  not not_365 (not_365_out, OP4);
  not not_366 (not_366_out, OP3);
  not not_367 (not_367_out, OP2);
  not not_368 (not_368_out, OP1);
  not not_369 (not_369_out, OP0);
  not not_370 (not_370_out, F5);
  not not_371 (not_371_out, F4);
  not not_372 (not_372_out, F3);
  not not_373 (not_373_out, F0);
  not not_374 (not_374_out, OP5);
  not not_375 (not_375_out, OP4);
  not not_376 (not_376_out, OP3);
  not not_377 (not_377_out, OP1);
  not not_378 (not_378_out, OP0);
  not not_379 (not_379_out, OP5);
  not not_380 (not_380_out, OP4);
  not not_381 (not_381_out, OP3);
  not not_382 (not_382_out, OP1);
  not not_383 (not_383_out, OP5);
  not not_384 (not_384_out, OP4);
  not not_385 (not_385_out, OP3);
  not not_386 (not_386_out, OP2);
  not not_387 (not_387_out, OP1);
  not not_388 (not_388_out, OP0);
  not not_389 (not_389_out, F5);
  not not_390 (not_390_out, F4);
  not not_391 (not_391_out, F2);
  not not_392 (not_392_out, F1);
  not not_393 (not_393_out, F0);
  not not_394 (not_394_out, OP5);
  not not_395 (not_395_out, OP4);
  not not_396 (not_396_out, OP3);
  not not_397 (not_397_out, OP2);
  not not_398 (not_398_out, OP1);
  not not_399 (not_399_out, OP0);
  not not_400 (not_400_out, F5);
  not not_401 (not_401_out, F4);
  not not_402 (not_402_out, F2);
  not not_403 (not_403_out, F1);
  not not_404 (not_404_out, F0);
  not not_405 (not_405_out, OP5);
  not not_406 (not_406_out, OP4);
  not not_407 (not_407_out, OP3);
  not not_408 (not_408_out, OP2);
  not not_409 (not_409_out, OP0);
  not not_410 (not_410_out, OP5);
  not not_411 (not_411_out, OP4);
  not not_412 (not_412_out, OP3);
  not not_413 (not_413_out, OP2);
  not not_414 (not_414_out, OP5);
  not not_415 (not_415_out, OP4);
  not not_416 (not_416_out, OP3);
  not not_417 (not_417_out, OP2);
  and and_1 (and_1_out, OP5, not_1_out, not_2_out, not_3_out, OP1, OP0);
  and and_2 (and_2_out, OP5, not_4_out, not_5_out, OP2, not_6_out, not_7_out);
  and and_3 (MemWrite, OP5, not_8_out, OP3, not_9_out, OP1, OP0);
  and and_4 (and_4_out, not_10_out, not_11_out, OP3, not_12_out, not_13_out, not_14_out);
  and and_5 (and_5_out, not_15_out, not_16_out, OP3, OP2, not_17_out, not_18_out);
  and and_6 (and_6_out, not_19_out, not_20_out, OP3, not_21_out, not_22_out, OP0);
  and and_7 (and_7_out, not_23_out, not_24_out, OP3, not_25_out, OP1, not_26_out);
  and and_8 (and_8_out, not_27_out, not_28_out, OP3, OP2, not_29_out, OP0);
  and and_9 (and_9_out, OP5, not_30_out, not_31_out, not_32_out, OP1, OP0);
  and and_10 (and_10_out, OP5, not_33_out, OP3, not_34_out, OP1, OP0);
  and and_11 (and_11_out, OP5, not_35_out, not_36_out, OP2, not_37_out, not_38_out);
  and and_12 (and_12_out, not_39_out, not_40_out, not_41_out, not_42_out, not_43_out, not_44_out, not_45_out, not_46_out, not_47_out, not_48_out, not_49_out, not_50_out);
  and and_13 (and_13_out, not_51_out, not_52_out, not_53_out, not_54_out, not_55_out, not_56_out, not_57_out, not_58_out, not_59_out, not_60_out, F1, F0);
  and and_14 (and_14_out, not_61_out, not_62_out, not_63_out, not_64_out, not_65_out, not_66_out, not_67_out, not_68_out, not_69_out, not_70_out, F1, not_71_out);
  and and_15 (and_15_out, not_72_out, not_73_out, not_74_out, not_75_out, not_76_out, not_77_out, F5, not_78_out, not_79_out, not_80_out, not_81_out, not_82_out);
  and and_16 (and_16_out, not_83_out, not_84_out, not_85_out, not_86_out, not_87_out, not_88_out, F5, not_89_out, not_90_out, not_91_out, not_92_out, F0);
  and and_17 (and_17_out, not_93_out, not_94_out, not_95_out, not_96_out, not_97_out, not_98_out, F5, not_99_out, not_100_out, not_101_out, F1, not_102_out);
  and and_18 (and_18_out, not_103_out, not_104_out, not_105_out, not_106_out, not_107_out, not_108_out, F5, not_109_out, not_110_out, F2, not_111_out, not_112_out);
  and and_19 (and_19_out, not_113_out, not_114_out, not_115_out, not_116_out, not_117_out, not_118_out, F5, not_119_out, not_120_out, F2, not_121_out, F0);
  and and_20 (and_20_out, not_122_out, not_123_out, not_124_out, not_125_out, not_126_out, not_127_out, F5, not_128_out, not_129_out, F2, F1, F0);
  and and_21 (and_21_out, not_130_out, not_131_out, not_132_out, not_133_out, not_134_out, not_135_out, F5, not_136_out, F3, not_137_out, F1, not_138_out);
  and and_22 (and_22_out, not_139_out, not_140_out, not_141_out, not_142_out, not_143_out, not_144_out, F5, not_145_out, F3, not_146_out, F1, F0);
  and and_23 (and_23_out, not_147_out, not_148_out, not_149_out, not_150_out, OP1, OP0);
  and and_24 (and_24_out, not_151_out, not_152_out, OP3, not_153_out, not_154_out, not_155_out);
  and and_25 (and_25_out, not_156_out, not_157_out, OP3, OP2, not_158_out, not_159_out);
  and and_26 (and_26_out, not_160_out, not_161_out, OP3, not_162_out, not_163_out, OP0);
  and and_27 (and_27_out, not_164_out, not_165_out, OP3, not_166_out, OP1, not_167_out);
  and and_28 (and_28_out, not_168_out, not_169_out, OP3, OP2, not_170_out, OP0);
  and and_29 (and_29_out, OP5, not_171_out, not_172_out, not_173_out, OP1, OP0);
  and and_30 (and_30_out, not_174_out, not_175_out, not_176_out, not_177_out, not_178_out, not_179_out, not_180_out, not_181_out, not_182_out, F2, not_183_out, not_184_out);
  and and_31 (and_31_out, not_185_out, not_186_out, not_187_out, not_188_out, not_189_out, not_190_out, not_191_out, not_192_out, not_193_out, F2, F1, not_194_out);
  and and_32 (and_32_out, OP5, not_195_out, not_196_out, OP2, not_197_out, not_198_out);
  and and_33 (SysCALL, not_199_out, not_200_out, not_201_out, not_202_out, not_203_out, not_204_out, not_205_out, not_206_out, F3, F2, not_207_out, not_208_out);
  and and_34 (and_34_out, not_209_out, not_210_out, not_211_out, OP2, not_212_out, not_213_out);
  and and_35 (and_35_out, not_214_out, not_215_out, not_216_out, OP2, not_217_out, OP0);
  and and_36 (and_36_out, not_218_out, not_219_out, OP3, not_220_out, not_221_out, not_222_out);
  and and_37 (and_37_out, not_223_out, not_224_out, OP3, not_225_out, not_226_out, OP0);
  and and_38 (and_38_out, not_227_out, not_228_out, OP3, not_229_out, OP1, not_230_out);
  and and_39 (and_39_out, OP5, not_231_out, not_232_out, not_233_out, OP1, OP0);
  and and_40 (and_40_out, OP5, not_234_out, OP3, not_235_out, OP1, OP0);
  and and_41 (and_41_out, OP5, not_236_out, not_237_out, OP2, not_238_out, not_239_out);
  and and_42 (and_42_out, not_240_out, not_241_out, not_242_out, not_243_out, not_244_out, OP0);
  and and_43 (and_43_out, not_245_out, not_246_out, not_247_out, not_248_out, not_249_out, not_250_out, not_251_out, not_252_out, not_253_out, not_254_out, not_255_out, not_256_out);
  and and_44 (and_44_out, not_257_out, not_258_out, not_259_out, not_260_out, not_261_out, not_262_out, not_263_out, not_264_out, not_265_out, not_266_out, F1, F0);
  and and_45 (and_45_out, not_267_out, not_268_out, not_269_out, not_270_out, not_271_out, not_272_out, not_273_out, not_274_out, not_275_out, not_276_out, F1, not_277_out);
  and and_46 (and_46_out, not_278_out, not_279_out, not_280_out, not_281_out, not_282_out, not_283_out, F5, not_284_out, not_285_out, not_286_out, not_287_out, not_288_out);
  and and_47 (and_47_out, not_289_out, not_290_out, not_291_out, not_292_out, not_293_out, not_294_out, F5, not_295_out, not_296_out, not_297_out, not_298_out, F0);
  and and_48 (and_48_out, not_299_out, not_300_out, not_301_out, not_302_out, not_303_out, not_304_out, F5, not_305_out, not_306_out, not_307_out, F1, not_308_out);
  and and_49 (and_49_out, not_309_out, not_310_out, not_311_out, not_312_out, not_313_out, not_314_out, F5, not_315_out, not_316_out, F2, not_317_out, not_318_out);
  and and_50 (and_50_out, not_319_out, not_320_out, not_321_out, not_322_out, not_323_out, not_324_out, F5, not_325_out, not_326_out, F2, not_327_out, F0);
  and and_51 (and_51_out, not_328_out, not_329_out, not_330_out, not_331_out, not_332_out, not_333_out, F5, not_334_out, not_335_out, F2, F1, F0);
  and and_52 (and_52_out, not_336_out, not_337_out, not_338_out, not_339_out, not_340_out, not_341_out, F5, not_342_out, F3, not_343_out, F1, not_344_out);
  and and_53 (and_53_out, not_345_out, not_346_out, not_347_out, not_348_out, not_349_out, not_350_out, F5, not_351_out, F3, not_352_out, F1, F0);
  and and_54 (and_54_out, not_353_out, not_354_out, not_355_out, not_356_out, not_357_out, not_358_out, not_359_out, not_360_out, not_361_out, F2, not_362_out, not_363_out);
  and and_55 (and_55_out, not_364_out, not_365_out, not_366_out, not_367_out, not_368_out, not_369_out, not_370_out, not_371_out, not_372_out, F2, F1, not_373_out);
  and and_56 (BEQ, not_374_out, not_375_out, not_376_out, OP2, not_377_out, not_378_out);
  and and_57 (BNE, not_379_out, not_380_out, not_381_out, OP2, not_382_out, OP0);
  and and_58 (JR, not_383_out, not_384_out, not_385_out, not_386_out, not_387_out, not_388_out, not_389_out, not_390_out, F3, not_391_out, not_392_out, not_393_out);
  and and_59 (and_59_out, not_394_out, not_395_out, not_396_out, not_397_out, not_398_out, not_399_out, not_400_out, not_401_out, F3, not_402_out, not_403_out, not_404_out);
  and and_60 (and_60_out, not_405_out, not_406_out, not_407_out, not_408_out, OP1, not_409_out);
  and and_61 (and_61_out, not_410_out, not_411_out, not_412_out, not_413_out, OP1, OP0);
  and and_62 (JAL, not_414_out, not_415_out, not_416_out, not_417_out, OP1, OP0);
  or or_1 (MemToReg, and_1_out, and_2_out);
  or or_2 (ALU_SRC, and_4_out, and_5_out, and_6_out, and_7_out, and_8_out, and_9_out, and_10_out, and_11_out);
  or or_3 (SignedExt, and_34_out, and_35_out, and_36_out, and_37_out, and_38_out, and_39_out, and_40_out, and_41_out, and_42_out);
  or or_4 (JMP, and_59_out, and_60_out, and_61_out);
  or or_5 (RegWrite, and_12_out, and_13_out, and_14_out, and_15_out, and_16_out, and_17_out, and_18_out, and_19_out, and_20_out, and_21_out, and_22_out, and_23_out, and_24_out, and_25_out, and_26_out, and_27_out, and_28_out, and_29_out, and_30_out, and_31_out, and_32_out);
  or or_6 (RegDst, and_43_out, and_44_out, and_45_out, and_46_out, and_47_out, and_48_out, and_49_out, and_50_out, and_51_out, and_52_out, and_53_out, and_54_out, and_55_out);
endmodule

// ALU
module MIPS_ALU (
  input  [4:0] shamt,
  input  [31:0] X,
  input  [31:0] Y,
  input  [3:0] AluOP,
  output Equal,
  output [31:0] Result,
  output [31:0] Result_2
);

  wire [0:0] comparator_1_lt, comparator_2_lt;
  wire [31:0] adder_1_out, AND_out, divider_1_out, divider_1_rem, multiplier_1_cout, multiplier_1_out,
       NOR_out, OR_out, shifter_1_out, shifter_2_out, shifter_3_out, subtractor_1_out, XOR_out;

  assign AND_out = X & Y;  // AND_Gate AND, 32 bits wide
  assign OR_out = X | Y;  // OR_Gate OR, 32 bits wide
  Shifter #(.width(32)) shifter_1 (.in(Y), .\dist (shamt), .out(shifter_1_out));
  Shifter #(.width(32), .shift("ar")) shifter_2 (.in(Y), .\dist (shamt), .out(shifter_2_out));
  Shifter #(.width(32), .shift("lr")) shifter_3 (.in(Y), .\dist (shamt), .out(shifter_3_out));
  Multiplier #(.width(32)) multiplier_1 (.a(X), .b(Y), .out(multiplier_1_out), .cout(multiplier_1_cout));  // open: cin
  Divider #(.width(32)) divider_1 (.a(X), .b(Y), .out(divider_1_out), .rem(divider_1_rem));  // open: upper
  Adder #(.width(32)) adder_1 (.a(X), .b(Y), .out(adder_1_out));  // open: cin, cout
  Subtractor #(.width(32)) subtractor_1 (.a(X), .b(Y), .out(subtractor_1_out));  // open: bin, bout
  assign XOR_out = X ^ Y;  // XOR_Gate XOR, 32 bits wide
  assign NOR_out = ~(X | Y);  // NOR_Gate NOR, 32 bits wide
  Comparator #(.width(32)) comparator_1 (.a(X), .b(Y), .eq(Equal), .lt(comparator_1_lt[0]));  // open: gt
  Comparator #(.width(32), .mode("unsigned")) comparator_2 (.a(X), .b(Y), .lt(comparator_2_lt[0]));  // open: gt, eq
  Multiplexer #(.select(4), .width(32), .enable("false")) multiplexer_1 (
    .in0(shifter_1_out), .in1(shifter_2_out), .in2(shifter_3_out), .in3(multiplier_1_out),
    .in4(divider_1_out), .in5(adder_1_out), .in6(subtractor_1_out), .in7(AND_out), .in8(OR_out),
    .in9(XOR_out), .in10(NOR_out), .in11({{31{1'b0}}, comparator_1_lt[0]}),
    .in12({{31{1'b0}}, comparator_2_lt[0]}), .in13({32{1'b0}}), .in14({32{1'b0}}), .in15({32{1'b0}}),
    .out(Result), .sel(AluOP));
  Multiplexer #(.select(4), .width(32), .enable("false")) multiplexer_2 (
    .in0({32{1'b0}}), .in1({32{1'b0}}), .in2({32{1'b0}}), .in3(multiplier_1_cout), .in4(divider_1_rem),
    .in5({32{1'b0}}), .in6({32{1'b0}}), .in7({32{1'b0}}), .in8({32{1'b0}}), .in9({32{1'b0}}),
    .in10({32{1'b0}}), .in11({32{1'b0}}), .in12({32{1'b0}}), .in13({32{1'b0}}), .in14({32{1'b0}}),
    .in15({32{1'b0}}), .out(Result_2), .sel(AluOP));

  // Other names for the same wires on the sheet: Result2[31:0] = Result_2; S[3:0] = AluOP

  // Notes on the sheet:
  //   不要改变此引脚区域内容，也不要改变ALU封装形式
  //   输入引脚
  //   输出引脚
endmodule

module MIPS_Regifile (
  input  [31:0] Din,
  input  Clk,
  input  WE,
  input  [4:0] R1_num,
  input  [4:0] W_num,
  input  [4:0] R2_num,
  output [31:0] R1,
  output [31:0] R2
);

  // RegisterFile registerfile_1: pin names not known; wires that end beside it: Din, Clk, WE, W_num, R1_num, R2_num, R1, R2
endmodule

module \理想流水线  (
);

  wire and_1_out, and_2_out, and_3_out, and_5_out, CLK, comparator_1_eq, comparator_2_eq, Cond, EX_Beq,
       EX_BLTZ, EX_Bne, EX_Jmp, EX_JR, ex_mem_1_mem_jal, ex_mem_1_mem_memtoreg, ex_mem_1_mem_regwrite,
       ex_mem_1_mem_stop, \ex_mem_1_传输状态out_表明当前传输数据有效 , EX_Shift, Go, ID_BLTZ, id_ex_1_ex_alusrcb,
       id_ex_1_ex_jal, id_ex_1_ex_lbu, id_ex_1_ex_memtoreg, id_ex_1_ex_memwrite, id_ex_1_ex_regwrite,
       id_ex_1_ex_syscall, \id_ex_1_传输状态out_表明当前传输数据有效 , ID_JAL, ID_Jmp, ID_JR, ID_LBU, ID_RegDst, ID_Shift,
       ID_SignedExt, ID_stop, ID_Syscall, \if_id_1_传输状态out_表明当前传输数据有效 , IR1, IR2, IR3, MEM_LBU, MEM_MemWrite,
       mem_wb_1_wb_jal, mips_alu_1_equal, not_1_out, not_2_out, not_3_out, not_4_out, RST, Run, W1, W2, W3,
       WB_RegWrite, WE_stop, \硬布线控制器_1_alu_src , \硬布线控制器_1_beq , \硬布线控制器_1_bne , \硬布线控制器_1_memtoreg ,
       \硬布线控制器_1_memwrite , \硬布线控制器_1_regwrite , \硬布线控制器_1_sllv , \硬布线控制器_1_srlv ;
  wire [3:0] id_ex_1_ex_aluop, \硬布线控制器_1_alu_op ;
  wire [4:0] ex_mem_1_mem_w_num, id_ex_1_ex_shamt, id_ex_1_ex_w_num, ID_W_num, if_id_1_id_ir_3,
       if_id_1_id_ir_4, if_id_1_id_ir_5, if_id_1_id_ir_6, multiplexer_2_out, multiplexer_3_out,
       multiplexer_4_out, multiplexer_8_out, R1, WB_W_num;
  wire [5:0] if_id_1_id_ir, if_id_1_id_ir_2;
  wire [7:0] multiplexer_10_out;
  wire [15:0] \LoadUse次数 , \总周期数 , \插入气泡数 , \无条件分支数 , \条件分支成功数 ;
  wire [31:0] adder_1_out, adder_2_out, adder_3_out, bit_extender_1_out, bit_extender_2_out, ex_mem_1_mem_ir,
       ex_mem_1_mem_r2, ex_mem_1_mem_result, EX_PC, id_ex_1_ex_immed, id_ex_1_ex_ir, id_ex_1_ex_r1,
       id_ex_1_ex_r2, ID_PC, ID_R1, ID_R2, IF_PC, LedData, MEM_PC, mem_wb_1_wb_din, mips_alu_1_result,
       multiplexer_1_out, multiplexer_6_out, multiplexer_7_out, multiplexer_9_out, multiplexer_11_out,
       ram_1_data, rom_1_data, WB_Din, WB_PC;

  Button \u_总复位  (.out(RST));
  Button _1 (.out(IR1));
  Button _2 (.out(IR2));
  Button _3 (.out(IR3));
  Button \u_继续运行  (.out(Go));
  LED led_1 (.in(W1));
  LED led_2 (.in(W2));
  LED led_3 (.in(W3));
  Hex_Digit_Display hex_digit_display_1 (.value(LedData[31:28]));  // open: dp
  Hex_Digit_Display hex_digit_display_2 (.value(LedData[27:24]));  // open: dp
  Hex_Digit_Display hex_digit_display_3 (.value(LedData[23:20]));  // open: dp
  Multiplexer #(.select(2), .width(32), .enable("false")) multiplexer_1 (
    .in0(adder_1_out), .out(multiplexer_1_out), .sel({Cond, EX_Jmp}));  // open: in1, in2, in3
  Hex_Digit_Display hex_digit_display_4 (.value(LedData[15:12]));  // open: dp
  Hex_Digit_Display hex_digit_display_5 (.value(LedData[19:16]));  // open: dp
  Hex_Digit_Display hex_digit_display_6 (.value(LedData[11:8]));  // open: dp
  Hex_Digit_Display hex_digit_display_7 (.value(LedData[7:4]));  // open: dp
  Clock clock_1 (.out(CLK));
  Hex_Digit_Display hex_digit_display_8 (.value(LedData[3:0]));  // open: dp
  Register #(.width(32)) PC (.D(multiplexer_1_out), .en(Run), .Q(IF_PC), .clk(CLK), .clr(RST));
  or or_1 (Cond, and_1_out, and_2_out, and_3_out);
  Adder #(.width(32)) adder_1 (.a(IF_PC), .b(32'h4), .out(adder_1_out));  // open: cin, cout
  // Probe on \总周期数 
  // Probe on \无条件分支数 
  // Probe on \条件分支成功数 
  // Probe on \插入气泡数 
  // Probe on \LoadUse次数 
  // Probe on IF_PC[11:0]
  ROM #(.addrWidth(10), .dataWidth(32)) rom_1 (.addr(IF_PC[11:2]), .data(rom_1_data));  // open: sel
  not not_1 (not_1_out, Run);
  // Probe on ID_PC[11:0]
  and and_1 (and_1_out, mips_alu_1_result[0], EX_BLTZ);
  and and_2 (and_2_out, ~mips_alu_1_equal, EX_Bne);  // AND_Gate
  and and_3 (and_3_out, mips_alu_1_equal, EX_Beq);
  IF_ID if_id_1 (
    .IF_PC(IF_PC), .IF_IR(rom_1_data), .\传输状态In_表明当前传输数据有效 (1'b1), .CLK(CLK), .ID_PC(ID_PC),
    .ID_IR({if_id_1_id_ir, if_id_1_id_ir_6, if_id_1_id_ir_5, if_id_1_id_ir_4, if_id_1_id_ir_3, if_id_1_id_ir_2}),
    .\传输状态Out_表明当前传输数据有效 (\if_id_1_传输状态out_表明当前传输数据有效 ), .\同步清零_气泡_高电平有效 (1'b0),
    .\使能端_低电平有效_stall_高电平有效 (not_1_out));
  // Probe on EX_PC[11:0]
  // Probe on MEM_PC[11:0]
  // Probe on WB_PC[11:0]
  or or_2 (ID_Shift, \硬布线控制器_1_sllv , \硬布线控制器_1_srlv );
  Adder #(.width(32)) adder_2 (.a(ID_PC), .b(32'h4), .out(adder_2_out));  // open: cin, cout
  Multiplexer #(.width(5), .enable("false")) multiplexer_2 (
    .in1(if_id_1_id_ir_4), .out(multiplexer_2_out), .sel(ID_RegDst));  // open: in0
  or or_3 (Run, Go, ~WE_stop);  // OR_Gate
  \硬布线控制器  \u_硬布线控制器_1  (
    .Func(if_id_1_id_ir_2), .OP(if_id_1_id_ir), .ALU_OP(\硬布线控制器_1_alu_op ), .MemToReg(\硬布线控制器_1_memtoreg ),
    .MemWrite(\硬布线控制器_1_memwrite ), .ALU_SRC(\硬布线控制器_1_alu_src ), .RegWrite(\硬布线控制器_1_regwrite ),
    .SysCALL(ID_Syscall), .SignedExt(ID_SignedExt), .RegDst(ID_RegDst), .JR(ID_JR), .JMP(ID_Jmp),
    .Beq(\硬布线控制器_1_beq ), .JAL(ID_JAL), .Bne(\硬布线控制器_1_bne ), .SLLV(\硬布线控制器_1_sllv ), .SRLV(\硬布线控制器_1_srlv ),
    .LBU(ID_LBU), .BLTZ(ID_BLTZ), .REGIMM(if_id_1_id_ir_5));
  Multiplexer #(.width(5), .enable("false")) multiplexer_3 (
    .in0(if_id_1_id_ir_6), .in1(5'b00010), .out(multiplexer_3_out), .sel(ID_Syscall));
  Multiplexer #(.width(5), .enable("false")) multiplexer_4 (
    .in0(if_id_1_id_ir_5), .in1(5'b00100), .out(multiplexer_4_out), .sel(ID_Syscall));
  Multiplexer #(.width(5), .enable("false")) multiplexer_5 (
    .in0(multiplexer_2_out), .in1({5{1'b1}}), .out(ID_W_num), .sel(ID_JAL));
  assign bit_extender_1_out = {{16{1'b0}}, {if_id_1_id_ir_4, if_id_1_id_ir_3, if_id_1_id_ir_2}};  // Bit_Extender bit_extender_1
  assign bit_extender_2_out = {{16{if_id_1_id_ir_4[4]}}, {if_id_1_id_ir_4, if_id_1_id_ir_3, if_id_1_id_ir_2}};  // Bit_Extender bit_extender_2
  Multiplexer #(.width(32), .enable("false")) multiplexer_6 (
    .in0(bit_extender_1_out), .in1(bit_extender_2_out), .out(multiplexer_6_out), .sel(ID_SignedExt));
  Counter #(.width(16), .max('hffff)) counter_1 (
    .count(Run), .Q(\总周期数 ), .clk(CLK), .clr(RST));  // open: load, D, carry
  MIPS_Regifile mips_regifile_1 (
    .Din(WB_Din), .Clk(CLK), .R1(ID_R1), .R2(ID_R2), .WE(WB_RegWrite), .W_num(WB_W_num),
    .R1_num(multiplexer_3_out), .R2_num(multiplexer_4_out));
  not not_2 (not_2_out, Run);
  Counter #(.width(16), .max('hffff)) counter_2 (
    .count(Cond), .Q(\条件分支成功数 ), .clk(CLK), .clr(RST));  // open: load, D, carry
  ID_EX id_ex_1 (
    .ID_PC(ID_PC),
    .ID_IR({if_id_1_id_ir, if_id_1_id_ir_6, if_id_1_id_ir_5, if_id_1_id_ir_4, if_id_1_id_ir_3, if_id_1_id_ir_2}),
    .ID_R1(ID_R1), .ID_R2(ID_R2), .ID_immed(multiplexer_6_out), .ID_shamt(if_id_1_id_ir_3),
    .\传输状态In_表明当前传输数据有效 (\if_id_1_传输状态out_表明当前传输数据有效 ), .CLK(CLK), .EX_PC(EX_PC), .EX_IR(id_ex_1_ex_ir),
    .EX_R1(id_ex_1_ex_r1), .EX_R2(id_ex_1_ex_r2), .EX_immed(id_ex_1_ex_immed), .EX_shamt(id_ex_1_ex_shamt),
    .\传输状态Out_表明当前传输数据有效 (\id_ex_1_传输状态out_表明当前传输数据有效 ), .\同步清零_气泡_高电平有效 (1'b0),
    .\使能端_低电平有效_stall_高电平有效 (not_2_out), .ID_BLTZ(ID_BLTZ), .EX_BLTZ(EX_BLTZ), .ID_LBU(ID_LBU),
    .EX_LBU(id_ex_1_ex_lbu), .ID_Shift(ID_Shift), .EX_Shift(EX_Shift), .ID_JR(ID_JR), .EX_JR(EX_JR),
    .ID_Jmp(ID_Jmp), .EX_Jmp(EX_Jmp), .ID_JAL(ID_JAL), .EX_JAL(id_ex_1_ex_jal),
    .ID_RegWrite(\硬布线控制器_1_regwrite ), .EX_RegWrite(id_ex_1_ex_regwrite), .ID_ALUSrcB(\硬布线控制器_1_alu_src ),
    .EX_ALUSrcB(id_ex_1_ex_alusrcb), .ID_AluOP(\硬布线控制器_1_alu_op ), .EX_AluOP(id_ex_1_ex_aluop),
    .ID_MemWrite(\硬布线控制器_1_memwrite ), .EX_MemWrite(id_ex_1_ex_memwrite), .ID_MemToReg(\硬布线控制器_1_memtoreg ),
    .EX_MemToReg(id_ex_1_ex_memtoreg), .ID_Bne(\硬布线控制器_1_bne ), .EX_Bne(EX_Bne), .ID_Beq(\硬布线控制器_1_beq ),
    .EX_Beq(EX_Beq),
    .ID_Jaddr({adder_2_out[31:28], if_id_1_id_ir_6, if_id_1_id_ir_5, if_id_1_id_ir_4, if_id_1_id_ir_3, if_id_1_id_ir_2, 2'b00}),
    .ID_W_num(ID_W_num), .EX_W_num(id_ex_1_ex_w_num), .ID_Syscall(ID_stop), .EX_Syscall(id_ex_1_ex_syscall));  // open: EX_Jaddr, ID_R1_num, EX_R1_num, ID_R2_num, EX_R2_num
  Multiplexer #(.width(32), .enable("false")) multiplexer_7 (
    .in0(id_ex_1_ex_r2), .in1(id_ex_1_ex_immed), .out(multiplexer_7_out), .sel(id_ex_1_ex_alusrcb));
  Multiplexer #(.width(5), .enable("false")) multiplexer_8 (
    .in0(id_ex_1_ex_shamt), .in1(R1), .out(multiplexer_8_out), .sel(EX_Shift));
  Counter #(.width(16), .max('hffff)) counter_3 (
    .count(EX_Jmp), .Q(\无条件分支数 ), .clk(CLK), .clr(RST));  // open: load, D, carry
  MIPS_ALU mips_alu_1 (
    .X(id_ex_1_ex_r1), .Y(multiplexer_7_out), .AluOP(id_ex_1_ex_aluop), .Equal(mips_alu_1_equal),
    .Result(mips_alu_1_result), .shamt(multiplexer_8_out));  // open: Result_2
  not not_3 (not_3_out, Run);
  EX_MEM ex_mem_1 (
    .EX_MemToReg(id_ex_1_ex_memtoreg), .EX_MemWrite(id_ex_1_ex_memwrite), .EX_RegWrite(id_ex_1_ex_regwrite),
    .EX_JAL(id_ex_1_ex_jal), .EX_LBU(id_ex_1_ex_lbu), .EX_PC(EX_PC), .EX_IR(id_ex_1_ex_ir),
    .EX_Result(mips_alu_1_result), .EX_R2(id_ex_1_ex_r2), .\传输状态In_表明当前传输数据有效 (\id_ex_1_传输状态out_表明当前传输数据有效 ),
    .CLK(CLK), .MEM_MemToReg(ex_mem_1_mem_memtoreg), .MEM_MemWrite(MEM_MemWrite),
    .MEM_RegWrite(ex_mem_1_mem_regwrite), .MEM_JAL(ex_mem_1_mem_jal), .MEM_LBU(MEM_LBU), .MEM_PC(MEM_PC),
    .MEM_IR(ex_mem_1_mem_ir), .MEM_Result(ex_mem_1_mem_result), .MEM_R2(ex_mem_1_mem_r2),
    .\传输状态Out_表明当前传输数据有效 (\ex_mem_1_传输状态out_表明当前传输数据有效 ), .\同步清零_气泡_高电平有效 (1'b0),
    .\使能端_低电平有效_stall_高电平有效 (not_3_out), .EX_W_num(id_ex_1_ex_w_num), .MEM_W_num(ex_mem_1_mem_w_num),
    .EX_stop(id_ex_1_ex_syscall), .MEM_stop(ex_mem_1_mem_stop));  // open: EX_display, MEM_display
  Comparator #(.width(32), .mode("unsigned")) comparator_1 (
    .a(ID_R1), .b(32'h22), .eq(comparator_1_eq));  // open: gt, lt
  and and_4 (ID_stop, ~comparator_1_eq, ID_Syscall);  // AND_Gate
  RAM #(.addrWidth(10), .dataWidth(32), .bus("separate")) ram_1 (
    .addr(ex_mem_1_mem_result[11:2]), .din(ex_mem_1_mem_r2), .data(ram_1_data), .str(MEM_MemWrite),
    .sel(1'b1), .clk(CLK), .ld(1'b1), .clr(RST));
  Multiplexer #(.width(32), .enable("false")) multiplexer_9 (
    .in0(ex_mem_1_mem_result), .in1(ram_1_data), .out(multiplexer_9_out), .sel(ex_mem_1_mem_memtoreg));
  Comparator #(.width(32), .mode("unsigned")) comparator_2 (
    .a(ID_R1), .b(32'h22), .eq(comparator_2_eq));  // open: gt, lt
  Multiplexer #(.select(2), .width(8), .enable("false")) multiplexer_10 (
    .in0(multiplexer_9_out[7:0]), .in1(multiplexer_9_out[15:8]), .in2(multiplexer_9_out[23:16]),
    .in3(multiplexer_9_out[31:24]), .out(multiplexer_10_out), .sel(ex_mem_1_mem_result[1:0]));
  and and_5 (and_5_out, ~comparator_2_eq, ID_Syscall);  // AND_Gate
  Multiplexer #(.width(32), .enable("false")) multiplexer_11 (
    .in0(multiplexer_9_out), .in1({{24{1'b0}}, multiplexer_10_out}), .out(multiplexer_11_out), .sel(MEM_LBU));
  not not_4 (not_4_out, Run);
  MEM_WB mem_wb_1 (
    .MEM_W_num(ex_mem_1_mem_w_num), .MEM_RegWrite(ex_mem_1_mem_regwrite), .MEM_PC(MEM_PC),
    .MEM_IR(ex_mem_1_mem_ir), .MEM_Din(multiplexer_11_out),
    .\传输状态In_表明当前传输数据有效 (\ex_mem_1_传输状态out_表明当前传输数据有效 ), .CLK(CLK), .WB_W_num(WB_W_num),
    .WB_RegWrite(WB_RegWrite), .WE_PC(WB_PC), .WB_Din(mem_wb_1_wb_din), .\同步清零_气泡_高电平有效 (1'b0),
    .\使能端_低电平有效_stall_高电平有效 (not_4_out), .MEM_JAL(ex_mem_1_mem_jal), .WB_JAL(mem_wb_1_wb_jal),
    .MEM_stop(ex_mem_1_mem_stop), .WB_stop(WE_stop));  // open: WE_IR, 传输状态Out_表明当前传输数据有效, MEM_display, WB_display, MEM_R2, WE_R2
  Register #(.width(32)) register_1 (.D(ID_R2), .en(and_5_out), .Q(LedData), .clk(CLK), .clr(RST));
  Adder #(.width(32)) adder_3 (.a(WB_PC), .b(32'h4), .out(adder_3_out));  // open: cin, cout
  Multiplexer #(.width(32), .enable("false")) multiplexer_12 (
    .in0(mem_wb_1_wb_din), .in1(adder_3_out), .out(WB_Din), .sel(mem_wb_1_wb_jal));

  // Other names for the same wires on the sheet: Uncond = EX_Jmp

  // Notes on the sheet:
  //   中断源
  //   中断等待指示
  //   数码管输出
  //   指令存储器
  //   contents of rom_1 (hex, n*v repeats v):
  //   20100000 20110000 20120000 20130000 36100000 36310001 36520002 36730003 ae100000 ae110004 ae120008
  //   ae13000c 2002000a 20110000 20120000 20130000 c
  //   流水调试日志用
  //   指令字
  //   rd
endmodule

// 源寄存器使用情况
module \源寄存器使用情况  (
  input  OP0,
  input  OP1,
  input  OP2,
  input  OP3,
  input  OP4,
  input  OP5,
  input  F0,
  input  F1,
  input  F2,
  input  F3,
  input  F4,
  input  F5,
  output R1_Used,
  output R2_Used
);

  wire and_1_out, and_2_out, and_3_out, and_4_out, and_5_out, and_6_out, and_7_out, and_8_out, and_9_out,
       and_10_out, and_11_out, and_12_out, and_13_out, and_14_out, and_15_out, and_16_out, and_17_out,
       and_18_out, and_19_out, and_20_out, and_21_out, and_22_out, and_23_out, and_24_out, and_25_out,
       and_26_out, and_27_out, and_28_out, and_29_out, and_30_out, and_31_out, and_32_out, and_33_out,
       and_34_out, and_35_out, and_36_out, and_37_out, and_38_out, and_39_out, and_40_out, and_41_out,
       and_42_out, and_43_out, not_1_out, not_2_out, not_3_out, not_4_out, not_5_out, not_6_out, not_7_out,
       not_8_out, not_9_out, not_10_out, not_11_out, not_12_out, not_13_out, not_14_out, not_15_out,
       not_16_out, not_17_out, not_18_out, not_19_out, not_20_out, not_21_out, not_22_out, not_23_out,
       not_24_out, not_25_out, not_26_out, not_27_out, not_28_out, not_29_out, not_30_out, not_31_out,
       not_32_out, not_33_out, not_34_out, not_35_out, not_36_out, not_37_out, not_38_out, not_39_out,
       not_40_out, not_41_out, not_42_out, not_43_out, not_44_out, not_45_out, not_46_out, not_47_out,
       not_48_out, not_49_out, not_50_out, not_51_out, not_52_out, not_53_out, not_54_out, not_55_out,
       not_56_out, not_57_out, not_58_out, not_59_out, not_60_out, not_61_out, not_62_out, not_63_out,
       not_64_out, not_65_out, not_66_out, not_67_out, not_68_out, not_69_out, not_70_out, not_71_out,
       not_72_out, not_73_out, not_74_out, not_75_out, not_76_out, not_77_out, not_78_out, not_79_out,
       not_80_out, not_81_out, not_82_out, not_83_out, not_84_out, not_85_out, not_86_out, not_87_out,
       not_88_out, not_89_out, not_90_out, not_91_out, not_92_out, not_93_out, not_94_out, not_95_out,
       not_96_out, not_97_out, not_98_out, not_99_out, not_100_out, not_101_out, not_102_out, not_103_out,
       not_104_out, not_105_out, not_106_out, not_107_out, not_108_out, not_109_out, not_110_out,
       not_111_out, not_112_out, not_113_out, not_114_out, not_115_out, not_116_out, not_117_out,
       not_118_out, not_119_out, not_120_out, not_121_out, not_122_out, not_123_out, not_124_out,
       not_125_out, not_126_out, not_127_out, not_128_out, not_129_out, not_130_out, not_131_out,
       not_132_out, not_133_out, not_134_out, not_135_out, not_136_out, not_137_out, not_138_out,
       not_139_out, not_140_out, not_141_out, not_142_out, not_143_out, not_144_out, not_145_out,
       not_146_out, not_147_out, not_148_out, not_149_out, not_150_out, not_151_out, not_152_out,
       not_153_out, not_154_out, not_155_out, not_156_out, not_157_out, not_158_out, not_159_out,
       not_160_out, not_161_out, not_162_out, not_163_out, not_164_out, not_165_out, not_166_out,
       not_167_out, not_168_out, not_169_out, not_170_out, not_171_out, not_172_out, not_173_out,
       not_174_out, not_175_out, not_176_out, not_177_out, not_178_out, not_179_out, not_180_out,
       not_181_out, not_182_out, not_183_out, not_184_out, not_185_out, not_186_out, not_187_out,
       not_188_out, not_189_out, not_190_out, not_191_out, not_192_out, not_193_out, not_194_out,
       not_195_out, not_196_out, not_197_out, not_198_out, not_199_out, not_200_out, not_201_out,
       not_202_out, not_203_out, not_204_out, not_205_out, not_206_out, not_207_out, not_208_out,
       not_209_out, not_210_out, not_211_out, not_212_out, not_213_out, not_214_out, not_215_out,
       not_216_out, not_217_out, not_218_out, not_219_out, not_220_out, not_221_out, not_222_out,
       not_223_out, not_224_out, not_225_out, not_226_out, not_227_out, not_228_out, not_229_out,
       not_230_out, not_231_out, not_232_out, not_233_out, not_234_out, not_235_out, not_236_out,
       not_237_out, not_238_out, not_239_out, not_240_out, not_241_out, not_242_out, not_243_out,
       not_244_out, not_245_out, not_246_out, not_247_out, not_248_out, not_249_out, not_250_out,
       not_251_out, not_252_out, not_253_out, not_254_out, not_255_out, not_256_out, not_257_out,
       not_258_out, not_259_out, not_260_out, not_261_out, not_262_out, not_263_out, not_264_out,
       not_265_out, not_266_out, not_267_out, not_268_out, not_269_out, not_270_out, not_271_out,
       not_272_out, not_273_out, not_274_out, not_275_out, not_276_out, not_277_out, not_278_out,
       not_279_out, not_280_out, not_281_out, not_282_out, not_283_out, not_284_out, not_285_out,
       not_286_out, not_287_out, not_288_out, not_289_out, not_290_out, not_291_out, not_292_out,
       not_293_out, not_294_out, not_295_out, not_296_out, not_297_out, not_298_out, not_299_out,
       not_300_out, not_301_out, not_302_out, not_303_out, not_304_out, not_305_out, not_306_out,
       not_307_out, not_308_out, not_309_out, not_310_out, not_311_out, not_312_out, not_313_out,
       not_314_out, not_315_out, not_316_out, not_317_out, not_318_out, not_319_out, not_320_out,
       not_321_out, not_322_out, not_323_out, not_324_out, not_325_out, not_326_out, not_327_out,
       not_328_out, not_329_out, not_330_out, not_331_out, not_332_out, not_333_out, not_334_out,
       not_335_out, not_336_out, not_337_out, not_338_out, not_339_out, not_340_out, not_341_out,
       not_342_out, not_343_out;

  not not_1 (not_1_out, OP5);
  not not_2 (not_2_out, OP4);
  not not_3 (not_3_out, OP3);
  not not_4 (not_4_out, OP2);
  not not_5 (not_5_out, OP1);
  not not_6 (not_6_out, OP0);
  not not_7 (not_7_out, F5);
  not not_8 (not_8_out, F4);
  not not_9 (not_9_out, F3);
  not not_10 (not_10_out, F2);
  not not_11 (not_11_out, F1);
  not not_12 (not_12_out, F0);
  not not_13 (not_13_out, OP5);
  not not_14 (not_14_out, OP4);
  not not_15 (not_15_out, OP3);
  not not_16 (not_16_out, OP2);
  not not_17 (not_17_out, OP1);
  not not_18 (not_18_out, OP0);
  not not_19 (not_19_out, F5);
  not not_20 (not_20_out, F4);
  not not_21 (not_21_out, F3);
  not not_22 (not_22_out, F2);
  not not_23 (not_23_out, OP5);
  not not_24 (not_24_out, OP4);
  not not_25 (not_25_out, OP3);
  not not_26 (not_26_out, OP2);
  not not_27 (not_27_out, OP1);
  not not_28 (not_28_out, OP0);
  not not_29 (not_29_out, F5);
  not not_30 (not_30_out, F4);
  not not_31 (not_31_out, F3);
  not not_32 (not_32_out, F2);
  not not_33 (not_33_out, F0);
  not not_34 (not_34_out, OP5);
  not not_35 (not_35_out, OP4);
  not not_36 (not_36_out, OP3);
  not not_37 (not_37_out, OP2);
  not not_38 (not_38_out, OP1);
  not not_39 (not_39_out, OP0);
  not not_40 (not_40_out, F4);
  not not_41 (not_41_out, F3);
  not not_42 (not_42_out, F2);
  not not_43 (not_43_out, F1);
  not not_44 (not_44_out, F0);
  not not_45 (not_45_out, OP5);
  not not_46 (not_46_out, OP4);
  not not_47 (not_47_out, OP3);
  not not_48 (not_48_out, OP2);
  not not_49 (not_49_out, OP1);
  not not_50 (not_50_out, OP0);
  not not_51 (not_51_out, F4);
  not not_52 (not_52_out, F3);
  not not_53 (not_53_out, F2);
  not not_54 (not_54_out, F1);
  not not_55 (not_55_out, OP5);
  not not_56 (not_56_out, OP4);
  not not_57 (not_57_out, OP3);
  not not_58 (not_58_out, OP2);
  not not_59 (not_59_out, OP1);
  not not_60 (not_60_out, OP0);
  not not_61 (not_61_out, F4);
  not not_62 (not_62_out, F3);
  not not_63 (not_63_out, F2);
  not not_64 (not_64_out, F0);
  not not_65 (not_65_out, OP5);
  not not_66 (not_66_out, OP4);
  not not_67 (not_67_out, OP3);
  not not_68 (not_68_out, OP2);
  not not_69 (not_69_out, OP1);
  not not_70 (not_70_out, OP0);
  not not_71 (not_71_out, F4);
  not not_72 (not_72_out, F3);
  not not_73 (not_73_out, F1);
  not not_74 (not_74_out, F0);
  not not_75 (not_75_out, OP5);
  not not_76 (not_76_out, OP4);
  not not_77 (not_77_out, OP3);
  not not_78 (not_78_out, OP2);
  not not_79 (not_79_out, OP1);
  not not_80 (not_80_out, OP0);
  not not_81 (not_81_out, F4);
  not not_82 (not_82_out, F3);
  not not_83 (not_83_out, F1);
  not not_84 (not_84_out, OP5);
  not not_85 (not_85_out, OP4);
  not not_86 (not_86_out, OP3);
  not not_87 (not_87_out, OP2);
  not not_88 (not_88_out, OP1);
  not not_89 (not_89_out, OP0);
  not not_90 (not_90_out, F4);
  not not_91 (not_91_out, F3);
  not not_92 (not_92_out, OP5);
  not not_93 (not_93_out, OP4);
  not not_94 (not_94_out, OP3);
  not not_95 (not_95_out, OP2);
  not not_96 (not_96_out, OP1);
  not not_97 (not_97_out, OP0);
  not not_98 (not_98_out, F4);
  not not_99 (not_99_out, F2);
  not not_100 (not_100_out, F0);
  not not_101 (not_101_out, OP5);
  not not_102 (not_102_out, OP4);
  not not_103 (not_103_out, OP3);
  not not_104 (not_104_out, OP2);
  not not_105 (not_105_out, OP1);
  not not_106 (not_106_out, OP0);
  not not_107 (not_107_out, F4);
  not not_108 (not_108_out, F2);
  not not_109 (not_109_out, OP5);
  not not_110 (not_110_out, OP4);
  not not_111 (not_111_out, OP3);
  not not_112 (not_112_out, OP2);
  not not_113 (not_113_out, OP1);
  not not_114 (not_114_out, OP0);
  not not_115 (not_115_out, F5);
  not not_116 (not_116_out, F4);
  not not_117 (not_117_out, F2);
  not not_118 (not_118_out, F1);
  not not_119 (not_119_out, F0);
  not not_120 (not_120_out, OP5);
  not not_121 (not_121_out, OP4);
  not not_122 (not_122_out, OP3);
  not not_123 (not_123_out, OP2);
  not not_124 (not_124_out, OP1);
  not not_125 (not_125_out, OP0);
  not not_126 (not_126_out, F5);
  not not_127 (not_127_out, F4);
  not not_128 (not_128_out, F1);
  not not_129 (not_129_out, F0);
  not not_130 (not_130_out, OP5);
  not not_131 (not_131_out, OP4);
  not not_132 (not_132_out, OP3);
  not not_133 (not_133_out, OP1);
  not not_134 (not_134_out, OP0);
  not not_135 (not_135_out, OP5);
  not not_136 (not_136_out, OP4);
  not not_137 (not_137_out, OP3);
  not not_138 (not_138_out, OP1);
  not not_139 (not_139_out, OP5);
  not not_140 (not_140_out, OP4);
  not not_141 (not_141_out, OP2);
  not not_142 (not_142_out, OP1);
  not not_143 (not_143_out, OP0);
  not not_144 (not_144_out, OP5);
  not not_145 (not_145_out, OP4);
  not not_146 (not_146_out, OP1);
  not not_147 (not_147_out, OP0);
  not not_148 (not_148_out, OP5);
  not not_149 (not_149_out, OP4);
  not not_150 (not_150_out, OP2);
  not not_151 (not_151_out, OP1);
  not not_152 (not_152_out, OP5);
  not not_153 (not_153_out, OP4);
  not not_154 (not_154_out, OP2);
  not not_155 (not_155_out, OP0);
  not not_156 (not_156_out, OP5);
  not not_157 (not_157_out, OP4);
  not not_158 (not_158_out, OP1);
  not not_159 (not_159_out, OP4);
  not not_160 (not_160_out, OP3);
  not not_161 (not_161_out, OP2);
  not not_162 (not_162_out, OP4);
  not not_163 (not_163_out, OP2);
  not not_164 (not_164_out, OP5);
  not not_165 (not_165_out, OP4);
  not not_166 (not_166_out, OP3);
  not not_167 (not_167_out, OP2);
  not not_168 (not_168_out, OP1);
  not not_169 (not_169_out, OP0);
  not not_170 (not_170_out, F5);
  not not_171 (not_171_out, F4);
  not not_172 (not_172_out, F3);
  not not_173 (not_173_out, F1);
  not not_174 (not_174_out, F0);
  not not_175 (not_175_out, OP5);
  not not_176 (not_176_out, OP4);
  not not_177 (not_177_out, OP3);
  not not_178 (not_178_out, OP2);
  not not_179 (not_179_out, OP1);
  not not_180 (not_180_out, OP0);
  not not_181 (not_181_out, F5);
  not not_182 (not_182_out, F4);
  not not_183 (not_183_out, F3);
  not not_184 (not_184_out, F0);
  not not_185 (not_185_out, OP4);
  not not_186 (not_186_out, OP3);
  not not_187 (not_187_out, OP1);
  not not_188 (not_188_out, OP0);
  not not_189 (not_189_out, OP5);
  not not_190 (not_190_out, OP4);
  not not_191 (not_191_out, OP3);
  not not_192 (not_192_out, OP2);
  not not_193 (not_193_out, OP1);
  not not_194 (not_194_out, OP5);
  not not_195 (not_195_out, OP4);
  not not_196 (not_196_out, OP3);
  not not_197 (not_197_out, OP2);
  not not_198 (not_198_out, OP1);
  not not_199 (not_199_out, OP0);
  not not_200 (not_200_out, F5);
  not not_201 (not_201_out, F4);
  not not_202 (not_202_out, F3);
  not not_203 (not_203_out, F2);
  not not_204 (not_204_out, F1);
  not not_205 (not_205_out, F0);
  not not_206 (not_206_out, OP5);
  not not_207 (not_207_out, OP4);
  not not_208 (not_208_out, OP3);
  not not_209 (not_209_out, OP2);
  not not_210 (not_210_out, OP1);
  not not_211 (not_211_out, OP0);
  not not_212 (not_212_out, F5);
  not not_213 (not_213_out, F4);
  not not_214 (not_214_out, F3);
  not not_215 (not_215_out, F2);
  not not_216 (not_216_out, OP5);
  not not_217 (not_217_out, OP4);
  not not_218 (not_218_out, OP3);
  not not_219 (not_219_out, OP2);
  not not_220 (not_220_out, OP1);
  not not_221 (not_221_out, OP0);
  not not_222 (not_222_out, F5);
  not not_223 (not_223_out, F4);
  not not_224 (not_224_out, F3);
  not not_225 (not_225_out, F2);
  not not_226 (not_226_out, F0);
  not not_227 (not_227_out, OP5);
  not not_228 (not_228_out, OP4);
  not not_229 (not_229_out, OP3);
  not not_230 (not_230_out, OP2);
  not not_231 (not_231_out, OP1);
  not not_232 (not_232_out, OP0);
  not not_233 (not_233_out, F4);
  not not_234 (not_234_out, F3);
  not not_235 (not_235_out, F2);
  not not_236 (not_236_out, F1);
  not not_237 (not_237_out, F0);
  not not_238 (not_238_out, OP5);
  not not_239 (not_239_out, OP4);
  not not_240 (not_240_out, OP3);
  not not_241 (not_241_out, OP2);
  not not_242 (not_242_out, OP1);
  not not_243 (not_243_out, OP0);
  not not_244 (not_244_out, F4);
  not not_245 (not_245_out, F3);
  not not_246 (not_246_out, F2);
  not not_247 (not_247_out, F1);
  not not_248 (not_248_out, OP5);
  not not_249 (not_249_out, OP4);
  not not_250 (not_250_out, OP3);
  not not_251 (not_251_out, OP2);
  not not_252 (not_252_out, OP1);
  not not_253 (not_253_out, OP0);
  not not_254 (not_254_out, F4);
  not not_255 (not_255_out, F3);
  not not_256 (not_256_out, F2);
  not not_257 (not_257_out, F0);
  not not_258 (not_258_out, OP5);
  not not_259 (not_259_out, OP4);
  not not_260 (not_260_out, OP3);
  not not_261 (not_261_out, OP2);
  not not_262 (not_262_out, OP1);
  not not_263 (not_263_out, OP0);
  not not_264 (not_264_out, F4);
  not not_265 (not_265_out, F3);
  not not_266 (not_266_out, F1);
  not not_267 (not_267_out, F0);
  not not_268 (not_268_out, OP5);
  not not_269 (not_269_out, OP4);
  not not_270 (not_270_out, OP3);
  not not_271 (not_271_out, OP2);
  not not_272 (not_272_out, OP1);
  not not_273 (not_273_out, OP0);
  not not_274 (not_274_out, F4);
  not not_275 (not_275_out, F3);
  not not_276 (not_276_out, F1);
  not not_277 (not_277_out, OP5);
  not not_278 (not_278_out, OP4);
  not not_279 (not_279_out, OP3);
  not not_280 (not_280_out, OP2);
  not not_281 (not_281_out, OP1);
  not not_282 (not_282_out, OP0);
  not not_283 (not_283_out, F4);
  not not_284 (not_284_out, F3);
  not not_285 (not_285_out, OP5);
  not not_286 (not_286_out, OP4);
  not not_287 (not_287_out, OP3);
  not not_288 (not_288_out, OP2);
  not not_289 (not_289_out, OP1);
  not not_290 (not_290_out, OP0);
  not not_291 (not_291_out, F4);
  not not_292 (not_292_out, F2);
  not not_293 (not_293_out, F0);
  not not_294 (not_294_out, OP5);
  not not_295 (not_295_out, OP4);
  not not_296 (not_296_out, OP3);
  not not_297 (not_297_out, OP2);
  not not_298 (not_298_out, OP1);
  not not_299 (not_299_out, OP0);
  not not_300 (not_300_out, F4);
  not not_301 (not_301_out, F2);
  not not_302 (not_302_out, OP5);
  not not_303 (not_303_out, OP4);
  not not_304 (not_304_out, OP3);
  not not_305 (not_305_out, OP2);
  not not_306 (not_306_out, OP1);
  not not_307 (not_307_out, OP0);
  not not_308 (not_308_out, F5);
  not not_309 (not_309_out, F4);
  not not_310 (not_310_out, F1);
  not not_311 (not_311_out, F0);
  not not_312 (not_312_out, OP5);
  not not_313 (not_313_out, OP4);
  not not_314 (not_314_out, OP3);
  not not_315 (not_315_out, OP1);
  not not_316 (not_316_out, OP0);
  not not_317 (not_317_out, OP5);
  not not_318 (not_318_out, OP4);
  not not_319 (not_319_out, OP3);
  not not_320 (not_320_out, OP1);
  not not_321 (not_321_out, OP4);
  not not_322 (not_322_out, OP2);
  not not_323 (not_323_out, OP5);
  not not_324 (not_324_out, OP4);
  not not_325 (not_325_out, OP3);
  not not_326 (not_326_out, OP2);
  not not_327 (not_327_out, OP1);
  not not_328 (not_328_out, OP0);
  not not_329 (not_329_out, F5);
  not not_330 (not_330_out, F4);
  not not_331 (not_331_out, F3);
  not not_332 (not_332_out, F1);
  not not_333 (not_333_out, F0);
  not not_334 (not_334_out, OP5);
  not not_335 (not_335_out, OP4);
  not not_336 (not_336_out, OP3);
  not not_337 (not_337_out, OP2);
  not not_338 (not_338_out, OP1);
  not not_339 (not_339_out, OP0);
  not not_340 (not_340_out, F5);
  not not_341 (not_341_out, F4);
  not not_342 (not_342_out, F3);
  not not_343 (not_343_out, F0);
  and and_1 (and_1_out, not_1_out, not_2_out, not_3_out, not_4_out, not_5_out, not_6_out, not_7_out, not_8_out, not_9_out, not_10_out, not_11_out, not_12_out);
  and and_2 (and_2_out, not_13_out, not_14_out, not_15_out, not_16_out, not_17_out, not_18_out, not_19_out, not_20_out, not_21_out, not_22_out, F1, F0);
  and and_3 (and_3_out, not_23_out, not_24_out, not_25_out, not_26_out, not_27_out, not_28_out, not_29_out, not_30_out, not_31_out, not_32_out, F1, not_33_out);
  and and_4 (and_4_out, not_34_out, not_35_out, not_36_out, not_37_out, not_38_out, not_39_out, F5, not_40_out, not_41_out, not_42_out, not_43_out, not_44_out);
  and and_5 (and_5_out, not_45_out, not_46_out, not_47_out, not_48_out, not_49_out, not_50_out, F5, not_51_out, not_52_out, not_53_out, not_54_out, F0);
  and and_6 (and_6_out, not_55_out, not_56_out, not_57_out, not_58_out, not_59_out, not_60_out, F5, not_61_out, not_62_out, not_63_out, F1, not_64_out);
  and and_7 (and_7_out, not_65_out, not_66_out, not_67_out, not_68_out, not_69_out, not_70_out, F5, not_71_out, not_72_out, F2, not_73_out, not_74_out);
  and and_8 (and_8_out, not_75_out, not_76_out, not_77_out, not_78_out, not_79_out, not_80_out, F5, not_81_out, not_82_out, F2, not_83_out, F0);
  and and_9 (and_9_out, not_84_out, not_85_out, not_86_out, not_87_out, not_88_out, not_89_out, F5, not_90_out, not_91_out, F2, F1, F0);
  and and_10 (and_10_out, not_92_out, not_93_out, not_94_out, not_95_out, not_96_out, not_97_out, F5, not_98_out, F3, not_99_out, F1, not_100_out);
  and and_11 (and_11_out, not_101_out, not_102_out, not_103_out, not_104_out, not_105_out, not_106_out, F5, not_107_out, F3, not_108_out, F1, F0);
  and and_12 (and_12_out, not_109_out, not_110_out, not_111_out, not_112_out, not_113_out, not_114_out, not_115_out, not_116_out, F3, not_117_out, not_118_out, not_119_out);
  and and_13 (and_13_out, not_120_out, not_121_out, not_122_out, not_123_out, not_124_out, not_125_out, not_126_out, not_127_out, F3, F2, not_128_out, not_129_out);
  and and_14 (and_14_out, not_130_out, not_131_out, not_132_out, OP2, not_133_out, not_134_out);
  and and_15 (and_15_out, not_135_out, not_136_out, not_137_out, OP2, not_138_out, OP0);
  and and_16 (and_16_out, not_139_out, not_140_out, OP3, not_141_out, not_142_out, not_143_out);
  and and_17 (and_17_out, not_144_out, not_145_out, OP3, OP2, not_146_out, not_147_out);
  and and_18 (and_18_out, not_148_out, not_149_out, OP3, not_150_out, not_151_out, OP0);
  and and_19 (and_19_out, not_152_out, not_153_out, OP3, not_154_out, OP1, not_155_out);
  and and_20 (and_20_out, not_156_out, not_157_out, OP3, OP2, not_158_out, OP0);
  and and_21 (and_21_out, OP5, not_159_out, not_160_out, not_161_out, OP1, OP0);
  and and_22 (and_22_out, OP5, not_162_out, OP3, not_163_out, OP1, OP0);
  and and_23 (and_23_out, not_164_out, not_165_out, not_166_out, not_167_out, not_168_out, not_169_out, not_170_out, not_171_out, not_172_out, F2, not_173_out, not_174_out);
  and and_24 (and_24_out, not_175_out, not_176_out, not_177_out, not_178_out, not_179_out, not_180_out, not_181_out, not_182_out, not_183_out, F2, F1, not_184_out);
  and and_25 (and_25_out, OP5, not_185_out, not_186_out, OP2, not_187_out, not_188_out);
  and and_26 (and_26_out, not_189_out, not_190_out, not_191_out, not_192_out, not_193_out, OP0);
  and and_27 (and_27_out, not_194_out, not_195_out, not_196_out, not_197_out, not_198_out, not_199_out, not_200_out, not_201_out, not_202_out, not_203_out, not_204_out, not_205_out);
  and and_28 (and_28_out, not_206_out, not_207_out, not_208_out, not_209_out, not_210_out, not_211_out, not_212_out, not_213_out, not_214_out, not_215_out, F1, F0);
  and and_29 (and_29_out, not_216_out, not_217_out, not_218_out, not_219_out, not_220_out, not_221_out, not_222_out, not_223_out, not_224_out, not_225_out, F1, not_226_out);
  and and_30 (and_30_out, not_227_out, not_228_out, not_229_out, not_230_out, not_231_out, not_232_out, F5, not_233_out, not_234_out, not_235_out, not_236_out, not_237_out);
  and and_31 (and_31_out, not_238_out, not_239_out, not_240_out, not_241_out, not_242_out, not_243_out, F5, not_244_out, not_245_out, not_246_out, not_247_out, F0);
  and and_32 (and_32_out, not_248_out, not_249_out, not_250_out, not_251_out, not_252_out, not_253_out, F5, not_254_out, not_255_out, not_256_out, F1, not_257_out);
  and and_33 (and_33_out, not_258_out, not_259_out, not_260_out, not_261_out, not_262_out, not_263_out, F5, not_264_out, not_265_out, F2, not_266_out, not_267_out);
  and and_34 (and_34_out, not_268_out, not_269_out, not_270_out, not_271_out, not_272_out, not_273_out, F5, not_274_out, not_275_out, F2, not_276_out, F0);
  and and_35 (and_35_out, not_277_out, not_278_out, not_279_out, not_280_out, not_281_out, not_282_out, F5, not_283_out, not_284_out, F2, F1, F0);
  and and_36 (and_36_out, not_285_out, not_286_out, not_287_out, not_288_out, not_289_out, not_290_out, F5, not_291_out, F3, not_292_out, F1, not_293_out);
  and and_37 (and_37_out, not_294_out, not_295_out, not_296_out, not_297_out, not_298_out, not_299_out, F5, not_300_out, F3, not_301_out, F1, F0);
  and and_38 (and_38_out, not_302_out, not_303_out, not_304_out, not_305_out, not_306_out, not_307_out, not_308_out, not_309_out, F3, F2, not_310_out, not_311_out);
  and and_39 (and_39_out, not_312_out, not_313_out, not_314_out, OP2, not_315_out, not_316_out);
  and and_40 (and_40_out, not_317_out, not_318_out, not_319_out, OP2, not_320_out, OP0);
  and and_41 (and_41_out, OP5, not_321_out, OP3, not_322_out, OP1, OP0);
  and and_42 (and_42_out, not_323_out, not_324_out, not_325_out, not_326_out, not_327_out, not_328_out, not_329_out, not_330_out, not_331_out, F2, not_332_out, not_333_out);
  and and_43 (and_43_out, not_334_out, not_335_out, not_336_out, not_337_out, not_338_out, not_339_out, not_340_out, not_341_out, not_342_out, F2, F1, not_343_out);
  or or_1 (R1_Used, and_1_out, and_2_out, and_3_out, and_4_out, and_5_out, and_6_out, and_7_out, and_8_out, and_9_out, and_10_out, and_11_out, and_12_out, and_13_out, and_14_out, and_15_out, and_16_out, and_17_out, and_18_out, and_19_out, and_20_out, and_21_out, and_22_out, and_23_out, and_24_out, and_25_out, and_26_out);
  or or_2 (R2_Used, and_27_out, and_28_out, and_29_out, and_30_out, and_31_out, and_32_out, and_33_out, and_34_out, and_35_out, and_36_out, and_37_out, and_38_out, and_39_out, and_40_out, and_41_out, and_42_out, and_43_out);
endmodule

module \数据相关检测  (
  input  [5:0] OP,
  input  [4:0] EX_WriteReg_num,
  input  EX_RegWrite,
  input  [4:0] MEM_WriteReg_num,
  input  MEM_RegWrite,
  input  [5:0] Func,
  input  [4:0] ID_R1_num,
  input  [4:0] ID_R2_num,
  output \数据相关 
);

  wire and_1_out, and_2_out, and_3_out, and_4_out, and_5_out, and_6_out, comparator_1_eq, comparator_2_eq,
       comparator_3_eq, comparator_4_eq, comparator_5_eq, comparator_6_eq, or_1_out, or_2_out,
       \源寄存器使用情况_1_r1_used , \源寄存器使用情况_1_r2_used ;

  \源寄存器使用情况  \u_源寄存器使用情况_1  (
    .OP0(OP[0]), .OP1(OP[1]), .OP2(OP[2]), .OP3(OP[3]), .OP4(OP[4]), .OP5(OP[5]), .F0(Func[0]), .F1(Func[1]),
    .F2(Func[2]), .F3(Func[3]), .F4(Func[4]), .F5(Func[5]), .R1_Used(\源寄存器使用情况_1_r1_used ),
    .R2_Used(\源寄存器使用情况_1_r2_used ));
  Comparator #(.width(5)) comparator_1 (.a(EX_WriteReg_num), .b(ID_R1_num), .eq(comparator_1_eq));  // open: gt, lt
  Comparator #(.width(5)) comparator_2 (.a(MEM_WriteReg_num), .b(ID_R1_num), .eq(comparator_2_eq));  // open: gt, lt
  Comparator #(.width(5)) comparator_3 (.a({5{1'b0}}), .b(ID_R1_num), .eq(comparator_3_eq));  // open: gt, lt
  Comparator #(.width(5)) comparator_4 (.a({5{1'b0}}), .b(ID_R2_num), .eq(comparator_4_eq));  // open: gt, lt
  Comparator #(.width(5)) comparator_5 (.a(EX_WriteReg_num), .b(ID_R2_num), .eq(comparator_5_eq));  // open: gt, lt
  Comparator #(.width(5)) comparator_6 (.a(MEM_WriteReg_num), .b(ID_R2_num), .eq(comparator_6_eq));  // open: gt, lt
  and and_1 (and_1_out, EX_RegWrite, comparator_1_eq);
  and and_2 (and_2_out, MEM_RegWrite, comparator_2_eq);
  and and_3 (and_3_out, EX_RegWrite, comparator_5_eq);
  and and_4 (and_4_out, MEM_RegWrite, comparator_6_eq);
  or or_1 (or_1_out, and_1_out, and_2_out);
  or or_2 (or_2_out, and_3_out, and_4_out);
  and and_5 (and_5_out, or_1_out, ~comparator_3_eq, \源寄存器使用情况_1_r1_used );  // AND_Gate
  and and_6 (and_6_out, \源寄存器使用情况_1_r2_used , ~comparator_4_eq, or_2_out);  // AND_Gate
  or or_3 (\数据相关 , and_5_out, and_6_out);

  // Other names for the same wires on the sheet: OP_CODE[5:0] = OP
endmodule

module IF_ID (
  input  [31:0] IF_PC,
  input  [31:0] IF_IR,
  input  \传输状态In_表明当前传输数据有效 ,
  input  CLK,
  input  \同步清零_气泡_高电平有效 ,
  input  \使能端_低电平有效_stall_高电平有效 ,
  output [31:0] ID_PC,
  output [31:0] ID_IR,
  output \传输状态Out_表明当前传输数据有效 
);

  wire multiplexer_3_out, not_1_out;
  wire [31:0] multiplexer_1_out, multiplexer_2_out;

  Multiplexer #(.width(32), .enable("false")) multiplexer_1 (
    .in0(IF_PC), .in1({32{1'b0}}), .out(multiplexer_1_out), .sel(\同步清零_气泡_高电平有效 ));
  Multiplexer #(.width(32), .enable("false")) multiplexer_2 (
    .in0(IF_IR), .in1({32{1'b0}}), .out(multiplexer_2_out), .sel(\同步清零_气泡_高电平有效 ));
  Multiplexer #(.enable("false")) multiplexer_3 (
    .in0(\传输状态In_表明当前传输数据有效 ), .in1(1'b0), .out(multiplexer_3_out), .sel(\同步清零_气泡_高电平有效 ));
  Register #(.width(32)) register_1 (.D(multiplexer_1_out), .en(not_1_out), .Q(ID_PC), .clk(CLK));  // open: clr
  Register #(.width(32)) register_2 (.D(multiplexer_2_out), .en(not_1_out), .Q(ID_IR), .clk(CLK));  // open: clr
  Register #(.width(1)) register_3 (
    .D(multiplexer_3_out), .en(not_1_out), .Q(\传输状态Out_表明当前传输数据有效 ), .clk(CLK));  // open: clr
  not not_1 (not_1_out, \使能端_低电平有效_stall_高电平有效 );
endmodule
module ID_EX (
  input  [4:0] ID_R2_num,
  input  [4:0] ID_R1_num,
  input  ID_Syscall,
  input  [4:0] ID_W_num,
  input  [31:0] ID_Jaddr,
  input  ID_Beq,
  input  ID_Bne,
  input  ID_MemToReg,
  input  ID_MemWrite,
  input  [3:0] ID_AluOP,
  input  ID_ALUSrcB,
  input  ID_RegWrite,
  input  ID_JAL,
  input  ID_Jmp,
  input  ID_JR,
  input  ID_Shift,
  input  ID_LBU,
  input  ID_BLTZ,
  input  [31:0] ID_PC,
  input  [31:0] ID_IR,
  input  [31:0] ID_R1,
  input  [31:0] ID_R2,
  input  [31:0] ID_immed,
  input  [4:0] ID_shamt,
  input  \传输状态In_表明当前传输数据有效 ,
  input  CLK,
  input  \同步清零_气泡_高电平有效 ,
  input  \使能端_低电平有效_stall_高电平有效 ,
  output [4:0] EX_R2_num,
  output [4:0] EX_R1_num,
  output EX_Syscall,
  output [4:0] EX_W_num,
  output [31:0] EX_Jaddr,
  output EX_Beq,
  output EX_Bne,
  output EX_MemToReg,
  output EX_MemWrite,
  output [3:0] EX_AluOP,
  output EX_ALUSrcB,
  output EX_RegWrite,
  output EX_JAL,
  output EX_Jmp,
  output EX_JR,
  output EX_Shift,
  output EX_LBU,
  output EX_BLTZ,
  output [31:0] EX_PC,
  output [31:0] EX_IR,
  output [31:0] EX_R1,
  output [31:0] EX_R2,
  output [31:0] EX_immed,
  output [4:0] EX_shamt,
  output \传输状态Out_表明当前传输数据有效 
);

  wire multiplexer_3_out, multiplexer_6_out, multiplexer_7_out, multiplexer_8_out, multiplexer_9_out,
       multiplexer_11_out, multiplexer_12_out, multiplexer_13_out, multiplexer_14_out, multiplexer_15_out,
       multiplexer_16_out, multiplexer_17_out, multiplexer_18_out, multiplexer_25_out, not_1_out;
  wire [3:0] multiplexer_10_out;
  wire [4:0] multiplexer_1_out, multiplexer_2_out, multiplexer_4_out, multiplexer_24_out;
  wire [31:0] multiplexer_5_out, multiplexer_19_out, multiplexer_20_out, multiplexer_21_out,
       multiplexer_22_out, multiplexer_23_out;

  Multiplexer #(.width(5), .enable("false")) multiplexer_1 (
    .in0(ID_R2_num), .in1({5{1'b0}}), .out(multiplexer_1_out), .sel(\同步清零_气泡_高电平有效 ));
  Multiplexer #(.width(5), .enable("false")) multiplexer_2 (
    .in0(ID_R1_num), .in1({5{1'b0}}), .out(multiplexer_2_out), .sel(\同步清零_气泡_高电平有效 ));
  Multiplexer #(.enable("false")) multiplexer_3 (
    .in0(ID_Syscall), .in1(1'b0), .out(multiplexer_3_out), .sel(\同步清零_气泡_高电平有效 ));
  Multiplexer #(.width(5), .enable("false")) multiplexer_4 (
    .in0(ID_W_num), .in1({5{1'b0}}), .out(multiplexer_4_out), .sel(\同步清零_气泡_高电平有效 ));
  Multiplexer #(.width(32), .enable("false")) multiplexer_5 (
    .in0(ID_Jaddr), .in1({32{1'b0}}), .out(multiplexer_5_out), .sel(\同步清零_气泡_高电平有效 ));
  Multiplexer #(.enable("false")) multiplexer_6 (
    .in0(ID_Beq), .in1(1'b0), .out(multiplexer_6_out), .sel(\同步清零_气泡_高电平有效 ));
  Multiplexer #(.enable("false")) multiplexer_7 (
    .in0(ID_Bne), .in1(1'b0), .out(multiplexer_7_out), .sel(\同步清零_气泡_高电平有效 ));
  Multiplexer #(.enable("false")) multiplexer_8 (
    .in0(ID_MemToReg), .in1(1'b0), .out(multiplexer_8_out), .sel(\同步清零_气泡_高电平有效 ));
  Multiplexer #(.enable("false")) multiplexer_9 (
    .in0(ID_MemWrite), .in1(1'b0), .out(multiplexer_9_out), .sel(\同步清零_气泡_高电平有效 ));
  Multiplexer #(.width(4), .enable("false")) multiplexer_10 (
    .in0(ID_AluOP), .in1(4'b0000), .out(multiplexer_10_out), .sel(\同步清零_气泡_高电平有效 ));
  Multiplexer #(.enable("false")) multiplexer_11 (
    .in0(ID_ALUSrcB), .in1(1'b0), .out(multiplexer_11_out), .sel(\同步清零_气泡_高电平有效 ));
  Multiplexer #(.enable("false")) multiplexer_12 (
    .in0(ID_RegWrite), .in1(1'b0), .out(multiplexer_12_out), .sel(\同步清零_气泡_高电平有效 ));
  Multiplexer #(.enable("false")) multiplexer_13 (
    .in0(ID_JAL), .in1(1'b0), .out(multiplexer_13_out), .sel(\同步清零_气泡_高电平有效 ));
  Multiplexer #(.enable("false")) multiplexer_14 (
    .in0(ID_Jmp), .in1(1'b0), .out(multiplexer_14_out), .sel(\同步清零_气泡_高电平有效 ));
  Multiplexer #(.enable("false")) multiplexer_15 (
    .in0(ID_JR), .in1(1'b0), .out(multiplexer_15_out), .sel(\同步清零_气泡_高电平有效 ));
  Multiplexer #(.enable("false")) multiplexer_16 (
    .in0(ID_Shift), .in1(1'b0), .out(multiplexer_16_out), .sel(\同步清零_气泡_高电平有效 ));
  Multiplexer #(.enable("false")) multiplexer_17 (
    .in0(ID_LBU), .in1(1'b0), .out(multiplexer_17_out), .sel(\同步清零_气泡_高电平有效 ));
  Multiplexer #(.enable("false")) multiplexer_18 (
    .in0(ID_BLTZ), .in1(1'b0), .out(multiplexer_18_out), .sel(\同步清零_气泡_高电平有效 ));
  Multiplexer #(.width(32), .enable("false")) multiplexer_19 (
    .in0(ID_PC), .in1({32{1'b0}}), .out(multiplexer_19_out), .sel(\同步清零_气泡_高电平有效 ));
  Multiplexer #(.width(32), .enable("false")) multiplexer_20 (
    .in0(ID_IR), .in1({32{1'b0}}), .out(multiplexer_20_out), .sel(\同步清零_气泡_高电平有效 ));
  Multiplexer #(.width(32), .enable("false")) multiplexer_21 (
    .in0(ID_R1), .in1({32{1'b0}}), .out(multiplexer_21_out), .sel(\同步清零_气泡_高电平有效 ));
  Multiplexer #(.width(32), .enable("false")) multiplexer_22 (
    .in0(ID_R2), .in1({32{1'b0}}), .out(multiplexer_22_out), .sel(\同步清零_气泡_高电平有效 ));
  Multiplexer #(.width(32), .enable("false")) multiplexer_23 (
    .in0(ID_immed), .in1({32{1'b0}}), .out(multiplexer_23_out), .sel(\同步清零_气泡_高电平有效 ));
  Multiplexer #(.width(5), .enable("false")) multiplexer_24 (
    .in0(ID_shamt), .in1({5{1'b0}}), .out(multiplexer_24_out), .sel(\同步清零_气泡_高电平有效 ));
  Multiplexer #(.enable("false")) multiplexer_25 (
    .in0(\传输状态In_表明当前传输数据有效 ), .in1(1'b0), .out(multiplexer_25_out), .sel(\同步清零_气泡_高电平有效 ));
  not not_1 (not_1_out, \使能端_低电平有效_stall_高电平有效 );
  Register #(.width(5)) register_1 (.D(multiplexer_1_out), .en(not_1_out), .Q(EX_R2_num), .clk(CLK));  // open: clr
  Register #(.width(5)) register_2 (.D(multiplexer_2_out), .en(not_1_out), .Q(EX_R1_num), .clk(CLK));  // open: clr
  Register #(.width(1)) register_3 (.D(multiplexer_3_out), .en(not_1_out), .Q(EX_Syscall), .clk(CLK));  // open: clr
  Register #(.width(5)) register_4 (.D(multiplexer_4_out), .en(not_1_out), .Q(EX_W_num), .clk(CLK));  // open: clr
  Register #(.width(32)) register_5 (.D(multiplexer_5_out), .en(not_1_out), .Q(EX_Jaddr), .clk(CLK));  // open: clr
  Register #(.width(1)) register_6 (.D(multiplexer_6_out), .en(not_1_out), .Q(EX_Beq), .clk(CLK));  // open: clr
  Register #(.width(1)) register_7 (.D(multiplexer_7_out), .en(not_1_out), .Q(EX_Bne), .clk(CLK));  // open: clr
  Register #(.width(1)) register_8 (.D(multiplexer_8_out), .en(not_1_out), .Q(EX_MemToReg), .clk(CLK));  // open: clr
  Register #(.width(1)) register_9 (.D(multiplexer_9_out), .en(not_1_out), .Q(EX_MemWrite), .clk(CLK));  // open: clr
  Register #(.width(4)) register_10 (.D(multiplexer_10_out), .en(not_1_out), .Q(EX_AluOP), .clk(CLK));  // open: clr
  Register #(.width(1)) register_11 (.D(multiplexer_11_out), .en(not_1_out), .Q(EX_ALUSrcB), .clk(CLK));  // open: clr
  Register #(.width(1)) register_12 (.D(multiplexer_12_out), .en(not_1_out), .Q(EX_RegWrite), .clk(CLK));  // open: clr
  Register #(.width(1)) register_13 (.D(multiplexer_13_out), .en(not_1_out), .Q(EX_JAL), .clk(CLK));  // open: clr
  Register #(.width(1)) register_14 (.D(multiplexer_14_out), .en(not_1_out), .Q(EX_Jmp), .clk(CLK));  // open: clr
  Register #(.width(1)) register_15 (.D(multiplexer_15_out), .en(not_1_out), .Q(EX_JR), .clk(CLK));  // open: clr
  Register #(.width(1)) register_16 (.D(multiplexer_16_out), .en(not_1_out), .Q(EX_Shift), .clk(CLK));  // open: clr
  Register #(.width(1)) register_17 (.D(multiplexer_17_out), .en(not_1_out), .Q(EX_LBU), .clk(CLK));  // open: clr
  Register #(.width(1)) register_18 (.D(multiplexer_18_out), .en(not_1_out), .Q(EX_BLTZ), .clk(CLK));  // open: clr
  Register #(.width(32)) register_19 (.D(multiplexer_19_out), .en(not_1_out), .Q(EX_PC), .clk(CLK));  // open: clr
  Register #(.width(32)) register_20 (.D(multiplexer_20_out), .en(not_1_out), .Q(EX_IR), .clk(CLK));  // open: clr
  Register #(.width(32)) register_21 (.D(multiplexer_21_out), .en(not_1_out), .Q(EX_R1), .clk(CLK));  // open: clr
  Register #(.width(32)) register_22 (.D(multiplexer_22_out), .en(not_1_out), .Q(EX_R2), .clk(CLK));  // open: clr
  Register #(.width(32)) register_23 (.D(multiplexer_23_out), .en(not_1_out), .Q(EX_immed), .clk(CLK));  // open: clr
  Register #(.width(5)) register_24 (.D(multiplexer_24_out), .en(not_1_out), .Q(EX_shamt), .clk(CLK));  // open: clr
  Register #(.width(1)) register_25 (
    .D(multiplexer_25_out), .en(not_1_out), .Q(\传输状态Out_表明当前传输数据有效 ), .clk(CLK));  // open: clr
endmodule

module EX_MEM (
  input  EX_display,
  input  EX_stop,
  input  EX_MemToReg,
  input  EX_MemWrite,
  input  [4:0] EX_W_num,
  input  EX_RegWrite,
  input  EX_JAL,
  input  EX_LBU,
  input  [31:0] EX_PC,
  input  [31:0] EX_IR,
  input  [31:0] EX_Result,
  input  [31:0] EX_R2,
  input  \传输状态In_表明当前传输数据有效 ,
  input  CLK,
  input  \同步清零_气泡_高电平有效 ,
  input  \使能端_低电平有效_stall_高电平有效 ,
  output MEM_display,
  output MEM_stop,
  output MEM_MemToReg,
  output MEM_MemWrite,
  output [4:0] MEM_W_num,
  output MEM_RegWrite,
  output MEM_JAL,
  output MEM_LBU,
  output [31:0] MEM_PC,
  output [31:0] MEM_IR,
  output [31:0] MEM_Result,
  output [31:0] MEM_R2,
  output \传输状态Out_表明当前传输数据有效 
);

  wire multiplexer_1_out, multiplexer_2_out, multiplexer_3_out, multiplexer_4_out, multiplexer_6_out,
       multiplexer_7_out, multiplexer_8_out, multiplexer_13_out, not_1_out;
  wire [4:0] multiplexer_5_out;
  wire [31:0] multiplexer_9_out, multiplexer_10_out, multiplexer_11_out, multiplexer_12_out;

  Multiplexer #(.enable("false")) multiplexer_1 (
    .in0(EX_display), .in1(1'b0), .out(multiplexer_1_out), .sel(\同步清零_气泡_高电平有效 ));
  Multiplexer #(.enable("false")) multiplexer_2 (
    .in0(EX_stop), .in1(1'b0), .out(multiplexer_2_out), .sel(\同步清零_气泡_高电平有效 ));
  Multiplexer #(.enable("false")) multiplexer_3 (
    .in0(EX_MemToReg), .in1(1'b0), .out(multiplexer_3_out), .sel(\同步清零_气泡_高电平有效 ));
  Multiplexer #(.enable("false")) multiplexer_4 (
    .in0(EX_MemWrite), .in1(1'b0), .out(multiplexer_4_out), .sel(\同步清零_气泡_高电平有效 ));
  Multiplexer #(.width(5), .enable("false")) multiplexer_5 (
    .in0(EX_W_num), .in1({5{1'b0}}), .out(multiplexer_5_out), .sel(\同步清零_气泡_高电平有效 ));
  Multiplexer #(.enable("false")) multiplexer_6 (
    .in0(EX_RegWrite), .in1(1'b0), .out(multiplexer_6_out), .sel(\同步清零_气泡_高电平有效 ));
  Multiplexer #(.enable("false")) multiplexer_7 (
    .in0(EX_JAL), .in1(1'b0), .out(multiplexer_7_out), .sel(\同步清零_气泡_高电平有效 ));
  Multiplexer #(.enable("false")) multiplexer_8 (
    .in0(EX_LBU), .in1(1'b0), .out(multiplexer_8_out), .sel(\同步清零_气泡_高电平有效 ));
  Multiplexer #(.width(32), .enable("false")) multiplexer_9 (
    .in0(EX_PC), .in1({32{1'b0}}), .out(multiplexer_9_out), .sel(\同步清零_气泡_高电平有效 ));
  Multiplexer #(.width(32), .enable("false")) multiplexer_10 (
    .in0(EX_IR), .in1({32{1'b0}}), .out(multiplexer_10_out), .sel(\同步清零_气泡_高电平有效 ));
  Multiplexer #(.width(32), .enable("false")) multiplexer_11 (
    .in0(EX_Result), .in1({32{1'b0}}), .out(multiplexer_11_out), .sel(\同步清零_气泡_高电平有效 ));
  Multiplexer #(.width(32), .enable("false")) multiplexer_12 (
    .in0(EX_R2), .in1({32{1'b0}}), .out(multiplexer_12_out), .sel(\同步清零_气泡_高电平有效 ));
  Multiplexer #(.enable("false")) multiplexer_13 (
    .in0(\传输状态In_表明当前传输数据有效 ), .in1(1'b0), .out(multiplexer_13_out), .sel(\同步清零_气泡_高电平有效 ));
  not not_1 (not_1_out, \使能端_低电平有效_stall_高电平有效 );
  Register #(.width(1)) register_1 (.D(multiplexer_1_out), .en(not_1_out), .Q(MEM_display), .clk(CLK));  // open: clr
  Register #(.width(1)) register_2 (.D(multiplexer_2_out), .en(not_1_out), .Q(MEM_stop), .clk(CLK));  // open: clr
  Register #(.width(1)) register_3 (.D(multiplexer_3_out), .en(not_1_out), .Q(MEM_MemToReg), .clk(CLK));  // open: clr
  Register #(.width(1)) register_4 (.D(multiplexer_4_out), .en(not_1_out), .Q(MEM_MemWrite), .clk(CLK));  // open: clr
  Register #(.width(5)) register_5 (.D(multiplexer_5_out), .en(not_1_out), .Q(MEM_W_num), .clk(CLK));  // open: clr
  Register #(.width(1)) register_6 (.D(multiplexer_6_out), .en(not_1_out), .Q(MEM_RegWrite), .clk(CLK));  // open: clr
  Register #(.width(1)) register_7 (.D(multiplexer_7_out), .en(not_1_out), .Q(MEM_JAL), .clk(CLK));  // open: clr
  Register #(.width(1)) register_8 (.D(multiplexer_8_out), .en(not_1_out), .Q(MEM_LBU), .clk(CLK));  // open: clr
  Register #(.width(32)) register_9 (.D(multiplexer_9_out), .en(not_1_out), .Q(MEM_PC), .clk(CLK));  // open: clr
  Register #(.width(32)) register_10 (.D(multiplexer_10_out), .en(not_1_out), .Q(MEM_IR), .clk(CLK));  // open: clr
  Register #(.width(32)) register_11 (.D(multiplexer_11_out), .en(not_1_out), .Q(MEM_Result), .clk(CLK));  // open: clr
  Register #(.width(32)) register_12 (.D(multiplexer_12_out), .en(not_1_out), .Q(MEM_R2), .clk(CLK));  // open: clr
  Register #(.width(1)) register_13 (
    .D(multiplexer_13_out), .en(not_1_out), .Q(\传输状态Out_表明当前传输数据有效 ), .clk(CLK));  // open: clr
endmodule

module MEM_WB (
  input  MEM_display,
  input  MEM_stop,
  input  [4:0] MEM_W_num,
  input  MEM_RegWrite,
  input  MEM_JAL,
  input  [31:0] MEM_PC,
  input  [31:0] MEM_IR,
  input  [31:0] MEM_Din,
  input  [31:0] MEM_R2,
  input  \传输状态In_表明当前传输数据有效 ,
  input  CLK,
  input  \同步清零_气泡_高电平有效 ,
  input  \使能端_低电平有效_stall_高电平有效 ,
  output WB_display,
  output WB_stop,
  output [4:0] WB_W_num,
  output WB_RegWrite,
  output WB_JAL,
  output [31:0] WE_PC,
  output [31:0] WE_IR,
  output [31:0] WB_Din,
  output [31:0] WE_R2,
  output \传输状态Out_表明当前传输数据有效 
);

  wire multiplexer_1_out, multiplexer_2_out, multiplexer_4_out, multiplexer_5_out, multiplexer_10_out,
       not_1_out;
  wire [4:0] multiplexer_3_out;
  wire [31:0] multiplexer_6_out, multiplexer_7_out, multiplexer_8_out, multiplexer_9_out;

  Multiplexer #(.enable("false")) multiplexer_1 (
    .in0(MEM_display), .in1(1'b0), .out(multiplexer_1_out), .sel(\同步清零_气泡_高电平有效 ));
  Multiplexer #(.enable("false")) multiplexer_2 (
    .in0(MEM_stop), .in1(1'b0), .out(multiplexer_2_out), .sel(\同步清零_气泡_高电平有效 ));
  Multiplexer #(.width(5), .enable("false")) multiplexer_3 (
    .in0(MEM_W_num), .in1({5{1'b0}}), .out(multiplexer_3_out), .sel(\同步清零_气泡_高电平有效 ));
  Multiplexer #(.enable("false")) multiplexer_4 (
    .in0(MEM_RegWrite), .in1(1'b0), .out(multiplexer_4_out), .sel(\同步清零_气泡_高电平有效 ));
  Multiplexer #(.enable("false")) multiplexer_5 (
    .in0(MEM_JAL), .in1(1'b0), .out(multiplexer_5_out), .sel(\同步清零_气泡_高电平有效 ));
  Multiplexer #(.width(32), .enable("false")) multiplexer_6 (
    .in0(MEM_PC), .in1({32{1'b0}}), .out(multiplexer_6_out), .sel(\同步清零_气泡_高电平有效 ));
  Multiplexer #(.width(32), .enable("false")) multiplexer_7 (
    .in0(MEM_IR), .in1({32{1'b0}}), .out(multiplexer_7_out), .sel(\同步清零_气泡_高电平有效 ));
  Multiplexer #(.width(32), .enable("false")) multiplexer_8 (
    .in0(MEM_Din), .in1({32{1'b0}}), .out(multiplexer_8_out), .sel(\同步清零_气泡_高电平有效 ));
  Multiplexer #(.width(32), .enable("false")) multiplexer_9 (
    .in0(MEM_R2), .in1({32{1'b0}}), .out(multiplexer_9_out), .sel(\同步清零_气泡_高电平有效 ));
  Multiplexer #(.enable("false")) multiplexer_10 (
    .in0(\传输状态In_表明当前传输数据有效 ), .in1(1'b0), .out(multiplexer_10_out), .sel(\同步清零_气泡_高电平有效 ));
  not not_1 (not_1_out, \使能端_低电平有效_stall_高电平有效 );
  Register #(.width(1)) register_1 (.D(multiplexer_1_out), .en(not_1_out), .Q(WB_display), .clk(CLK));  // open: clr
  Register #(.width(1)) register_2 (.D(multiplexer_2_out), .en(not_1_out), .Q(WB_stop), .clk(CLK));  // open: clr
  Register #(.width(5)) register_3 (.D(multiplexer_3_out), .en(not_1_out), .Q(WB_W_num), .clk(CLK));  // open: clr
  Register #(.width(1)) register_4 (.D(multiplexer_4_out), .en(not_1_out), .Q(WB_RegWrite), .clk(CLK));  // open: clr
  Register #(.width(1)) register_5 (.D(multiplexer_5_out), .en(not_1_out), .Q(WB_JAL), .clk(CLK));  // open: clr
  Register #(.width(32)) register_6 (.D(multiplexer_6_out), .en(not_1_out), .Q(WE_PC), .clk(CLK));  // open: clr
  Register #(.width(32)) register_7 (.D(multiplexer_7_out), .en(not_1_out), .Q(WE_IR), .clk(CLK));  // open: clr
  Register #(.width(32)) register_8 (.D(multiplexer_8_out), .en(not_1_out), .Q(WB_Din), .clk(CLK));  // open: clr
  Register #(.width(32)) register_9 (.D(multiplexer_9_out), .en(not_1_out), .Q(WE_R2), .clk(CLK));  // open: clr
  Register #(.width(1)) register_10 (
    .D(multiplexer_10_out), .en(not_1_out), .Q(\传输状态Out_表明当前传输数据有效 ), .clk(CLK));  // open: clr
endmodule

module \分支相关流水线  (
);

  wire and_1_out, and_2_out, and_3_out, and_5_out, CLK, comparator_1_eq, comparator_2_eq, Cond, EX_Beq,
       EX_BLTZ, EX_Bne, EX_Jmp, EX_JR, ex_mem_1_mem_jal, ex_mem_1_mem_memtoreg, ex_mem_1_mem_regwrite,
       ex_mem_1_mem_stop, \ex_mem_1_传输状态out_表明当前传输数据有效 , EX_Shift, Go, ID_BLTZ, id_ex_1_ex_alusrcb,
       id_ex_1_ex_jal, id_ex_1_ex_lbu, id_ex_1_ex_memtoreg, id_ex_1_ex_memwrite, id_ex_1_ex_regwrite,
       id_ex_1_ex_syscall, \id_ex_1_传输状态out_表明当前传输数据有效 , ID_JAL, ID_Jmp, ID_JR, ID_LBU, ID_RegDst, ID_Shift,
       ID_SignedExt, ID_stop, ID_Syscall, \if_id_1_传输状态out_表明当前传输数据有效 , IR1, IR2, IR3, MEM_LBU, MEM_MemWrite,
       mem_wb_1_wb_jal, mips_alu_1_equal, not_1_out, not_2_out, not_3_out, not_4_out, or_1_out, RST, Run, W1,
       W2, W3, WB_RegWrite, WE_stop, \硬布线控制器_1_alu_src , \硬布线控制器_1_beq , \硬布线控制器_1_bne , \硬布线控制器_1_memtoreg ,
       \硬布线控制器_1_memwrite , \硬布线控制器_1_regwrite , \硬布线控制器_1_sllv , \硬布线控制器_1_srlv ;
  wire [3:0] id_ex_1_ex_aluop, \硬布线控制器_1_alu_op ;
  wire [4:0] ex_mem_1_mem_w_num, id_ex_1_ex_shamt, id_ex_1_ex_w_num, ID_W_num, if_id_1_id_ir_3,
       if_id_1_id_ir_4, if_id_1_id_ir_5, if_id_1_id_ir_6, multiplexer_2_out, multiplexer_3_out,
       multiplexer_4_out, multiplexer_9_out, WB_W_num;
  wire [5:0] if_id_1_id_ir, if_id_1_id_ir_2;
  wire [7:0] multiplexer_11_out;
  wire [15:0] \LoadUse次数 , \总周期数 , \插入气泡数 , \无条件分支数 , \条件分支成功数 ;
  wire [31:0] adder_1_out, adder_2_out, adder_3_out, adder_5_out, bit_extender_1_out, bit_extender_2_out,
       EX_Cond_addr, ex_mem_1_mem_ir, ex_mem_1_mem_r2, ex_mem_1_mem_result, EX_PC, EX_R1, EX_Uncond_addr,
       id_ex_1_ex_immed, id_ex_1_ex_ir, id_ex_1_ex_jaddr, id_ex_1_ex_r2, ID_PC, ID_R1, ID_R2, IF_PC, LedData,
       MEM_PC, mem_wb_1_wb_din, mem_wb_1_we_ir, mips_alu_1_result, multiplexer_1_out, multiplexer_6_out,
       multiplexer_8_out, multiplexer_10_out, multiplexer_12_out, ram_1_data, rom_1_data, shifter_1_out,
       WB_Din, WB_PC;

  Button \u_总复位  (.out(RST));
  Button _1 (.out(IR1));
  Button _2 (.out(IR2));
  Button _3 (.out(IR3));
  Button \u_继续运行  (.out(Go));
  LED led_1 (.in(W1));
  LED led_2 (.in(W2));
  LED led_3 (.in(W3));
  Hex_Digit_Display hex_digit_display_1 (.value(LedData[31:28]));  // open: dp
  Hex_Digit_Display hex_digit_display_2 (.value(LedData[23:20]));  // open: dp
  Hex_Digit_Display hex_digit_display_3 (.value(LedData[27:24]));  // open: dp
  Multiplexer #(.select(2), .width(32), .enable("false")) multiplexer_1 (
    .in0(adder_1_out), .in1(EX_Uncond_addr), .in2(EX_Cond_addr), .out(multiplexer_1_out), .sel({Cond, EX_Jmp}));  // open: in3
  Hex_Digit_Display hex_digit_display_4 (.value(LedData[19:16]));  // open: dp
  Hex_Digit_Display hex_digit_display_5 (.value(LedData[15:12]));  // open: dp
  Hex_Digit_Display hex_digit_display_6 (.value(LedData[11:8]));  // open: dp
  Hex_Digit_Display hex_digit_display_7 (.value(LedData[7:4]));  // open: dp
  Clock clock_1 (.out(CLK));
  Hex_Digit_Display hex_digit_display_8 (.value(LedData[3:0]));  // open: dp
  Register #(.width(32)) PC (.D(multiplexer_1_out), .en(Run), .Q(IF_PC), .clk(CLK), .clr(RST));
  Adder #(.width(32)) adder_1 (.a(IF_PC), .b(32'h4), .out(adder_1_out));  // open: cin, cout
  // Probe on \总周期数 
  // Probe on \无条件分支数 
  // Probe on \条件分支成功数 
  // Probe on \插入气泡数 
  // Probe on \LoadUse次数 
  // Probe on IF_PC[11:0]
  ROM #(.addrWidth(10), .dataWidth(32)) rom_1 (.addr(IF_PC[11:2]), .data(rom_1_data));  // open: sel
  not not_1 (not_1_out, Run);
  // Probe on ID_PC[11:0]
  IF_ID if_id_1 (
    .IF_PC(IF_PC), .IF_IR(rom_1_data), .\传输状态In_表明当前传输数据有效 (1'b1), .CLK(CLK), .ID_PC(ID_PC),
    .ID_IR({if_id_1_id_ir, if_id_1_id_ir_6, if_id_1_id_ir_5, if_id_1_id_ir_4, if_id_1_id_ir_3, if_id_1_id_ir_2}),
    .\传输状态Out_表明当前传输数据有效 (\if_id_1_传输状态out_表明当前传输数据有效 ), .\同步清零_气泡_高电平有效 (or_1_out),
    .\使能端_低电平有效_stall_高电平有效 (not_1_out));
  // Probe on EX_PC[11:0]
  // Probe on MEM_PC[11:0]
  or or_1 (or_1_out, EX_Jmp, Cond);
  // Probe on WB_PC[11:0]
  // Probe on {if_id_1_id_ir, if_id_1_id_ir_6, if_id_1_id_ir_5, if_id_1_id_ir_4, if_id_1_id_ir_3, if_id_1_id_ir_2}
  or or_2 (ID_Shift, \硬布线控制器_1_sllv , \硬布线控制器_1_srlv );
  Adder #(.width(32)) adder_2 (.a(ID_PC), .b(32'h4), .out(adder_2_out));  // open: cin, cout
  Multiplexer #(.width(5), .enable("false")) multiplexer_2 (
    .in0(if_id_1_id_ir_5), .in1(if_id_1_id_ir_4), .out(multiplexer_2_out), .sel(ID_RegDst));
  or or_3 (Run, Go, ~WE_stop);  // OR_Gate
  \硬布线控制器  \u_硬布线控制器_1  (
    .Func(if_id_1_id_ir_2), .OP(if_id_1_id_ir), .ALU_OP(\硬布线控制器_1_alu_op ), .MemToReg(\硬布线控制器_1_memtoreg ),
    .MemWrite(\硬布线控制器_1_memwrite ), .ALU_SRC(\硬布线控制器_1_alu_src ), .RegWrite(\硬布线控制器_1_regwrite ),
    .SysCALL(ID_Syscall), .SignedExt(ID_SignedExt), .RegDst(ID_RegDst), .JR(ID_JR), .JMP(ID_Jmp),
    .Beq(\硬布线控制器_1_beq ), .JAL(ID_JAL), .Bne(\硬布线控制器_1_bne ), .SLLV(\硬布线控制器_1_sllv ), .SRLV(\硬布线控制器_1_srlv ),
    .LBU(ID_LBU), .BLTZ(ID_BLTZ), .REGIMM(if_id_1_id_ir_5));
  Multiplexer #(.width(5), .enable("false")) multiplexer_3 (
    .in0(if_id_1_id_ir_6), .in1(5'b00010), .out(multiplexer_3_out), .sel(ID_Syscall));
  Multiplexer #(.width(5), .enable("false")) multiplexer_4 (
    .in0(if_id_1_id_ir_5), .in1(5'b00100), .out(multiplexer_4_out), .sel(ID_Syscall));
  Multiplexer #(.width(5), .enable("false")) multiplexer_5 (
    .in0(multiplexer_2_out), .in1({5{1'b1}}), .out(ID_W_num), .sel(ID_JAL));
  assign bit_extender_1_out = {{16{1'b0}}, {if_id_1_id_ir_4, if_id_1_id_ir_3, if_id_1_id_ir_2}};  // Bit_Extender bit_extender_1
  assign bit_extender_2_out = {{16{if_id_1_id_ir_4[4]}}, {if_id_1_id_ir_4, if_id_1_id_ir_3, if_id_1_id_ir_2}};  // Bit_Extender bit_extender_2
  Multiplexer #(.width(32), .enable("false")) multiplexer_6 (
    .in0(bit_extender_1_out), .in1(bit_extender_2_out), .out(multiplexer_6_out), .sel(ID_SignedExt));
  Counter #(.width(16), .max('hffff)) counter_1 (
    .count(Run), .Q(\总周期数 ), .clk(CLK), .clr(RST));  // open: load, D, carry
  or or_4 (Cond, and_1_out, and_2_out, and_3_out);
  MIPS_Regifile mips_regifile_1 (
    .Din(WB_Din), .Clk(CLK), .R1(ID_R1), .R2(ID_R2), .WE(WB_RegWrite), .W_num(WB_W_num),
    .R1_num(multiplexer_3_out), .R2_num(multiplexer_4_out));
  not not_2 (not_2_out, Run);
  Counter #(.width(16), .max('hffff)) counter_2 (
    .count(Cond), .Q(\条件分支成功数 ), .clk(CLK), .clr(RST));  // open: load, D, carry
  and and_1 (and_1_out, mips_alu_1_result[0], EX_BLTZ);
  and and_2 (and_2_out, ~mips_alu_1_equal, EX_Bne);  // AND_Gate
  and and_3 (and_3_out, mips_alu_1_equal, EX_Beq);
  ID_EX id_ex_1 (
    .ID_PC(ID_PC),
    .ID_IR({if_id_1_id_ir, if_id_1_id_ir_6, if_id_1_id_ir_5, if_id_1_id_ir_4, if_id_1_id_ir_3, if_id_1_id_ir_2}),
    .ID_R1(ID_R1), .ID_R2(ID_R2), .ID_immed(multiplexer_6_out), .ID_shamt(if_id_1_id_ir_3),
    .\传输状态In_表明当前传输数据有效 (\if_id_1_传输状态out_表明当前传输数据有效 ), .CLK(CLK), .EX_PC(EX_PC), .EX_IR(id_ex_1_ex_ir),
    .EX_R1(EX_R1), .EX_R2(id_ex_1_ex_r2), .EX_immed(id_ex_1_ex_immed), .EX_shamt(id_ex_1_ex_shamt),
    .\传输状态Out_表明当前传输数据有效 (\id_ex_1_传输状态out_表明当前传输数据有效 ), .\同步清零_气泡_高电平有效 (or_1_out),
    .\使能端_低电平有效_stall_高电平有效 (not_2_out), .ID_BLTZ(ID_BLTZ), .EX_BLTZ(EX_BLTZ), .ID_LBU(ID_LBU),
    .EX_LBU(id_ex_1_ex_lbu), .ID_Shift(ID_Shift), .EX_Shift(EX_Shift), .ID_JR(ID_JR), .EX_JR(EX_JR),
    .ID_Jmp(ID_Jmp), .EX_Jmp(EX_Jmp), .ID_JAL(ID_JAL), .EX_JAL(id_ex_1_ex_jal),
    .ID_RegWrite(\硬布线控制器_1_regwrite ), .EX_RegWrite(id_ex_1_ex_regwrite), .ID_ALUSrcB(\硬布线控制器_1_alu_src ),
    .EX_ALUSrcB(id_ex_1_ex_alusrcb), .ID_AluOP(\硬布线控制器_1_alu_op ), .EX_AluOP(id_ex_1_ex_aluop),
    .ID_MemWrite(\硬布线控制器_1_memwrite ), .EX_MemWrite(id_ex_1_ex_memwrite), .ID_MemToReg(\硬布线控制器_1_memtoreg ),
    .EX_MemToReg(id_ex_1_ex_memtoreg), .ID_Bne(\硬布线控制器_1_bne ), .EX_Bne(EX_Bne), .ID_Beq(\硬布线控制器_1_beq ),
    .EX_Beq(EX_Beq),
    .ID_Jaddr({adder_2_out[31:28], if_id_1_id_ir_6, if_id_1_id_ir_5, if_id_1_id_ir_4, if_id_1_id_ir_3, if_id_1_id_ir_2, 2'b00}),
    .EX_Jaddr(id_ex_1_ex_jaddr), .ID_W_num(ID_W_num), .EX_W_num(id_ex_1_ex_w_num), .ID_Syscall(ID_stop),
    .EX_Syscall(id_ex_1_ex_syscall));  // open: ID_R1_num, EX_R1_num, ID_R2_num, EX_R2_num
  Shifter #(.width(32)) shifter_1 (.in(id_ex_1_ex_immed), .\dist (5'b00010), .out(shifter_1_out));
  Multiplexer #(.width(32), .enable("false")) multiplexer_7 (
    .in0(id_ex_1_ex_jaddr), .in1(EX_R1), .out(EX_Uncond_addr), .sel(EX_JR));
  Multiplexer #(.width(32), .enable("false")) multiplexer_8 (
    .in0(id_ex_1_ex_r2), .in1(id_ex_1_ex_immed), .out(multiplexer_8_out), .sel(id_ex_1_ex_alusrcb));
  Multiplexer #(.width(5), .enable("false")) multiplexer_9 (
    .in0(id_ex_1_ex_shamt), .in1(EX_R1[4:0]), .out(multiplexer_9_out), .sel(EX_Shift));
  Adder #(.width(32)) adder_3 (.a(EX_PC), .b(32'h4), .out(adder_3_out));  // open: cin, cout
  Counter #(.width(16), .max('hffff)) counter_3 (
    .count(EX_Jmp), .Q(\无条件分支数 ), .clk(CLK), .clr(RST));  // open: load, D, carry
  MIPS_ALU mips_alu_1 (
    .X(EX_R1), .Y(multiplexer_8_out), .AluOP(id_ex_1_ex_aluop), .Equal(mips_alu_1_equal),
    .Result(mips_alu_1_result), .shamt(multiplexer_9_out));  // open: Result_2
  Adder #(.width(32)) adder_4 (.a(shifter_1_out), .b(adder_3_out), .out(EX_Cond_addr));  // open: cin, cout
  not not_3 (not_3_out, Run);
  EX_MEM ex_mem_1 (
    .EX_MemToReg(id_ex_1_ex_memtoreg), .EX_MemWrite(id_ex_1_ex_memwrite), .EX_RegWrite(id_ex_1_ex_regwrite),
    .EX_JAL(id_ex_1_ex_jal), .EX_LBU(id_ex_1_ex_lbu), .EX_PC(EX_PC), .EX_IR(id_ex_1_ex_ir),
    .EX_Result(mips_alu_1_result), .EX_R2(id_ex_1_ex_r2), .\传输状态In_表明当前传输数据有效 (\id_ex_1_传输状态out_表明当前传输数据有效 ),
    .CLK(CLK), .MEM_MemToReg(ex_mem_1_mem_memtoreg), .MEM_MemWrite(MEM_MemWrite),
    .MEM_RegWrite(ex_mem_1_mem_regwrite), .MEM_JAL(ex_mem_1_mem_jal), .MEM_LBU(MEM_LBU), .MEM_PC(MEM_PC),
    .MEM_IR(ex_mem_1_mem_ir), .MEM_Result(ex_mem_1_mem_result), .MEM_R2(ex_mem_1_mem_r2),
    .\传输状态Out_表明当前传输数据有效 (\ex_mem_1_传输状态out_表明当前传输数据有效 ), .\同步清零_气泡_高电平有效 (1'b0),
    .\使能端_低电平有效_stall_高电平有效 (not_3_out), .EX_W_num(id_ex_1_ex_w_num), .MEM_W_num(ex_mem_1_mem_w_num),
    .EX_stop(id_ex_1_ex_syscall), .MEM_stop(ex_mem_1_mem_stop));  // open: EX_display, MEM_display
  Comparator #(.width(32), .mode("unsigned")) comparator_1 (
    .a(ID_R1), .b(32'h22), .eq(comparator_1_eq));  // open: gt, lt
  RAM #(.addrWidth(10), .dataWidth(32), .bus("separate")) ram_1 (
    .addr(ex_mem_1_mem_result[11:2]), .din(ex_mem_1_mem_r2), .data(ram_1_data), .str(MEM_MemWrite),
    .sel(1'b1), .clk(CLK), .ld(1'b1), .clr(RST));
  Multiplexer #(.width(32), .enable("false")) multiplexer_10 (
    .in0(ex_mem_1_mem_result), .in1(ram_1_data), .out(multiplexer_10_out), .sel(ex_mem_1_mem_memtoreg));
  and and_4 (ID_stop, ~comparator_1_eq, ID_Syscall);  // AND_Gate
  Multiplexer #(.select(2), .width(8), .enable("false")) multiplexer_11 (
    .in0(multiplexer_10_out[7:0]), .in1(multiplexer_10_out[15:8]), .in2(multiplexer_10_out[23:16]),
    .in3(multiplexer_10_out[31:24]), .out(multiplexer_11_out), .sel(ex_mem_1_mem_result[1:0]));
  Multiplexer #(.width(32), .enable("false")) multiplexer_12 (
    .in0(multiplexer_10_out), .in1({{24{1'b0}}, multiplexer_11_out}), .out(multiplexer_12_out), .sel(MEM_LBU));
  not not_4 (not_4_out, Run);
  MEM_WB mem_wb_1 (
    .MEM_W_num(ex_mem_1_mem_w_num), .MEM_RegWrite(ex_mem_1_mem_regwrite), .MEM_PC(MEM_PC),
    .MEM_IR(ex_mem_1_mem_ir), .MEM_Din(multiplexer_12_out),
    .\传输状态In_表明当前传输数据有效 (\ex_mem_1_传输状态out_表明当前传输数据有效 ), .CLK(CLK), .WB_W_num(WB_W_num),
    .WB_RegWrite(WB_RegWrite), .WE_PC(WB_PC), .WE_IR(mem_wb_1_we_ir), .WB_Din(mem_wb_1_wb_din),
    .\同步清零_气泡_高电平有效 (1'b0), .\使能端_低电平有效_stall_高电平有效 (not_4_out), .MEM_JAL(ex_mem_1_mem_jal),
    .WB_JAL(mem_wb_1_wb_jal), .MEM_stop(ex_mem_1_mem_stop), .WB_stop(WE_stop));  // open: 传输状态Out_表明当前传输数据有效, MEM_display, WB_display, MEM_R2, WE_R2
  Adder #(.width(32)) adder_5 (.a(WB_PC), .b(32'h4), .out(adder_5_out));  // open: cin, cout
  Comparator #(.width(32), .mode("unsigned")) comparator_2 (
    .a(ID_R1), .b(32'h22), .eq(comparator_2_eq));  // open: gt, lt
  Multiplexer #(.width(32), .enable("false")) multiplexer_13 (
    .in0(mem_wb_1_wb_din), .in1(adder_5_out), .out(WB_Din), .sel(mem_wb_1_wb_jal));
  buf and_5 (and_5_out, ID_Syscall);  // AND_Gate
  Register #(.width(32)) register_1 (.D(ID_R2), .en(and_5_out), .Q(LedData), .clk(CLK), .clr(RST));

  // Other names for the same wires on the sheet: Uncond = EX_Jmp

  // Notes on the sheet:
  //   中断源
  //   中断等待指示
  //   数码管输出
  //   指令存储器
  //   contents of rom_1 (hex, n*v repeats v):
  //   20110100 20020022 8000006 20110004 20120005 20130006 10000003 20110007 20120008 20130009 14110003
  //   2011000a 2012000b 2013000c c000014 2002000a 0 0 0 c 2231ffff 0 0 0 112020 0 0 0 c 1620fff6 3e00008
  //   流水调试日志用
  //   指令字
  //   rd
endmodule

module \气泡流水线  (
);

  wire and_1_out, and_2_out, and_3_out, and_5_out, and_6_out, and_7_out, and_8_out, CLK, comparator_1_eq,
       comparator_2_eq, Cond, EX_Beq, EX_BLTZ, EX_Bne, EX_Jmp, EX_JR, ex_mem_1_mem_jal,
       ex_mem_1_mem_memtoreg, ex_mem_1_mem_stop, \ex_mem_1_传输状态out_表明当前传输数据有效 , EX_RegWrite, EX_Shift, Go,
       ID_BLTZ, id_ex_1_ex_alusrcb, id_ex_1_ex_jal, id_ex_1_ex_lbu, id_ex_1_ex_memtoreg, id_ex_1_ex_memwrite,
       id_ex_1_ex_syscall, \id_ex_1_传输状态out_表明当前传输数据有效 , ID_JAL, ID_Jmp, ID_JR, ID_LBU, ID_RegDst, ID_Shift,
       ID_SignedExt, ID_stop, ID_Syscall, \if_id_1_传输状态out_表明当前传输数据有效 , \int , IR1, IR2, IR3, MEM_LBU,
       MEM_MemWrite, MEM_RegWrite, mem_wb_1_wb_jal, mips_alu_1_equal, not_1_out, not_2_out, not_3_out,
       not_4_out, or_2_out, Relate, RST, Run, W1, W2, W3, WB_RegWrite, WE_stop, \硬布线控制器_1_alu_src ,
       \硬布线控制器_1_beq , \硬布线控制器_1_bne , \硬布线控制器_1_memtoreg , \硬布线控制器_1_memwrite , \硬布线控制器_1_regwrite ,
       \硬布线控制器_1_sllv , \硬布线控制器_1_srlv ;
  wire [3:0] id_ex_1_ex_aluop, \硬布线控制器_1_alu_op ;
  wire [4:0] EX_W_num, id_ex_1_ex_shamt, ID_R1_num, ID_R2_num, ID_W_num, if_id_1_id_ir, if_id_1_id_ir_2,
       if_id_1_id_ir_3, if_id_1_id_ir_4, MEM_W_num, multiplexer_2_out, multiplexer_9_out, WB_W_num;
  wire [5:0] ID_Func, ID_OP;
  wire [7:0] multiplexer_11_out;
  wire [15:0] \LoadUse次数 , \总周期数 , \插入气泡数 , \无条件分支数 , \条件分支成功数 ;
  wire [31:0] adder_1_out, adder_2_out, adder_3_out, adder_5_out, bit_extender_1_out, bit_extender_2_out,
       EX_Cond_addr, ex_mem_1_mem_ir, ex_mem_1_mem_r2, ex_mem_1_mem_result, EX_PC, EX_R1, EX_Uncond_addr,
       id_ex_1_ex_immed, id_ex_1_ex_ir, id_ex_1_ex_jaddr, id_ex_1_ex_r2, ID_PC, ID_R1, ID_R2, IF_PC, LedData,
       MEM_PC, mem_wb_1_wb_din, mem_wb_1_we_ir, mips_alu_1_result, multiplexer_1_out, multiplexer_6_out,
       multiplexer_8_out, multiplexer_10_out, multiplexer_12_out, ram_1_data, rom_1_data, shifter_1_out,
       WB_Din, WB_PC;

  Button \u_总复位  (.out(RST));
  Button _1 (.out(IR1));
  Button _2 (.out(IR2));
  Button _3 (.out(IR3));
  Button \u_继续运行  (.out(Go));
  LED led_1 (.in(W1));
  LED led_2 (.in(W2));
  LED led_3 (.in(W3));
  Hex_Digit_Display hex_digit_display_1 (.value(LedData[31:28]));  // open: dp
  Counter #(.width(16), .max('hffff)) counter_1 (
    .count(Run), .Q(\总周期数 ), .clk(CLK), .clr(RST));  // open: load, D, carry
  Hex_Digit_Display hex_digit_display_2 (.value(LedData[27:24]));  // open: dp
  Hex_Digit_Display hex_digit_display_3 (.value(LedData[23:20]));  // open: dp
  Multiplexer #(.select(2), .width(32), .enable("false")) multiplexer_1 (
    .in0(adder_1_out), .in1(EX_Uncond_addr), .in2(EX_Cond_addr), .out(multiplexer_1_out), .sel({Cond, EX_Jmp}));  // open: in3
  \数据相关检测  \u_数据相关检测_1  (
    .OP(ID_OP), .EX_WriteReg_num(EX_W_num), .EX_RegWrite(EX_RegWrite), .MEM_WriteReg_num(MEM_W_num),
    .MEM_RegWrite(MEM_RegWrite), .\数据相关 (Relate), .Func(ID_Func), .ID_R1_num(ID_R1_num), .ID_R2_num(ID_R2_num));
  Hex_Digit_Display hex_digit_display_4 (.value(LedData[15:12]));  // open: dp
  Hex_Digit_Display hex_digit_display_5 (.value(LedData[19:16]));  // open: dp
  Hex_Digit_Display hex_digit_display_6 (.value(LedData[7:4]));  // open: dp
  Hex_Digit_Display hex_digit_display_7 (.value(LedData[11:8]));  // open: dp
  Clock clock_1 (.out(CLK));
  and and_1 (and_1_out, Run, ~Relate);  // AND_Gate
  Counter #(.width(16), .max('hffff)) counter_2 (
    .count(Cond), .Q(\条件分支成功数 ), .clk(CLK), .clr(RST));  // open: load, D, carry
  Hex_Digit_Display hex_digit_display_8 (.value(LedData[3:0]));  // open: dp
  Register #(.width(32)) PC (.D(multiplexer_1_out), .en(and_1_out), .Q(IF_PC), .clk(CLK), .clr(RST));
  Adder #(.width(32)) adder_1 (.a(IF_PC), .b(32'h4), .out(adder_1_out));  // open: cin, cout
  // Probe on \总周期数 
  // Probe on \无条件分支数 
  // Probe on \条件分支成功数 
  // Probe on \插入气泡数 
  // Probe on \LoadUse次数 
  and and_2 (and_2_out, Run, ~Relate);  // AND_Gate
  Counter #(.width(16), .max('hffff)) counter_3 (
    .count(EX_Jmp), .Q(\无条件分支数 ), .clk(CLK), .clr(RST));  // open: load, D, carry
  // Probe on IF_PC[11:0]
  ROM #(.addrWidth(10), .dataWidth(32)) rom_1 (.addr(IF_PC[11:2]), .data(rom_1_data));  // open: sel
  not not_1 (not_1_out, and_2_out);
  // Probe on ID_PC[11:0]
  IF_ID if_id_1 (
    .IF_PC(IF_PC), .IF_IR(rom_1_data), .\传输状态In_表明当前传输数据有效 (1'b1), .CLK(CLK), .ID_PC(ID_PC),
    .ID_IR({ID_OP, if_id_1_id_ir_4, if_id_1_id_ir_3, if_id_1_id_ir_2, if_id_1_id_ir, ID_Func}),
    .\传输状态Out_表明当前传输数据有效 (\if_id_1_传输状态out_表明当前传输数据有效 ), .\同步清零_气泡_高电平有效 (or_2_out),
    .\使能端_低电平有效_stall_高电平有效 (not_1_out));
  or or_1 (Run, Go, ~WE_stop);  // OR_Gate
  // Probe on MEM_PC[11:0]
  // Probe on EX_PC[11:0]
  or or_2 (or_2_out, EX_Jmp, Cond);
  and and_3 (and_3_out, Relate, Run);
  // Probe on WB_PC[11:0]
  // Probe on {ID_OP, if_id_1_id_ir_4, if_id_1_id_ir_3, if_id_1_id_ir_2, if_id_1_id_ir, ID_Func}
  Counter #(.width(16), .max('hffff)) counter_4 (
    .count(and_3_out), .Q(\插入气泡数 ), .clk(CLK), .clr(RST));  // open: load, D, carry
  Comparator #(.width(32), .mode("unsigned")) comparator_1 (
    .a(ID_R1), .b(32'h22), .eq(comparator_1_eq));  // open: gt, lt
  or or_3 (ID_Shift, \硬布线控制器_1_sllv , \硬布线控制器_1_srlv );
  Adder #(.width(32)) adder_2 (.a(ID_PC), .b(32'h4), .out(adder_2_out));  // open: cin, cout
  Multiplexer #(.width(5), .enable("false")) multiplexer_2 (
    .in0(if_id_1_id_ir_3), .in1(if_id_1_id_ir_2), .out(multiplexer_2_out), .sel(ID_RegDst));
  and and_4 (ID_stop, ~comparator_1_eq, ID_Syscall);  // AND_Gate
  \硬布线控制器  \u_硬布线控制器_1  (
    .Func(ID_Func), .OP(ID_OP), .ALU_OP(\硬布线控制器_1_alu_op ), .MemToReg(\硬布线控制器_1_memtoreg ),
    .MemWrite(\硬布线控制器_1_memwrite ), .ALU_SRC(\硬布线控制器_1_alu_src ), .RegWrite(\硬布线控制器_1_regwrite ),
    .SysCALL(ID_Syscall), .SignedExt(ID_SignedExt), .RegDst(ID_RegDst), .JR(ID_JR), .JMP(ID_Jmp),
    .Beq(\硬布线控制器_1_beq ), .JAL(ID_JAL), .Bne(\硬布线控制器_1_bne ), .SLLV(\硬布线控制器_1_sllv ), .SRLV(\硬布线控制器_1_srlv ),
    .LBU(ID_LBU), .BLTZ(ID_BLTZ), .REGIMM(if_id_1_id_ir_3));
  Multiplexer #(.width(5), .enable("false")) multiplexer_3 (
    .in0(if_id_1_id_ir_4), .in1(5'b00010), .out(ID_R1_num), .sel(ID_Syscall));
  Multiplexer #(.width(5), .enable("false")) multiplexer_4 (
    .in0(if_id_1_id_ir_3), .in1(5'b00100), .out(ID_R2_num), .sel(ID_Syscall));
  Multiplexer #(.width(5), .enable("false")) multiplexer_5 (
    .in0(multiplexer_2_out), .in1({5{1'b1}}), .out(ID_W_num), .sel(ID_JAL));
  assign bit_extender_1_out = {{16{1'b0}}, {if_id_1_id_ir_2, if_id_1_id_ir, ID_Func}};  // Bit_Extender bit_extender_1
  assign bit_extender_2_out = {{16{if_id_1_id_ir_2[4]}}, {if_id_1_id_ir_2, if_id_1_id_ir, ID_Func}};  // Bit_Extender bit_extender_2
  Multiplexer #(.width(32), .enable("false")) multiplexer_6 (
    .in0(bit_extender_1_out), .in1(bit_extender_2_out), .out(multiplexer_6_out), .sel(ID_SignedExt));
  or or_4 (Cond, and_5_out, and_6_out, and_7_out);
  MIPS_Regifile mips_regifile_1 (
    .Din(WB_Din), .Clk(CLK), .R1(ID_R1), .R2(ID_R2), .WE(WB_RegWrite), .W_num(WB_W_num), .R1_num(ID_R1_num),
    .R2_num(ID_R2_num));
  not not_2 (not_2_out, Run);
  Comparator #(.width(32), .mode("unsigned")) comparator_2 (
    .a(ID_R1), .b(32'h22), .eq(comparator_2_eq));  // open: gt, lt
  and and_5 (and_5_out, mips_alu_1_result[0], EX_BLTZ);
  and and_6 (and_6_out, ~mips_alu_1_equal, EX_Bne);  // AND_Gate
  and and_7 (and_7_out, mips_alu_1_equal, EX_Beq);
  or or_5 (\int , or_2_out, Relate);
  ID_EX id_ex_1 (
    .ID_PC(ID_PC),
    .ID_IR({ID_OP, if_id_1_id_ir_4, if_id_1_id_ir_3, if_id_1_id_ir_2, if_id_1_id_ir, ID_Func}),
    .ID_R1(ID_R1), .ID_R2(ID_R2), .ID_immed(multiplexer_6_out), .ID_shamt(if_id_1_id_ir),
    .\传输状态In_表明当前传输数据有效 (\if_id_1_传输状态out_表明当前传输数据有效 ), .CLK(CLK), .EX_PC(EX_PC), .EX_IR(id_ex_1_ex_ir),
    .EX_R1(EX_R1), .EX_R2(id_ex_1_ex_r2), .EX_immed(id_ex_1_ex_immed), .EX_shamt(id_ex_1_ex_shamt),
    .\传输状态Out_表明当前传输数据有效 (\id_ex_1_传输状态out_表明当前传输数据有效 ), .\同步清零_气泡_高电平有效 (\int ),
    .\使能端_低电平有效_stall_高电平有效 (not_2_out), .ID_BLTZ(ID_BLTZ), .EX_BLTZ(EX_BLTZ), .ID_LBU(ID_LBU),
    .EX_LBU(id_ex_1_ex_lbu), .ID_Shift(ID_Shift), .EX_Shift(EX_Shift), .ID_JR(ID_JR), .EX_JR(EX_JR),
    .ID_Jmp(ID_Jmp), .EX_Jmp(EX_Jmp), .ID_JAL(ID_JAL), .EX_JAL(id_ex_1_ex_jal),
    .ID_RegWrite(\硬布线控制器_1_regwrite ), .EX_RegWrite(EX_RegWrite), .ID_ALUSrcB(\硬布线控制器_1_alu_src ),
    .EX_ALUSrcB(id_ex_1_ex_alusrcb), .ID_AluOP(\硬布线控制器_1_alu_op ), .EX_AluOP(id_ex_1_ex_aluop),
    .ID_MemWrite(\硬布线控制器_1_memwrite ), .EX_MemWrite(id_ex_1_ex_memwrite), .ID_MemToReg(\硬布线控制器_1_memtoreg ),
    .EX_MemToReg(id_ex_1_ex_memtoreg), .ID_Bne(\硬布线控制器_1_bne ), .EX_Bne(EX_Bne), .ID_Beq(\硬布线控制器_1_beq ),
    .EX_Beq(EX_Beq),
    .ID_Jaddr({adder_2_out[31:28], if_id_1_id_ir_4, if_id_1_id_ir_3, if_id_1_id_ir_2, if_id_1_id_ir, ID_Func, 2'b00}),
    .EX_Jaddr(id_ex_1_ex_jaddr), .ID_W_num(ID_W_num), .EX_W_num(EX_W_num), .ID_Syscall(ID_stop),
    .EX_Syscall(id_ex_1_ex_syscall));  // open: ID_R1_num, EX_R1_num, ID_R2_num, EX_R2_num
  Shifter #(.width(32)) shifter_1 (.in(id_ex_1_ex_immed), .\dist (5'b00010), .out(shifter_1_out));
  Multiplexer #(.width(32), .enable("false")) multiplexer_7 (
    .in0(id_ex_1_ex_jaddr), .in1(EX_R1), .out(EX_Uncond_addr), .sel(EX_JR));
  and and_8 (and_8_out, comparator_2_eq, ID_Syscall);
  Multiplexer #(.width(32), .enable("false")) multiplexer_8 (
    .in0(id_ex_1_ex_r2), .in1(id_ex_1_ex_immed), .out(multiplexer_8_out), .sel(id_ex_1_ex_alusrcb));
  Multiplexer #(.width(5), .enable("false")) multiplexer_9 (
    .in0(id_ex_1_ex_shamt), .in1(EX_R1[4:0]), .out(multiplexer_9_out), .sel(EX_Shift));
  Adder #(.width(32)) adder_3 (.a(EX_PC), .b(32'h4), .out(adder_3_out));  // open: cin, cout
  MIPS_ALU mips_alu_1 (
    .X(EX_R1), .Y(multiplexer_8_out), .AluOP(id_ex_1_ex_aluop), .Equal(mips_alu_1_equal),
    .Result(mips_alu_1_result), .shamt(multiplexer_9_out));  // open: Result_2
  Adder #(.width(32)) adder_4 (.a(shifter_1_out), .b(adder_3_out), .out(EX_Cond_addr));  // open: cin, cout
  Register #(.width(32)) register_1 (.D(ID_R2), .en(and_8_out), .Q(LedData), .clk(CLK), .clr(RST));
  not not_3 (not_3_out, Run);
  EX_MEM ex_mem_1 (
    .EX_MemToReg(id_ex_1_ex_memtoreg), .EX_MemWrite(id_ex_1_ex_memwrite), .EX_RegWrite(EX_RegWrite),
    .EX_JAL(id_ex_1_ex_jal), .EX_LBU(id_ex_1_ex_lbu), .EX_PC(EX_PC), .EX_IR(id_ex_1_ex_ir),
    .EX_Result(mips_alu_1_result), .EX_R2(id_ex_1_ex_r2), .\传输状态In_表明当前传输数据有效 (\id_ex_1_传输状态out_表明当前传输数据有效 ),
    .CLK(CLK), .MEM_MemToReg(ex_mem_1_mem_memtoreg), .MEM_MemWrite(MEM_MemWrite),
    .MEM_RegWrite(MEM_RegWrite), .MEM_JAL(ex_mem_1_mem_jal), .MEM_LBU(MEM_LBU), .MEM_PC(MEM_PC),
    .MEM_IR(ex_mem_1_mem_ir), .MEM_Result(ex_mem_1_mem_result), .MEM_R2(ex_mem_1_mem_r2),
    .\传输状态Out_表明当前传输数据有效 (\ex_mem_1_传输状态out_表明当前传输数据有效 ), .\同步清零_气泡_高电平有效 (1'b0),
    .\使能端_低电平有效_stall_高电平有效 (not_3_out), .EX_W_num(EX_W_num), .MEM_W_num(MEM_W_num),
    .EX_stop(id_ex_1_ex_syscall), .MEM_stop(ex_mem_1_mem_stop));  // open: EX_display, MEM_display
  RAM #(.addrWidth(10), .dataWidth(32), .bus("separate")) ram_1 (
    .addr(ex_mem_1_mem_result[11:2]), .din(ex_mem_1_mem_r2), .data(ram_1_data), .str(MEM_MemWrite),
    .sel(1'b1), .clk(CLK), .ld(1'b1), .clr(RST));
  Multiplexer #(.width(32), .enable("false")) multiplexer_10 (
    .in0(ex_mem_1_mem_result), .in1(ram_1_data), .out(multiplexer_10_out), .sel(ex_mem_1_mem_memtoreg));
  Multiplexer #(.select(2), .width(8), .enable("false")) multiplexer_11 (
    .in0(multiplexer_10_out[7:0]), .in1(multiplexer_10_out[15:8]), .in2(multiplexer_10_out[23:16]),
    .in3(multiplexer_10_out[31:24]), .out(multiplexer_11_out), .sel(ex_mem_1_mem_result[1:0]));
  Multiplexer #(.width(32), .enable("false")) multiplexer_12 (
    .in0(multiplexer_10_out), .in1({{24{1'b0}}, multiplexer_11_out}), .out(multiplexer_12_out), .sel(MEM_LBU));
  not not_4 (not_4_out, Run);
  MEM_WB mem_wb_1 (
    .MEM_W_num(MEM_W_num), .MEM_RegWrite(MEM_RegWrite), .MEM_PC(MEM_PC), .MEM_IR(ex_mem_1_mem_ir),
    .MEM_Din(multiplexer_12_out), .\传输状态In_表明当前传输数据有效 (\ex_mem_1_传输状态out_表明当前传输数据有效 ), .CLK(CLK),
    .WB_W_num(WB_W_num), .WB_RegWrite(WB_RegWrite), .WE_PC(WB_PC), .WE_IR(mem_wb_1_we_ir),
    .WB_Din(mem_wb_1_wb_din), .\同步清零_气泡_高电平有效 (1'b0), .\使能端_低电平有效_stall_高电平有效 (not_4_out),
    .MEM_JAL(ex_mem_1_mem_jal), .WB_JAL(mem_wb_1_wb_jal), .MEM_stop(ex_mem_1_mem_stop), .WB_stop(WE_stop));  // open: 传输状态Out_表明当前传输数据有效, MEM_display, WB_display, MEM_R2, WE_R2
  Adder #(.width(32)) adder_5 (.a(WB_PC), .b(32'h4), .out(adder_5_out));  // open: cin, cout
  Multiplexer #(.width(32), .enable("false")) multiplexer_13 (
    .in0(mem_wb_1_wb_din), .in1(adder_5_out), .out(WB_Din), .sel(mem_wb_1_wb_jal));

  // Other names for the same wires on the sheet: Uncond = EX_Jmp

  // Notes on the sheet:
  //   中断源
  //   中断等待指示
  //   数码管输出
  //   指令存储器
  //   contents of rom_1 (hex, n*v repeats v):
  //   20110001 8000c05 20110001 20120002 20130003 8000c09 20110001 20120002 20130003 8000c0d 20110001
  //   20120002 20130003 8000c11 20110001 20120002 20130003 c000cb8 20100001 20110001 118fc0 112020
  //   20020022 c 118882 12200001 8000c15 112020 20020022 c 20110001 118880 112020 20020022 c 12200001
  //   8000c1f 20110001 118fc0 112020 20020022 c 1188c3 112020 20020022 c 118903 112020 20020022 c 118903
  //   112020 20020022 c 118903 112020 20020022 c 118903 112020 20020022 c 118903 112020 20020022 c 118903
  //   112020 20020022 c 118903 112020 20020022 c 20100001 109fc0 139fc3 8021 2012000c 24160003 26100001
  //   3210000f 20080008 20090001 139900 2709825 132020 20020022 c 1094022 1500fff9 22100001 2018000f
  //   2188024 108700 20080008 20090001 139902 2709825 132021 20020022 c 1094022 1500fff9 108702 2c9b022
  //   12c00001 8000c50 4020 1084027 84400 3508ffff 82021 20020022 c 2010ffff 20110000 ae300000 22100001
  //   22310004 ae300000 22100001 22310004 ae300000 22100001 22310004 ae300000 22100001 22310004 ae300000
  //   22100001 22310004 ae300000 22100001 22310004 ae300000 22100001 22310004 ae300000 22100001 22310004
  //   ae300000 22100001 22310004 ae300000 22100001 22310004 ae300000 22100001 22310004 ae300000 22100001
  //   22310004 ae300000 22100001 22310004 ae300000 22100001 22310004 ae300000 22100001 22310004 ae300000
  //   22100001 22310004 22100001 8020 2011003c 8e130000 8e340000 274402a 11000002 ae330000 ae140000
  //   2231fffc 1611fff8 102020 20020022 c 22100004 2011003c 1611fff2 20020032 c 20100000 22100001 102020
  //   20020022 c 22100002 102020 20020022 c 22100003 102020 20020022 c 22100004 102020 20020022 c 22100005
  //   102020 20020022 c 22100006 102020 20020022 c 22100007 102020 20020022 c 22100008 102020 20020022
  //   20020022 c 3e00008
  //   流水调试日志用
  //   指令字
  //   rd
endmodule

module \重定向流水线  (
);

  wire and_1_out, and_2_out, and_3_out, and_5_out, and_6_out, and_7_out, and_8_out, and_9_out, and_10_out,
       and_11_out, and_12_out, and_13_out, and_14_out, and_15_out, and_16_out, and_19_out, and_20_out,
       and_21_out, CLK, comparator_1_eq, comparator_2_eq, comparator_3_eq, comparator_4_eq, comparator_5_eq,
       comparator_6_eq, comparator_7_eq, comparator_8_eq, comparator_9_eq, comparator_10_eq,
       comparator_11_eq, comparator_12_eq, Cond, EX_Beq, EX_BLTZ, EX_Bne, EX_display, EX_Jmp, EX_JR,
       ex_mem_1_mem_display, ex_mem_1_mem_jal, ex_mem_1_mem_memtoreg, ex_mem_1_mem_stop,
       \ex_mem_1_传输状态out_表明当前传输数据有效 , EX_MemToReg, EX_RegWrite, EX_Shift, EX_stop, EX_Syscall, Go, ID_BLTZ,
       id_ex_1_ex_alusrcb, id_ex_1_ex_jal, id_ex_1_ex_lbu, id_ex_1_ex_memwrite, \id_ex_1_传输状态out_表明当前传输数据有效 ,
       ID_JAL, ID_Jmp, ID_JR, ID_LBU, ID_RegDst, ID_Shift, ID_SignedExt, ID_Syscall,
       \if_id_1_传输状态out_表明当前传输数据有效 , ins, IR1, IR2, IR3, LoadUse, MEM_LBU, MEM_MemWrite, MEM_RegWrite,
       mem_wb_1_wb_jal, mips_alu_1_equal, not_1_out, not_2_out, not_3_out, not_4_out, or_2_out, or_4_out,
       RST, Run, W1, W2, W3, WB_display, WB_RegWrite, WB_stop, \源寄存器使用情况_1_r1_used , \源寄存器使用情况_1_r2_used ,
       \源寄存器使用情况_2_r1_used , \源寄存器使用情况_2_r2_used , \硬布线控制器_1_alu_src , \硬布线控制器_1_beq , \硬布线控制器_1_bne ,
       \硬布线控制器_1_memtoreg , \硬布线控制器_1_memwrite , \硬布线控制器_1_regwrite , \硬布线控制器_1_sllv , \硬布线控制器_1_srlv ;
  wire [3:0] id_ex_1_ex_aluop, \硬布线控制器_1_alu_op ;
  wire [4:0] EX_R1_num, EX_R2_num, EX_W_num, id_ex_1_ex_shamt, ID_R1_num, ID_R2_num, ID_W_num, MEM_W_num,
       multiplexer_6_out, multiplexer_13_out, WB_W_num;
  wire [5:0] ID_Func;
  wire [7:0] multiplexer_16_out;
  wire [15:0] \LoadUse次数 , \总周期数 , \插入气泡数 , \无条件分支数 , \条件分支成功数 ;
  wire [31:0] adder_1_out, adder_2_out, adder_3_out, adder_5_out, adder_6_out, bit_extender_1_out,
       bit_extender_2_out, EX_ALU_A, EX_ALU_B, EX_Cond_addr, EX_IR, ex_mem_1_mem_ir, ex_mem_1_mem_r2,
       ex_mem_1_mem_result, EX_PC, EX_R1, EX_R2, EX_Uncond_addr, id_ex_1_ex_immed, id_ex_1_ex_jaddr, ID_PC,
       ID_R1, ID_R2, IF_PC, LedData, MEM_PC, MEM_Result, mem_wb_1_wb_din, mem_wb_1_we_ir, mips_alu_1_result,
       multiplexer_1_out, multiplexer_2_out, multiplexer_3_out, multiplexer_10_out, multiplexer_12_out,
       multiplexer_15_out, multiplexer_17_out, ram_1_data, rom_1_data, shifter_1_out, WB_Din, WB_PC, WB_R2;
  wire [31:6] ID_IR;

  Button \u_总复位  (.out(RST));
  Button _1 (.out(IR1));
  Button _2 (.out(IR2));
  Button _3 (.out(IR3));
  Button \u_继续运行  (.out(Go));
  LED led_1 (.in(W1));
  LED led_2 (.in(W2));
  LED led_3 (.in(W3));
  Counter #(.width(16), .max('hffff)) counter_1 (
    .count(Run), .Q(\总周期数 ), .clk(CLK), .clr(RST));  // open: load, D, carry
  Hex_Digit_Display hex_digit_display_1 (.value(LedData[31:28]));  // open: dp
  Hex_Digit_Display hex_digit_display_2 (.value(LedData[23:20]));  // open: dp
  Hex_Digit_Display hex_digit_display_3 (.value(LedData[27:24]));  // open: dp
  Multiplexer #(.select(2), .width(32), .enable("false")) multiplexer_1 (
    .in0(adder_1_out), .in1(EX_Uncond_addr), .in2(EX_Cond_addr), .out(multiplexer_1_out), .sel({Cond, EX_Jmp}));  // open: in3
  or or_1 (Run, Go, ~WB_stop);  // OR_Gate
  Hex_Digit_Display hex_digit_display_4 (.value(LedData[15:12]));  // open: dp
  Hex_Digit_Display hex_digit_display_5 (.value(LedData[19:16]));  // open: dp
  and and_1 (and_1_out, Cond, Run);
  \源寄存器使用情况  \u_源寄存器使用情况_1  (
    .OP0(EX_IR[26]), .OP1(EX_IR[27]), .OP2(EX_IR[28]), .OP3(EX_IR[29]), .OP4(EX_IR[30]), .OP5(EX_IR[31]),
    .F0(EX_IR[0]), .F1(EX_IR[1]), .F2(EX_IR[2]), .F3(EX_IR[3]), .F4(EX_IR[4]), .F5(EX_IR[5]),
    .R1_Used(\源寄存器使用情况_1_r1_used ), .R2_Used(\源寄存器使用情况_1_r2_used ));
  \源寄存器使用情况  \u_源寄存器使用情况_2  (
    .OP0(ID_IR[26]), .OP1(ID_IR[27]), .OP2(ID_IR[28]), .OP3(ID_IR[29]), .OP4(ID_IR[30]), .OP5(ID_IR[31]),
    .F0(ID_Func[0]), .F1(ID_Func[1]), .F2(ID_Func[2]), .F3(ID_Func[3]), .F4(ID_Func[4]), .F5(ID_Func[5]),
    .R1_Used(\源寄存器使用情况_2_r1_used ), .R2_Used(\源寄存器使用情况_2_r2_used ));
  Hex_Digit_Display hex_digit_display_6 (.value(LedData[11:8]));  // open: dp
  Hex_Digit_Display hex_digit_display_7 (.value(LedData[7:4]));  // open: dp
  Clock clock_1 (.out(CLK));
  and and_2 (and_2_out, Run, ~LoadUse);  // AND_Gate
  Counter #(.width(16), .max('hffff)) counter_2 (
    .count(and_1_out), .Q(\条件分支成功数 ), .clk(CLK), .clr(RST));  // open: load, D, carry
  Hex_Digit_Display hex_digit_display_8 (.value(LedData[3:0]));  // open: dp
  Register #(.width(32)) PC (.D(multiplexer_1_out), .en(and_2_out), .Q(IF_PC), .clk(CLK), .clr(RST));
  Adder #(.width(32)) adder_1 (.a(IF_PC), .b(32'h4), .out(adder_1_out));  // open: cin, cout
  Comparator #(.width(32), .mode("unsigned")) comparator_1 (
    .a(EX_ALU_A), .b(32'h22), .eq(comparator_1_eq));  // open: gt, lt
  // Probe on \总周期数 
  // Probe on \无条件分支数 
  // Probe on \条件分支成功数 
  // Probe on \插入气泡数 
  // Probe on \LoadUse次数 
  and and_3 (and_3_out, Run, ~LoadUse);  // AND_Gate
  and and_4 (EX_stop, ~comparator_1_eq, EX_Syscall);  // AND_Gate
  Counter #(.width(16), .max('hffff)) counter_3 (
    .count(and_5_out), .Q(\无条件分支数 ), .clk(CLK), .clr(RST));  // open: load, D, carry
  and and_5 (and_5_out, EX_Jmp, Run);
  Comparator #(.width(5)) comparator_2 (.a(WB_W_num), .b(EX_R1_num), .eq(comparator_2_eq));  // open: gt, lt
  Comparator #(.width(5)) comparator_3 (.a(MEM_W_num), .b(EX_R1_num), .eq(comparator_3_eq));  // open: gt, lt
  Comparator #(.width(5)) comparator_4 (.a({5{1'b0}}), .b(EX_R1_num), .eq(comparator_4_eq));  // open: gt, lt
  Comparator #(.width(5)) comparator_5 (.a({5{1'b0}}), .b(EX_R2_num), .eq(comparator_5_eq));  // open: gt, lt
  Comparator #(.width(5)) comparator_6 (.a(MEM_W_num), .b(EX_R2_num), .eq(comparator_6_eq));  // open: gt, lt
  Comparator #(.width(5)) comparator_7 (.a(WB_W_num), .b(EX_R2_num), .eq(comparator_7_eq));  // open: gt, lt
  Comparator #(.width(5)) comparator_8 (.a(EX_W_num), .b(ID_R1_num), .eq(comparator_8_eq));  // open: gt, lt
  Comparator #(.width(5)) comparator_9 (.a({5{1'b0}}), .b(ID_R1_num), .eq(comparator_9_eq));  // open: gt, lt
  Comparator #(.width(5)) comparator_10 (.a({5{1'b0}}), .b(ID_R2_num), .eq(comparator_10_eq));  // open: gt, lt
  Comparator #(.width(5)) comparator_11 (.a(EX_W_num), .b(ID_R2_num), .eq(comparator_11_eq));  // open: gt, lt
  // Probe on IF_PC[11:0]
  ROM #(.addrWidth(10), .dataWidth(32)) rom_1 (.addr(IF_PC[11:2]), .data(rom_1_data));  // open: sel
  not not_1 (not_1_out, and_3_out);
  // Probe on ID_PC[11:0]
  IF_ID if_id_1 (
    .IF_PC(IF_PC), .IF_IR(rom_1_data), .\传输状态In_表明当前传输数据有效 (1'b1), .CLK(CLK), .ID_PC(ID_PC),
    .ID_IR({ID_IR, ID_Func}), .\传输状态Out_表明当前传输数据有效 (\if_id_1_传输状态out_表明当前传输数据有效 ),
    .\同步清零_气泡_高电平有效 (or_2_out), .\使能端_低电平有效_stall_高电平有效 (not_1_out));
  and and_6 (and_6_out, WB_RegWrite, comparator_2_eq);
  and and_7 (and_7_out, MEM_RegWrite, comparator_3_eq);
  and and_8 (and_8_out, MEM_RegWrite, comparator_6_eq);
  and and_9 (and_9_out, WB_RegWrite, comparator_7_eq);
  // Probe on EX_PC[11:0]
  // Probe on MEM_PC[11:0]
  or or_2 (or_2_out, EX_Jmp, Cond);
  and and_10 (and_10_out, ins, Run);
  and and_11 (and_11_out, and_6_out, ~comparator_4_eq, \源寄存器使用情况_1_r1_used );  // AND_Gate
  and and_12 (and_12_out, and_7_out, ~comparator_4_eq, \源寄存器使用情况_1_r1_used );  // AND_Gate
  and and_13 (and_13_out, \源寄存器使用情况_1_r2_used , ~comparator_5_eq, and_8_out);  // AND_Gate
  and and_14 (and_14_out, \源寄存器使用情况_1_r2_used , ~comparator_5_eq, and_9_out);  // AND_Gate
  // Probe on WB_PC[11:0]
  // Probe on {ID_IR, ID_Func}
  Comparator #(.width(32), .mode("unsigned")) comparator_12 (
    .a(EX_ALU_A), .b(32'h22), .eq(comparator_12_eq));  // open: gt, lt
  Counter #(.width(16), .max('hffff)) counter_4 (
    .count(and_10_out), .Q(\插入气泡数 ), .clk(CLK), .clr(RST));  // open: load, D, carry
  Multiplexer #(.width(32), .enable("false")) multiplexer_2 (
    .in0(EX_R1), .in1(WB_Din), .out(multiplexer_2_out), .sel(and_11_out));
  Multiplexer #(.width(32), .enable("false")) multiplexer_3 (
    .in0(EX_R2), .in1(WB_Din), .out(multiplexer_3_out), .sel(and_14_out));
  and and_15 (and_15_out, \源寄存器使用情况_2_r2_used , ~comparator_10_eq, comparator_11_eq);  // AND_Gate
  and and_16 (and_16_out, comparator_8_eq, ~comparator_9_eq, \源寄存器使用情况_2_r1_used );  // AND_Gate
  or or_3 (ID_Shift, \硬布线控制器_1_sllv , \硬布线控制器_1_srlv );
  Adder #(.width(32)) adder_2 (.a(ID_PC), .b(32'h4), .out(adder_2_out));  // open: cin, cout
  and and_17 (EX_display, comparator_12_eq, EX_Syscall);
  Multiplexer #(.width(32), .enable("false")) multiplexer_4 (
    .in0(multiplexer_2_out), .in1(MEM_Result), .out(EX_ALU_A), .sel(and_12_out));
  Multiplexer #(.width(32), .enable("false")) multiplexer_5 (
    .in0(multiplexer_3_out), .in1(MEM_Result), .out(EX_ALU_B), .sel(and_13_out));
  Multiplexer #(.width(5), .enable("false")) multiplexer_6 (
    .in0(ID_IR[20:16]), .in1(ID_IR[15:11]), .out(multiplexer_6_out), .sel(ID_RegDst));
  Counter #(.width(16), .max('hffff)) counter_5 (
    .count(LoadUse), .Q(\LoadUse次数 ), .clk(CLK), .clr(RST));  // open: load, D, carry
  or or_4 (or_4_out, and_16_out, and_15_out);
  \硬布线控制器  \u_硬布线控制器_1  (
    .Func(ID_Func), .OP(ID_IR[31:26]), .ALU_OP(\硬布线控制器_1_alu_op ), .MemToReg(\硬布线控制器_1_memtoreg ),
    .MemWrite(\硬布线控制器_1_memwrite ), .ALU_SRC(\硬布线控制器_1_alu_src ), .RegWrite(\硬布线控制器_1_regwrite ),
    .SysCALL(ID_Syscall), .SignedExt(ID_SignedExt), .RegDst(ID_RegDst), .JR(ID_JR), .JMP(ID_Jmp),
    .Beq(\硬布线控制器_1_beq ), .JAL(ID_JAL), .Bne(\硬布线控制器_1_bne ), .SLLV(\硬布线控制器_1_sllv ), .SRLV(\硬布线控制器_1_srlv ),
    .LBU(ID_LBU), .BLTZ(ID_BLTZ), .REGIMM(ID_IR[20:16]));
  Multiplexer #(.width(5), .enable("false")) multiplexer_7 (
    .in0(ID_IR[25:21]), .in1(5'b00010), .out(ID_R1_num), .sel(ID_Syscall));
  Multiplexer #(.width(5), .enable("false")) multiplexer_8 (
    .in0(ID_IR[20:16]), .in1(5'b00100), .out(ID_R2_num), .sel(ID_Syscall));
  Multiplexer #(.width(5), .enable("false")) multiplexer_9 (
    .in0(multiplexer_6_out), .in1({5{1'b1}}), .out(ID_W_num), .sel(ID_JAL));
  assign bit_extender_1_out = {{16{1'b0}}, {ID_IR[15:6], ID_Func}};  // Bit_Extender bit_extender_1
  assign bit_extender_2_out = {{16{ID_IR[15]}}, {ID_IR[15:6], ID_Func}};  // Bit_Extender bit_extender_2
  // Probe on WB_Din
  // Probe on WB_W_num
  Multiplexer #(.width(32), .enable("false")) multiplexer_10 (
    .in0(bit_extender_1_out), .in1(bit_extender_2_out), .out(multiplexer_10_out), .sel(ID_SignedExt));
  and and_18 (LoadUse, or_4_out, EX_MemToReg);
  or or_5 (Cond, and_19_out, and_20_out, and_21_out);
  MIPS_Regifile mips_regifile_1 (
    .Din(WB_Din), .Clk(CLK), .R1(ID_R1), .R2(ID_R2), .WE(WB_RegWrite), .W_num(WB_W_num), .R1_num(ID_R1_num),
    .R2_num(ID_R2_num));
  not not_2 (not_2_out, Run);
  Register #(.width(32)) register_1 (.D(WB_R2), .en(WB_display), .Q(LedData), .clk(CLK), .clr(RST));
  and and_19 (and_19_out, mips_alu_1_result[0], EX_BLTZ);
  and and_20 (and_20_out, ~mips_alu_1_equal, EX_Bne);  // AND_Gate
  and and_21 (and_21_out, mips_alu_1_equal, EX_Beq);
  or or_6 (ins, or_2_out, LoadUse);
  ID_EX id_ex_1 (
    .ID_PC(ID_PC), .ID_IR({ID_IR, ID_Func}), .ID_R1(ID_R1), .ID_R2(ID_R2), .ID_immed(multiplexer_10_out),
    .ID_shamt(ID_IR[10:6]), .\传输状态In_表明当前传输数据有效 (\if_id_1_传输状态out_表明当前传输数据有效 ), .CLK(CLK), .EX_PC(EX_PC),
    .EX_IR(EX_IR), .EX_R1(EX_R1), .EX_R2(EX_R2), .EX_immed(id_ex_1_ex_immed), .EX_shamt(id_ex_1_ex_shamt),
    .\传输状态Out_表明当前传输数据有效 (\id_ex_1_传输状态out_表明当前传输数据有效 ), .\同步清零_气泡_高电平有效 (ins),
    .\使能端_低电平有效_stall_高电平有效 (not_2_out), .ID_BLTZ(ID_BLTZ), .EX_BLTZ(EX_BLTZ), .ID_LBU(ID_LBU),
    .EX_LBU(id_ex_1_ex_lbu), .ID_Shift(ID_Shift), .EX_Shift(EX_Shift), .ID_JR(ID_JR), .EX_JR(EX_JR),
    .ID_Jmp(ID_Jmp), .EX_Jmp(EX_Jmp), .ID_JAL(ID_JAL), .EX_JAL(id_ex_1_ex_jal),
    .ID_RegWrite(\硬布线控制器_1_regwrite ), .EX_RegWrite(EX_RegWrite), .ID_ALUSrcB(\硬布线控制器_1_alu_src ),
    .EX_ALUSrcB(id_ex_1_ex_alusrcb), .ID_AluOP(\硬布线控制器_1_alu_op ), .EX_AluOP(id_ex_1_ex_aluop),
    .ID_MemWrite(\硬布线控制器_1_memwrite ), .EX_MemWrite(id_ex_1_ex_memwrite), .ID_MemToReg(\硬布线控制器_1_memtoreg ),
    .EX_MemToReg(EX_MemToReg), .ID_Bne(\硬布线控制器_1_bne ), .EX_Bne(EX_Bne), .ID_Beq(\硬布线控制器_1_beq ),
    .EX_Beq(EX_Beq), .ID_Jaddr({adder_2_out[31:28], ID_IR[25:6], ID_Func, 2'b00}),
    .EX_Jaddr(id_ex_1_ex_jaddr), .ID_W_num(ID_W_num), .EX_W_num(EX_W_num), .ID_Syscall(ID_Syscall),
    .EX_Syscall(EX_Syscall), .ID_R1_num(ID_R1_num), .EX_R1_num(EX_R1_num), .ID_R2_num(ID_R2_num),
    .EX_R2_num(EX_R2_num));
  Shifter #(.width(32)) shifter_1 (.in(id_ex_1_ex_immed), .\dist (5'b00010), .out(shifter_1_out));
  Multiplexer #(.width(32), .enable("false")) multiplexer_11 (
    .in0(id_ex_1_ex_jaddr), .in1(EX_ALU_A), .out(EX_Uncond_addr), .sel(EX_JR));
  Multiplexer #(.width(32), .enable("false")) multiplexer_12 (
    .in0(EX_ALU_B), .in1(id_ex_1_ex_immed), .out(multiplexer_12_out), .sel(id_ex_1_ex_alusrcb));
  Multiplexer #(.width(5), .enable("false")) multiplexer_13 (
    .in0(id_ex_1_ex_shamt), .in1(EX_ALU_A[4:0]), .out(multiplexer_13_out), .sel(EX_Shift));
  Adder #(.width(32)) adder_3 (.a(EX_PC), .b(32'h4), .out(adder_3_out));  // open: cin, cout
  MIPS_ALU mips_alu_1 (
    .X(EX_ALU_A), .Y(multiplexer_12_out), .AluOP(id_ex_1_ex_aluop), .Equal(mips_alu_1_equal),
    .Result(mips_alu_1_result), .shamt(multiplexer_13_out));  // open: Result_2
  Adder #(.width(32)) adder_4 (.a(shifter_1_out), .b(adder_3_out), .out(EX_Cond_addr));  // open: cin, cout
  not not_3 (not_3_out, Run);
  EX_MEM ex_mem_1 (
    .EX_MemToReg(EX_MemToReg), .EX_MemWrite(id_ex_1_ex_memwrite), .EX_RegWrite(EX_RegWrite),
    .EX_JAL(id_ex_1_ex_jal), .EX_LBU(id_ex_1_ex_lbu), .EX_PC(EX_PC), .EX_IR(EX_IR),
    .EX_Result(mips_alu_1_result), .EX_R2(EX_ALU_B), .\传输状态In_表明当前传输数据有效 (\id_ex_1_传输状态out_表明当前传输数据有效 ),
    .CLK(CLK), .MEM_MemToReg(ex_mem_1_mem_memtoreg), .MEM_MemWrite(MEM_MemWrite),
    .MEM_RegWrite(MEM_RegWrite), .MEM_JAL(ex_mem_1_mem_jal), .MEM_LBU(MEM_LBU), .MEM_PC(MEM_PC),
    .MEM_IR(ex_mem_1_mem_ir), .MEM_Result(ex_mem_1_mem_result), .MEM_R2(ex_mem_1_mem_r2),
    .\传输状态Out_表明当前传输数据有效 (\ex_mem_1_传输状态out_表明当前传输数据有效 ), .\同步清零_气泡_高电平有效 (1'b0),
    .\使能端_低电平有效_stall_高电平有效 (not_3_out), .EX_W_num(EX_W_num), .MEM_W_num(MEM_W_num), .EX_stop(EX_stop),
    .MEM_stop(ex_mem_1_mem_stop), .EX_display(EX_display), .MEM_display(ex_mem_1_mem_display));
  Adder #(.width(32)) adder_5 (.a(MEM_PC), .b(32'h4), .out(adder_5_out));  // open: cin, cout
  Multiplexer #(.width(32), .enable("false")) multiplexer_14 (
    .in0(ex_mem_1_mem_result), .in1(adder_5_out), .out(MEM_Result), .sel(ex_mem_1_mem_jal));
  RAM #(.addrWidth(10), .dataWidth(32), .bus("separate")) ram_1 (
    .addr(ex_mem_1_mem_result[11:2]), .din(ex_mem_1_mem_r2), .data(ram_1_data), .str(MEM_MemWrite),
    .sel(1'b1), .clk(CLK), .ld(1'b1), .clr(RST));
  Multiplexer #(.width(32), .enable("false")) multiplexer_15 (
    .in0(ex_mem_1_mem_result), .in1(ram_1_data), .out(multiplexer_15_out), .sel(ex_mem_1_mem_memtoreg));
  Multiplexer #(.select(2), .width(8), .enable("false")) multiplexer_16 (
    .in0(multiplexer_15_out[7:0]), .in1(multiplexer_15_out[15:8]), .in2(multiplexer_15_out[23:16]),
    .in3(multiplexer_15_out[31:24]), .out(multiplexer_16_out), .sel(ex_mem_1_mem_result[1:0]));
  Multiplexer #(.width(32), .enable("false")) multiplexer_17 (
    .in0(multiplexer_15_out), .in1({{24{1'b0}}, multiplexer_16_out}), .out(multiplexer_17_out), .sel(MEM_LBU));
  // Probe on multiplexer_17_out
  not not_4 (not_4_out, Run);
  MEM_WB mem_wb_1 (
    .MEM_W_num(MEM_W_num), .MEM_RegWrite(MEM_RegWrite), .MEM_PC(MEM_PC), .MEM_IR(ex_mem_1_mem_ir),
    .MEM_Din(multiplexer_17_out), .\传输状态In_表明当前传输数据有效 (\ex_mem_1_传输状态out_表明当前传输数据有效 ), .CLK(CLK),
    .WB_W_num(WB_W_num), .WB_RegWrite(WB_RegWrite), .WE_PC(WB_PC), .WE_IR(mem_wb_1_we_ir),
    .WB_Din(mem_wb_1_wb_din), .\同步清零_气泡_高电平有效 (1'b0), .\使能端_低电平有效_stall_高电平有效 (not_4_out),
    .MEM_JAL(ex_mem_1_mem_jal), .WB_JAL(mem_wb_1_wb_jal), .MEM_stop(ex_mem_1_mem_stop), .WB_stop(WB_stop),
    .MEM_display(ex_mem_1_mem_display), .WB_display(WB_display), .MEM_R2(ex_mem_1_mem_r2), .WE_R2(WB_R2));  // open: 传输状态Out_表明当前传输数据有效
  Adder #(.width(32)) adder_6 (.a(WB_PC), .b(32'h4), .out(adder_6_out));  // open: cin, cout
  Multiplexer #(.width(32), .enable("false")) multiplexer_18 (
    .in0(mem_wb_1_wb_din), .in1(adder_6_out), .out(WB_Din), .sel(mem_wb_1_wb_jal));
  // Probe on WB_Din

  // Other names for the same wires on the sheet: Uncond = EX_Jmp; ID_IR[5:0] = ID_Func; ID_OP[5:0] = ID_IR[31:26]

  // Notes on the sheet:
  //   中断源
  //   中断等待指示
  //   数码管输出
  //   指令存储器
  //   contents of rom_1 (hex, n*v repeats v):
  //   20110001 8100005 20110001 20120002 20130003 8100009 20110001 20120002 20130003 810000d 20110001
  //   20120002 20130003 8100011 20110001 20120002 20130003 c1000fb 20100001 20110001 118fc0 112020
  //   20020022 c 118882 12200001 8100015 112020 20020022 c 20110001 118880 112020 20020022 c 12200001
  //   810001f 20110001 118fc0 112020 20020022 c 1188c3 112020 20020022 c 118903 112020 20020022 c 118903
  //   112020 20020022 c 118903 112020 20020022 c 118903 112020 20020022 c 118903 112020 20020022 c 118903
  //   112020 20020022 c 118903 112020 20020022 c 20100001 109fc0 139fc3 8021 2012000c 24160003 26100001
  //   3210000f 20080008 20090001 139900 2709825 132020 20020022 c 1094022 1500fff9 22100001 2018000f
  //   2188024 108700 20080008 20090001 139902 2709825 132021 20020022 c 1094022 1500fff9 108702 2c9b022
  //   12c00001 8100050 4020 1084027 84400 3508ffff 82021 20020022 c 2010ffff 20110000 ae300000 22100001
  //   22310004 ae300000 22100001 22310004 ae300000 22100001 22310004 ae300000 22100001 22310004 ae300000
  //   22100001 22310004 ae300000 22100001 22310004 ae300000 22100001 22310004 ae300000 22100001 22310004
  //   ae300000 22100001 22310004 ae300000 22100001 22310004 ae300000 22100001 22310004 ae300000 22100001
  //   22310004 ae300000 22100001 22310004 ae300000 22100001 22310004 ae300000 22100001 22310004 ae300000
  //   22100001 22310004 22100001 8020 2011003c 8e130000 8e340000 274402a 11000002 ae330000 ae140000
  //   2231fffc 1611fff8 102020 20020022 c 22100004 2011003c 1611fff2 20020032 c 20080001 20090003 20110876
  //   112020 20020022 c 200b0008 1118804 1318804 112020 20020022 c 216bffff 1560fff9 2002000a c 20080001
  //   20090003 20110876 118d00 112020 20020022 c 200b0008 1118806 1318806 112020 20020022 c 216bffff
  //   1560fff9 2002000a c 20090000 200b0010 34118483 20120404 118c00 129400 36318281 22520404 ad310000
  //   2328820 21290004 216bffff 1560fffb 200b0020 20090000 91310000 112020 20020022 c 21290001 216bffff
  //   1560fff9 2002000a c 2011fff1 112020 20020022 c 22310001 620fffb 2002000a c 2002000a c 20100000
  //   22100001 102020 20020022 c 22100002 102020 20020022 c 22100003 102020 20020022 c 22100004 102020
  //   20020022 c 22100005 102020 20020022 c 22100006 102020 20020022 c 22100007 102020 20020022 c 22100008
  //   102020 20020022 20020022 c 3e00008
  //   流水调试日志用
  //   指令字
  //   rd
endmodule
